// Logisim project cpu24.circ as structural Verilog: 20 circuits, main circuit ◇单周期MIPS
module \单周期MIPS  (
);

  wire and_1_out, and_2_out, and_3_out, and_4_out, and_5_out, and_6_out, and_7_out, Beq, BLEZ, Bne, CLK, Cmp,
       comparator_1_eq, comparator_2_eq, d_ff_1_qn, Equal, Go, JAL, JMP, LUI, MemWrite, not_1_out, PCEnable,
       RST, SH, SignedExt, syscall, XOR, \硬布线控制器_1_memtoreg , \硬布线控制器_1_regdst , \硬布线控制器_1_regwrite ;
  wire [1:0] En;
  wire [1:1] \硬布线控制器_1_alu_src ;
  wire [3:0] \硬布线控制器_1_alu_op ;
  wire [4:0] multiplexer_3_out, multiplexer_4_out, multiplexer_6_out, multiplexer_7_out;
  wire [15:0] \总周期数 , \无条件分支数 , \条件分支成功数 ;
  wire [25:0] addr;
  wire [31:0] adder_2_out, Addr2, bit_extender_1_out, bit_extender_2_out, LedData, multiplexer_1_out,
       multiplexer_2_out, multiplexer_5_out, multiplexer_10_out, multiplexer_12_out, pc_4, PC_q, R1, R2, R22,
       ram_1_data, result, shifter_1_out, shifter_2_out, Y;
  wire [31:26] rom_1_data;

  Button \u_总复位  (.out(RST));
  Button u_Go (.out(Go));
  Clock clock_1 (.out(CLK));
  Hex_Digit_Display hex_digit_display_1 (.value(LedData[27:24]));  // open: dp
  Hex_Digit_Display hex_digit_display_2 (.value(LedData[31:28]));  // open: dp
  Comparator #(.width(32)) comparator_1 (.a(R1), .b(32'h22), .eq(comparator_1_eq));  // open: gt, lt
  and and_1 (and_1_out, comparator_1_eq, syscall);
  Comparator #(.width(32)) comparator_2 (.a(result), .b(32'h1), .eq(comparator_2_eq));  // open: gt, lt
  Hex_Digit_Display hex_digit_display_3 (.value(LedData[19:16]));  // open: dp
  Hex_Digit_Display hex_digit_display_4 (.value(LedData[23:20]));  // open: dp
  not not_1 (not_1_out, comparator_1_eq);
  Register #(.width(32)) register_1 (.D(multiplexer_1_out), .Q(LedData), .clk(CLK));  // open: en, clr
  Multiplexer #(.width(32), .enable("false")) multiplexer_1 (
    .in0(LedData), .in1(R2), .out(multiplexer_1_out), .sel(and_1_out));
  Multiplexer #(.select(2), .width(32), .enable("false")) multiplexer_2 (
    .in0(pc_4), .in1(Addr2), .in2(R1), .in3(R1), .out(multiplexer_2_out), .sel(En));
  and and_2 (and_2_out, Bne, ~Equal);  // AND_Gate
  and and_3 (and_3_out, Equal, Beq);
  and and_4 (and_4_out, comparator_2_eq, BLEZ);
  Hex_Digit_Display hex_digit_display_5 (.value(LedData[11:8]));  // open: dp
  Hex_Digit_Display hex_digit_display_6 (.value(LedData[15:12]));  // open: dp
  D_Flip_Flop d_ff_1 (.clk(CLK), .D(Go), .Qn(d_ff_1_qn));  // open: Q, preset, en, reset
  Hex_Digit_Display hex_digit_display_7 (.value(LedData[7:4]));  // open: dp
  Hex_Digit_Display hex_digit_display_8 (.value(LedData[3:0]));  // open: dp
  and and_5 (and_5_out, d_ff_1_qn, syscall, not_1_out);
  Register #(.width(32)) PC (.D(multiplexer_2_out), .en(PCEnable), .Q(PC_q), .clk(CLK), .clr(RST));
  or or_1 (Cmp, and_2_out, and_3_out, and_4_out);
  not not_2 (PCEnable, and_5_out);
  Adder #(.width(32)) adder_1 (.a(PC_q), .b(32'h4), .out(pc_4));  // open: cin, cout
  or or_2 (En[0], JMP, Cmp);
  // Probe on \总周期数 
  // Probe on \无条件分支数 
  // Probe on \条件分支成功数 
  ROM #(.addrWidth(10), .dataWidth(32)) rom_1 (.addr(PC_q[11:2]), .data({rom_1_data, addr}));  // open: sel
  assign bit_extender_1_out = {{16{1'b0}}, addr[15:0]};  // Bit_Extender bit_extender_1
  assign bit_extender_2_out = {{16{addr[15]}}, addr[15:0]};  // Bit_Extender bit_extender_2
  \硬布线控制器  \u_硬布线控制器_1  (
    .Func(addr[5:0]), .OP(rom_1_data), .ALU_OP(\硬布线控制器_1_alu_op ), .MemToReg(\硬布线控制器_1_memtoreg ),
    .MemWrite(MemWrite), .ALU_SRC(\硬布线控制器_1_alu_src [1]), .RegWrite(\硬布线控制器_1_regwrite ), .SysCALL(syscall),
    .SignedExt(SignedExt), .RegDst(\硬布线控制器_1_regdst ), .JR(En[1]), .JMP(JMP), .Beq(Beq), .JAL(JAL),
    .Bne(Bne), .XOR(XOR), .LUI(LUI), .SH(SH), .BLEZ(BLEZ));
  Multiplexer #(.width(5), .enable("false")) multiplexer_3 (
    .in0(addr[20:16]), .in1(5'b00100), .out(multiplexer_3_out), .sel(syscall));
  Multiplexer #(.width(5), .enable("false")) multiplexer_4 (
    .in0(addr[20:16]), .in1(addr[15:11]), .out(multiplexer_4_out), .sel(\硬布线控制器_1_regdst ));
  Multiplexer #(.width(32), .enable("false")) multiplexer_5 (
    .in0(bit_extender_1_out), .in1(bit_extender_2_out), .out(multiplexer_5_out), .sel(SignedExt));
  Shifter #(.width(32)) shifter_1 (.in(bit_extender_2_out), .\dist (5'b00010), .out(shifter_1_out));
  Counter #(.width(16), .max('hffff)) counter_1 (
    .count(PCEnable), .Q(\总周期数 ), .clk(CLK), .clr(RST));  // open: load, D, carry
  Multiplexer #(.width(5), .enable("false")) multiplexer_6 (
    .in0(addr[25:21]), .in1(5'b00010), .out(multiplexer_6_out), .sel(syscall));
  Multiplexer #(.width(5), .enable("false")) multiplexer_7 (
    .in0(multiplexer_4_out), .in1({5{1'b1}}), .out(multiplexer_7_out), .sel(JAL));
  Adder #(.width(32)) adder_2 (.a(shifter_1_out), .b(pc_4), .out(adder_2_out));  // open: cin, cout
  MIPS_Regifile mips_regifile_1 (
    .Din(multiplexer_10_out), .Clk(CLK), .R1(R1), .R2(R2), .WE(\硬布线控制器_1_regwrite ),
    .W_num(multiplexer_7_out), .R1_num(multiplexer_6_out), .R2_num(multiplexer_3_out));
  Counter #(.width(16), .max('hffff)) counter_2 (
    .count(and_6_out), .Q(\条件分支成功数 ), .clk(CLK), .clr(RST));  // open: load, D, carry
  and and_6 (and_6_out, Cmp, PCEnable);
  Multiplexer #(.select(2), .width(32), .enable("false")) multiplexer_8 (
    .in0(R2), .in1(32'h1), .in2(multiplexer_5_out), .in3(32'h1), .out(Y), .sel({\硬布线控制器_1_alu_src [1], BLEZ}));
  Multiplexer #(.width(32), .enable("false")) multiplexer_9 (
    .in0({pc_4[31:28], addr, 2'b00}), .in1(adder_2_out), .out(Addr2), .sel(Cmp));
  Counter #(.width(16), .max('hffff)) counter_3 (
    .count(and_7_out), .Q(\无条件分支数 ), .clk(CLK), .clr(RST));  // open: load, D, carry
  and and_7 (and_7_out, JMP, PCEnable);
  MIPS_ALU mips_alu_1 (
    .X(R1), .Y(Y), .AluOP(\硬布线控制器_1_alu_op ), .Equal(Equal), .Result(result), .shamt(addr[10:6]));  // open: Result_2
  Multiplexer #(.select(3), .width(32), .enable("false")) multiplexer_10 (
    .in0(multiplexer_12_out), .in1(multiplexer_12_out), .in2(shifter_2_out), .in3({32{1'b0}}), .in4(pc_4),
    .in5({32{1'b0}}), .in7({32{1'b0}}), .out(multiplexer_10_out), .sel({JAL, LUI, XOR}));  // open: in6
  RAM #(.addrWidth(10), .dataWidth(32), .bus("separate")) ram_1 (
    .addr(result[11:2]), .din(R22), .data(ram_1_data), .str(MemWrite), .clk(CLK), .clr(RST));  // open: sel, ld
  Shifter #(.width(32)) shifter_2 (.in(Y), .\dist (5'b10000), .out(shifter_2_out));
  Multiplexer #(.width(32), .enable("false")) multiplexer_11 (
    .in0(R2), .in1({{16{1'b0}}, R2[15:0]}), .out(R22), .sel(SH));
  Multiplexer #(.width(32), .enable("false")) multiplexer_12 (
    .in0(result), .in1(ram_1_data), .out(multiplexer_12_out), .sel(\硬布线控制器_1_memtoreg ));

  // Other names for the same wires on the sheet: PC_choose = En[0]; JR = En[1]

  // Notes on the sheet:
  //   数码管输出应该用寄存器锁存，否则显示数据只能一闪而过
  //   可以通过项目增加Logisim库的方式将前几次实验完成的电路作为子电路引入到本电路中使用
  //   数码管输出
  //   指令存储器
  //   总复位信号应将除ROM以外所有存储组件全部清零
  //   指令字
  //   contents of rom_1 (hex, n*v repeats v):
  //   20110001 8100005 20110001 20120002 20130003 8100009 20110001 20120002 20130003 810000d 20110001
  //   20120002 20130003 8100011 20110001 20120002 20130003 c1000fa 20100001 20110001 118fc0 112020
  //   20020022 c 118882 12200001 8100015 112020 20020022 c 20110001 118880 112020 20020022 c 12200001
  //   810001f 20110001 118fc0 112020 20020022 c 1188c3 112020 20020022 c 118903 112020 20020022 c 118903
  //   112020 20020022 c 118903 112020 20020022 c 118903 112020 20020022 c 118903 112020 20020022 c 118903
  //   112020 20020022 c 118903 112020 20020022 c 20100001 109fc0 139fc3 8021 2012000c 24160003 26100001
  //   3210000f 20080008 20090001 139900 2709825 132020 20020022 c 1094022 1500fff9 22100001 2018000f
  //   2188024 108700 20080008 20090001 139902 2709825 132021 20020022 c 1094022 1500fff9 108702 2c9b022
  //   12c00001 8100050 4020 1084027 84400 3508ffff 82021 20020022 c 2010ffff 20110000 ae300000 22100001
  //   22310004 ae300000 22100001 22310004 ae300000 22100001 22310004 ae300000 22100001 22310004 ae300000
  //   22100001 22310004 ae300000 22100001 22310004 ae300000 22100001 22310004 ae300000 22100001 22310004
  //   ae300000 22100001 22310004 ae300000 22100001 22310004 ae300000 22100001 22310004 ae300000 22100001
  //   22310004 ae300000 22100001 22310004 ae300000 22100001 22310004 ae300000 22100001 22310004 ae300000
  //   22100001 22310004 22100001 8020 2011003c 8e130000 8e340000 274402a 11000002 ae330000 ae140000
  //   2231fffc 1611fff8 102020 20020022 c 22100004 2011003c 1611fff2 20020032 c 2008ffff 20117777 112020
  //   20020022 c 200b0010 2288826 112020 20020022 c 216bffff 1560fffa 2002000a c 200b0008 3c11fedc
  //   3631ffff 112020 20020022 c 3c11ba98 112020 c 3c117654 112020 c 3c113210 112020 c 216bffff 1560fff0
  //   2002000a c 20090000 200b0020 20110001 20120001 a5310000 112020 20020022 c 2328820 21290002 216bffff
  //   1560fff8 200b0010 20090000 8d310000 112020 20020022 c 21290004 216bffff 1560fff9 2002000a c 2011fff1
  //   112020 20020022 c 22310001 1a20fffb 2002000a c 2002000a c 20100000 22100001 102020 20020022 c
  //   22100002 102020 20020022 c 22100003 102020 20020022 c 22100004 102020 20020022 c 22100005 102020
  //   20020022 c 22100006 102020 20020022 c 22100007 102020 20020022 c 22100008 102020 20020022 20020022 c
  //   3e00008
  //   OP
  //   Func
  //   rs
  //   rt
  //   rd
  //   sa
  //   JR
  //   Beq
  //   JMP
  //   Bne
  //   OP
  //   JAL
  //   Func
  //   Syscall
  //   MemToReg
  //   MemWrite
  //   AluOP
  //   AluSrcB
  //   RegWrite
  //   RegDst
endmodule

// 单周期硬布线控制器
module \硬布线控制器  (
  input  [5:0] OP,
  input  [5:0] Func,
  output [3:0] ALU_OP,
  output MemToReg,
  output MemWrite,
  output ALU_SRC,
  output RegWrite,
  output SysCALL,
  output SignedExt,
  output RegDst,
  output Beq,
  output Bne,
  output JR,
  output JMP,
  output JAL,
  output XOR,
  output LUI,
  output SH,
  output BLEZ
);

  \运算控制器  \u_运算控制器_1  (
    .OP0(OP[0]), .OP1(OP[1]), .OP2(OP[2]), .OP3(OP[3]), .OP4(OP[4]), .OP5(OP[5]), .F0(Func[0]), .F1(Func[1]),
    .F2(Func[2]), .F3(Func[3]), .F4(Func[4]), .F5(Func[5]), .S0(ALU_OP[0]), .S1(ALU_OP[1]), .S2(ALU_OP[2]),
    .S3(ALU_OP[3]));
  \控制信号生成  \u_控制信号生成_1  (
    .OP0(OP[0]), .OP1(OP[1]), .OP2(OP[2]), .OP3(OP[3]), .OP4(OP[4]), .OP5(OP[5]), .F0(Func[0]), .F1(Func[1]),
    .F2(Func[2]), .F3(Func[3]), .F4(Func[4]), .F5(Func[5]), .MemToReg(MemToReg), .MemWrite(MemWrite),
    .ALU_SRC(ALU_SRC), .RegWrite(RegWrite), .SysCALL(SysCALL), .SignedExt(SignedExt), .RegDst(RegDst),
    .BEQ(Beq), .BNE(Bne), .JR(JR), .JMP(JMP), .JAL(JAL));
  personal personal_1 (
    .OP0(OP[0]), .OP1(OP[1]), .OP2(OP[2]), .OP3(OP[3]), .OP4(OP[4]), .OP5(OP[5]), .F0(Func[0]), .F1(Func[1]),
    .F2(Func[2]), .F3(Func[3]), .F4(Func[4]), .F5(Func[5]), .XOR(XOR), .LUI(LUI), .SH(SH), .BLEZ(BLEZ));

  // Other names for the same wires on the sheet: OP_CODE[5:0] = OP

  // Notes on the sheet:
  //   运算器控制器，根据指令生成运算器功能选择信号
  //   控制信号生成，产生数据通路需要的其他控制信号
endmodule

// 运算器控制器
module \运算控制器  (
  input  OP0,
  input  OP1,
  input  OP2,
  input  OP3,
  input  OP4,
  input  OP5,
  input  F0,
  input  F1,
  input  F2,
  input  F3,
  input  F4,
  input  F5,
  output S0,
  output S1,
  output S2,
  output S3
);

  wire and_1_out, and_2_out, and_3_out, and_4_out, and_5_out, and_6_out, and_7_out, and_8_out, and_9_out,
       and_10_out, and_11_out, and_12_out, and_13_out, and_14_out, and_15_out, and_16_out, and_17_out,
       and_18_out, and_19_out, and_20_out, and_21_out, and_22_out, and_23_out, and_24_out, and_25_out,
       and_26_out, and_27_out, and_28_out, and_29_out, and_30_out, and_31_out, and_32_out, and_33_out,
       and_34_out, and_35_out, and_36_out, and_37_out, and_38_out, and_39_out, and_40_out, and_41_out,
       not_1_out, not_2_out, not_3_out, not_4_out, not_5_out, not_6_out, not_7_out, not_8_out, not_9_out,
       not_10_out, not_11_out, not_12_out, not_13_out, not_14_out, not_15_out, not_16_out, not_17_out,
       not_18_out, not_19_out, not_20_out, not_21_out, not_22_out, not_23_out, not_24_out, not_25_out,
       not_26_out, not_27_out, not_28_out, not_29_out, not_30_out, not_31_out, not_32_out, not_33_out,
       not_34_out, not_35_out, not_36_out, not_37_out, not_38_out, not_39_out, not_40_out, not_41_out,
       not_42_out, not_43_out, not_44_out, not_45_out, not_46_out, not_47_out, not_48_out, not_49_out,
       not_50_out, not_51_out, not_52_out, not_53_out, not_54_out, not_55_out, not_56_out, not_57_out,
       not_58_out, not_59_out, not_60_out, not_61_out, not_62_out, not_63_out, not_64_out, not_65_out,
       not_66_out, not_67_out, not_68_out, not_69_out, not_70_out, not_71_out, not_72_out, not_73_out,
       not_74_out, not_75_out, not_76_out, not_77_out, not_78_out, not_79_out, not_80_out, not_81_out,
       not_82_out, not_83_out, not_84_out, not_85_out, not_86_out, not_87_out, not_88_out, not_89_out,
       not_90_out, not_91_out, not_92_out, not_93_out, not_94_out, not_95_out, not_96_out, not_97_out,
       not_98_out, not_99_out, not_100_out, not_101_out, not_102_out, not_103_out, not_104_out, not_105_out,
       not_106_out, not_107_out, not_108_out, not_109_out, not_110_out, not_111_out, not_112_out,
       not_113_out, not_114_out, not_115_out, not_116_out, not_117_out, not_118_out, not_119_out,
       not_120_out, not_121_out, not_122_out, not_123_out, not_124_out, not_125_out, not_126_out,
       not_127_out, not_128_out, not_129_out, not_130_out, not_131_out, not_132_out, not_133_out,
       not_134_out, not_135_out, not_136_out, not_137_out, not_138_out, not_139_out, not_140_out,
       not_141_out, not_142_out, not_143_out, not_144_out, not_145_out, not_146_out, not_147_out,
       not_148_out, not_149_out, not_150_out, not_151_out, not_152_out, not_153_out, not_154_out,
       not_155_out, not_156_out, not_157_out, not_158_out, not_159_out, not_160_out, not_161_out,
       not_162_out, not_163_out, not_164_out, not_165_out, not_166_out, not_167_out, not_168_out,
       not_169_out, not_170_out, not_171_out, not_172_out, not_173_out, not_174_out, not_175_out,
       not_176_out, not_177_out, not_178_out, not_179_out, not_180_out, not_181_out, not_182_out,
       not_183_out, not_184_out, not_185_out, not_186_out, not_187_out, not_188_out, not_189_out,
       not_190_out, not_191_out, not_192_out, not_193_out, not_194_out, not_195_out, not_196_out,
       not_197_out, not_198_out, not_199_out, not_200_out, not_201_out, not_202_out, not_203_out,
       not_204_out, not_205_out, not_206_out, not_207_out, not_208_out, not_209_out, not_210_out,
       not_211_out, not_212_out, not_213_out, not_214_out, not_215_out, not_216_out, not_217_out,
       not_218_out, not_219_out, not_220_out, not_221_out, not_222_out, not_223_out, not_224_out,
       not_225_out, not_226_out, not_227_out, not_228_out, not_229_out, not_230_out, not_231_out,
       not_232_out, not_233_out, not_234_out, not_235_out, not_236_out, not_237_out, not_238_out,
       not_239_out, not_240_out, not_241_out, not_242_out, not_243_out, not_244_out, not_245_out,
       not_246_out, not_247_out, not_248_out, not_249_out, not_250_out, not_251_out, not_252_out,
       not_253_out, not_254_out, not_255_out, not_256_out, not_257_out, not_258_out, not_259_out,
       not_260_out, not_261_out, not_262_out, not_263_out, not_264_out, not_265_out, not_266_out,
       not_267_out, not_268_out, not_269_out, not_270_out, not_271_out, not_272_out;

  not not_1 (not_1_out, OP5);
  not not_2 (not_2_out, OP4);
  not not_3 (not_3_out, OP3);
  not not_4 (not_4_out, OP2);
  not not_5 (not_5_out, OP1);
  not not_6 (not_6_out, OP0);
  not not_7 (not_7_out, F5);
  not not_8 (not_8_out, F4);
  not not_9 (not_9_out, F3);
  not not_10 (not_10_out, F2);
  not not_11 (not_11_out, OP5);
  not not_12 (not_12_out, OP4);
  not not_13 (not_13_out, OP3);
  not not_14 (not_14_out, OP2);
  not not_15 (not_15_out, OP1);
  not not_16 (not_16_out, OP0);
  not not_17 (not_17_out, F4);
  not not_18 (not_18_out, F3);
  not not_19 (not_19_out, F2);
  not not_20 (not_20_out, F1);
  not not_21 (not_21_out, F0);
  not not_22 (not_22_out, OP5);
  not not_23 (not_23_out, OP4);
  not not_24 (not_24_out, OP3);
  not not_25 (not_25_out, OP2);
  not not_26 (not_26_out, OP1);
  not not_27 (not_27_out, OP0);
  not not_28 (not_28_out, F4);
  not not_29 (not_29_out, F3);
  not not_30 (not_30_out, F2);
  not not_31 (not_31_out, F1);
  not not_32 (not_32_out, OP5);
  not not_33 (not_33_out, OP4);
  not not_34 (not_34_out, OP3);
  not not_35 (not_35_out, OP2);
  not not_36 (not_36_out, OP1);
  not not_37 (not_37_out, OP0);
  not not_38 (not_38_out, F4);
  not not_39 (not_39_out, F3);
  not not_40 (not_40_out, F1);
  not not_41 (not_41_out, F0);
  not not_42 (not_42_out, OP5);
  not not_43 (not_43_out, OP4);
  not not_44 (not_44_out, OP3);
  not not_45 (not_45_out, OP2);
  not not_46 (not_46_out, OP1);
  not not_47 (not_47_out, OP0);
  not not_48 (not_48_out, F4);
  not not_49 (not_49_out, F2);
  not not_50 (not_50_out, F0);
  not not_51 (not_51_out, OP5);
  not not_52 (not_52_out, OP4);
  not not_53 (not_53_out, OP2);
  not not_54 (not_54_out, OP1);
  not not_55 (not_55_out, OP0);
  not not_56 (not_56_out, OP5);
  not not_57 (not_57_out, OP4);
  not not_58 (not_58_out, OP1);
  not not_59 (not_59_out, OP0);
  not not_60 (not_60_out, OP5);
  not not_61 (not_61_out, OP4);
  not not_62 (not_62_out, OP2);
  not not_63 (not_63_out, OP1);
  not not_64 (not_64_out, OP5);
  not not_65 (not_65_out, OP4);
  not not_66 (not_66_out, OP2);
  not not_67 (not_67_out, OP0);
  not not_68 (not_68_out, OP4);
  not not_69 (not_69_out, OP3);
  not not_70 (not_70_out, OP2);
  not not_71 (not_71_out, OP4);
  not not_72 (not_72_out, OP2);
  not not_73 (not_73_out, OP5);
  not not_74 (not_74_out, OP4);
  not not_75 (not_75_out, OP3);
  not not_76 (not_76_out, OP2);
  not not_77 (not_77_out, OP1);
  not not_78 (not_78_out, OP0);
  not not_79 (not_79_out, F4);
  not not_80 (not_80_out, F3);
  not not_81 (not_81_out, F0);
  not not_82 (not_82_out, OP4);
  not not_83 (not_83_out, OP2);
  not not_84 (not_84_out, OP1);
  not not_85 (not_85_out, OP5);
  not not_86 (not_86_out, OP4);
  not not_87 (not_87_out, OP3);
  not not_88 (not_88_out, OP0);
  not not_89 (not_89_out, OP5);
  not not_90 (not_90_out, OP4);
  not not_91 (not_91_out, OP3);
  not not_92 (not_92_out, OP2);
  not not_93 (not_93_out, OP1);
  not not_94 (not_94_out, OP0);
  not not_95 (not_95_out, F5);
  not not_96 (not_96_out, F4);
  not not_97 (not_97_out, F3);
  not not_98 (not_98_out, F2);
  not not_99 (not_99_out, F0);
  not not_100 (not_100_out, OP5);
  not not_101 (not_101_out, OP4);
  not not_102 (not_102_out, OP3);
  not not_103 (not_103_out, OP2);
  not not_104 (not_104_out, OP1);
  not not_105 (not_105_out, OP0);
  not not_106 (not_106_out, F4);
  not not_107 (not_107_out, F3);
  not not_108 (not_108_out, F2);
  not not_109 (not_109_out, F0);
  not not_110 (not_110_out, OP5);
  not not_111 (not_111_out, OP4);
  not not_112 (not_112_out, OP3);
  not not_113 (not_113_out, OP2);
  not not_114 (not_114_out, OP1);
  not not_115 (not_115_out, OP0);
  not not_116 (not_116_out, F4);
  not not_117 (not_117_out, F3);
  not not_118 (not_118_out, F1);
  not not_119 (not_119_out, F0);
  not not_120 (not_120_out, OP5);
  not not_121 (not_121_out, OP4);
  not not_122 (not_122_out, OP3);
  not not_123 (not_123_out, OP2);
  not not_124 (not_124_out, OP1);
  not not_125 (not_125_out, OP0);
  not not_126 (not_126_out, F4);
  not not_127 (not_127_out, F3);
  not not_128 (not_128_out, OP5);
  not not_129 (not_129_out, OP4);
  not not_130 (not_130_out, OP3);
  not not_131 (not_131_out, OP2);
  not not_132 (not_132_out, OP1);
  not not_133 (not_133_out, OP0);
  not not_134 (not_134_out, F4);
  not not_135 (not_135_out, F2);
  not not_136 (not_136_out, F0);
  not not_137 (not_137_out, OP5);
  not not_138 (not_138_out, OP4);
  not not_139 (not_139_out, OP1);
  not not_140 (not_140_out, OP0);
  not not_141 (not_141_out, OP5);
  not not_142 (not_142_out, OP4);
  not not_143 (not_143_out, OP2);
  not not_144 (not_144_out, OP0);
  not not_145 (not_145_out, OP5);
  not not_146 (not_146_out, OP4);
  not not_147 (not_147_out, OP3);
  not not_148 (not_148_out, OP0);
  not not_149 (not_149_out, OP5);
  not not_150 (not_150_out, OP4);
  not not_151 (not_151_out, OP3);
  not not_152 (not_152_out, OP2);
  not not_153 (not_153_out, OP1);
  not not_154 (not_154_out, OP0);
  not not_155 (not_155_out, F4);
  not not_156 (not_156_out, F3);
  not not_157 (not_157_out, F2);
  not not_158 (not_158_out, F1);
  not not_159 (not_159_out, F0);
  not not_160 (not_160_out, OP5);
  not not_161 (not_161_out, OP4);
  not not_162 (not_162_out, OP3);
  not not_163 (not_163_out, OP2);
  not not_164 (not_164_out, OP1);
  not not_165 (not_165_out, OP0);
  not not_166 (not_166_out, F4);
  not not_167 (not_167_out, F3);
  not not_168 (not_168_out, F2);
  not not_169 (not_169_out, F1);
  not not_170 (not_170_out, OP5);
  not not_171 (not_171_out, OP4);
  not not_172 (not_172_out, OP3);
  not not_173 (not_173_out, OP2);
  not not_174 (not_174_out, OP1);
  not not_175 (not_175_out, OP0);
  not not_176 (not_176_out, F4);
  not not_177 (not_177_out, F3);
  not not_178 (not_178_out, F2);
  not not_179 (not_179_out, F0);
  not not_180 (not_180_out, OP5);
  not not_181 (not_181_out, OP4);
  not not_182 (not_182_out, OP3);
  not not_183 (not_183_out, OP2);
  not not_184 (not_184_out, OP1);
  not not_185 (not_185_out, OP0);
  not not_186 (not_186_out, F4);
  not not_187 (not_187_out, F3);
  not not_188 (not_188_out, F1);
  not not_189 (not_189_out, F0);
  not not_190 (not_190_out, OP5);
  not not_191 (not_191_out, OP4);
  not not_192 (not_192_out, OP3);
  not not_193 (not_193_out, OP2);
  not not_194 (not_194_out, OP1);
  not not_195 (not_195_out, OP0);
  not not_196 (not_196_out, F4);
  not not_197 (not_197_out, F2);
  not not_198 (not_198_out, OP5);
  not not_199 (not_199_out, OP4);
  not not_200 (not_200_out, OP2);
  not not_201 (not_201_out, OP1);
  not not_202 (not_202_out, OP0);
  not not_203 (not_203_out, OP5);
  not not_204 (not_204_out, OP4);
  not not_205 (not_205_out, OP1);
  not not_206 (not_206_out, OP0);
  not not_207 (not_207_out, OP5);
  not not_208 (not_208_out, OP4);
  not not_209 (not_209_out, OP2);
  not not_210 (not_210_out, OP1);
  not not_211 (not_211_out, OP4);
  not not_212 (not_212_out, OP3);
  not not_213 (not_213_out, OP2);
  not not_214 (not_214_out, OP4);
  not not_215 (not_215_out, OP2);
  not not_216 (not_216_out, OP4);
  not not_217 (not_217_out, OP2);
  not not_218 (not_218_out, OP1);
  not not_219 (not_219_out, OP5);
  not not_220 (not_220_out, OP4);
  not not_221 (not_221_out, OP3);
  not not_222 (not_222_out, OP2);
  not not_223 (not_223_out, OP1);
  not not_224 (not_224_out, OP0);
  not not_225 (not_225_out, F4);
  not not_226 (not_226_out, F3);
  not not_227 (not_227_out, F1);
  not not_228 (not_228_out, OP5);
  not not_229 (not_229_out, OP4);
  not not_230 (not_230_out, OP3);
  not not_231 (not_231_out, OP2);
  not not_232 (not_232_out, OP1);
  not not_233 (not_233_out, OP0);
  not not_234 (not_234_out, F4);
  not not_235 (not_235_out, F3);
  not not_236 (not_236_out, OP5);
  not not_237 (not_237_out, OP4);
  not not_238 (not_238_out, OP3);
  not not_239 (not_239_out, OP2);
  not not_240 (not_240_out, OP1);
  not not_241 (not_241_out, OP0);
  not not_242 (not_242_out, F4);
  not not_243 (not_243_out, F2);
  not not_244 (not_244_out, F0);
  not not_245 (not_245_out, OP5);
  not not_246 (not_246_out, OP4);
  not not_247 (not_247_out, OP3);
  not not_248 (not_248_out, OP2);
  not not_249 (not_249_out, OP1);
  not not_250 (not_250_out, OP0);
  not not_251 (not_251_out, F4);
  not not_252 (not_252_out, F2);
  not not_253 (not_253_out, OP5);
  not not_254 (not_254_out, OP4);
  not not_255 (not_255_out, OP2);
  not not_256 (not_256_out, OP0);
  not not_257 (not_257_out, OP5);
  not not_258 (not_258_out, OP4);
  not not_259 (not_259_out, OP1);
  not not_260 (not_260_out, OP5);
  not not_261 (not_261_out, OP4);
  not not_262 (not_262_out, OP3);
  not not_263 (not_263_out, OP2);
  not not_264 (not_264_out, OP1);
  not not_265 (not_265_out, OP0);
  not not_266 (not_266_out, F4);
  not not_267 (not_267_out, F3);
  not not_268 (not_268_out, F0);
  not not_269 (not_269_out, OP5);
  not not_270 (not_270_out, OP4);
  not not_271 (not_271_out, OP3);
  not not_272 (not_272_out, OP0);
  and and_1 (and_1_out, not_1_out, not_2_out, not_3_out, not_4_out, not_5_out, not_6_out, not_7_out, not_8_out, not_9_out, not_10_out, F1, F0);
  and and_2 (and_2_out, not_11_out, not_12_out, not_13_out, not_14_out, not_15_out, not_16_out, F5, not_17_out, not_18_out, not_19_out, not_20_out, not_21_out);
  and and_3 (and_3_out, not_22_out, not_23_out, not_24_out, not_25_out, not_26_out, not_27_out, F5, not_28_out, not_29_out, not_30_out, not_31_out, F0);
  and and_4 (and_4_out, not_32_out, not_33_out, not_34_out, not_35_out, not_36_out, not_37_out, F5, not_38_out, not_39_out, F2, not_40_out, not_41_out);
  and and_5 (and_5_out, not_42_out, not_43_out, not_44_out, not_45_out, not_46_out, not_47_out, F5, not_48_out, F3, not_49_out, F1, not_50_out);
  and and_6 (and_6_out, not_51_out, not_52_out, OP3, not_53_out, not_54_out, not_55_out);
  and and_7 (and_7_out, not_56_out, not_57_out, OP3, OP2, not_58_out, not_59_out);
  and and_8 (and_8_out, not_60_out, not_61_out, OP3, not_62_out, not_63_out, OP0);
  and and_9 (and_9_out, not_64_out, not_65_out, OP3, not_66_out, OP1, not_67_out);
  and and_10 (and_10_out, OP5, not_68_out, not_69_out, not_70_out, OP1, OP0);
  and and_11 (and_11_out, OP5, not_71_out, OP3, not_72_out, OP1, OP0);
  and and_12 (and_12_out, not_73_out, not_74_out, not_75_out, not_76_out, not_77_out, not_78_out, F5, not_79_out, not_80_out, F2, F1, not_81_out);
  and and_13 (and_13_out, OP5, not_82_out, OP3, not_83_out, not_84_out, OP0);
  and and_14 (and_14_out, not_85_out, not_86_out, not_87_out, OP2, OP1, not_88_out);
  and and_15 (and_15_out, not_89_out, not_90_out, not_91_out, not_92_out, not_93_out, not_94_out, not_95_out, not_96_out, not_97_out, not_98_out, F1, not_99_out);
  and and_16 (and_16_out, not_100_out, not_101_out, not_102_out, not_103_out, not_104_out, not_105_out, F5, not_106_out, not_107_out, not_108_out, F1, not_109_out);
  and and_17 (and_17_out, not_110_out, not_111_out, not_112_out, not_113_out, not_114_out, not_115_out, F5, not_116_out, not_117_out, F2, not_118_out, not_119_out);
  and and_18 (and_18_out, not_120_out, not_121_out, not_122_out, not_123_out, not_124_out, not_125_out, F5, not_126_out, not_127_out, F2, F1, F0);
  and and_19 (and_19_out, not_128_out, not_129_out, not_130_out, not_131_out, not_132_out, not_133_out, F5, not_134_out, F3, not_135_out, F1, not_136_out);
  and and_20 (and_20_out, not_137_out, not_138_out, OP3, OP2, not_139_out, not_140_out);
  and and_21 (and_21_out, not_141_out, not_142_out, OP3, not_143_out, OP1, not_144_out);
  and and_22 (and_22_out, not_145_out, not_146_out, not_147_out, OP2, OP1, not_148_out);
  and and_23 (and_23_out, not_149_out, not_150_out, not_151_out, not_152_out, not_153_out, not_154_out, F5, not_155_out, not_156_out, not_157_out, not_158_out, not_159_out);
  and and_24 (and_24_out, not_160_out, not_161_out, not_162_out, not_163_out, not_164_out, not_165_out, F5, not_166_out, not_167_out, not_168_out, not_169_out, F0);
  and and_25 (and_25_out, not_170_out, not_171_out, not_172_out, not_173_out, not_174_out, not_175_out, F5, not_176_out, not_177_out, not_178_out, F1, not_179_out);
  and and_26 (and_26_out, not_180_out, not_181_out, not_182_out, not_183_out, not_184_out, not_185_out, F5, not_186_out, not_187_out, F2, not_188_out, not_189_out);
  and and_27 (and_27_out, not_190_out, not_191_out, not_192_out, not_193_out, not_194_out, not_195_out, F5, not_196_out, F3, not_197_out, F1, F0);
  and and_28 (and_28_out, not_198_out, not_199_out, OP3, not_200_out, not_201_out, not_202_out);
  and and_29 (and_29_out, not_203_out, not_204_out, OP3, OP2, not_205_out, not_206_out);
  and and_30 (and_30_out, not_207_out, not_208_out, OP3, not_209_out, not_210_out, OP0);
  and and_31 (and_31_out, OP5, not_211_out, not_212_out, not_213_out, OP1, OP0);
  and and_32 (and_32_out, OP5, not_214_out, OP3, not_215_out, OP1, OP0);
  and and_33 (and_33_out, OP5, not_216_out, OP3, not_217_out, not_218_out, OP0);
  and and_34 (and_34_out, not_219_out, not_220_out, not_221_out, not_222_out, not_223_out, not_224_out, F5, not_225_out, not_226_out, F2, not_227_out, F0);
  and and_35 (and_35_out, not_228_out, not_229_out, not_230_out, not_231_out, not_232_out, not_233_out, F5, not_234_out, not_235_out, F2, F1, F0);
  and and_36 (and_36_out, not_236_out, not_237_out, not_238_out, not_239_out, not_240_out, not_241_out, F5, not_242_out, F3, not_243_out, F1, not_244_out);
  and and_37 (and_37_out, not_245_out, not_246_out, not_247_out, not_248_out, not_249_out, not_250_out, F5, not_251_out, F3, not_252_out, F1, F0);
  and and_38 (and_38_out, not_253_out, not_254_out, OP3, not_255_out, OP1, not_256_out);
  and and_39 (and_39_out, not_257_out, not_258_out, OP3, OP2, not_259_out, OP0);
  and and_40 (and_40_out, not_260_out, not_261_out, not_262_out, not_263_out, not_264_out, not_265_out, F5, not_266_out, not_267_out, F2, F1, not_268_out);
  and and_41 (and_41_out, not_269_out, not_270_out, not_271_out, OP2, OP1, not_272_out);
  or or_1 (S1, and_15_out, and_16_out, and_17_out, and_18_out, and_19_out, and_20_out, and_21_out, and_22_out);
  or or_2 (S2, and_23_out, and_24_out, and_25_out, and_26_out, and_27_out, and_28_out, and_29_out, and_30_out, and_31_out, and_32_out, and_33_out);
  or or_3 (S3, and_34_out, and_35_out, and_36_out, and_37_out, and_38_out, and_39_out, and_40_out, and_41_out);
  or or_4 (S0, and_1_out, and_2_out, and_3_out, and_4_out, and_5_out, and_6_out, and_7_out, and_8_out, and_9_out, and_10_out, and_11_out, and_12_out, and_13_out, and_14_out);
endmodule

// 控制信号生成
module \控制信号生成  (
  input  OP0,
  input  OP1,
  input  OP2,
  input  OP3,
  input  OP4,
  input  OP5,
  input  F0,
  input  F1,
  input  F2,
  input  F3,
  input  F4,
  input  F5,
  output MemToReg,
  output MemWrite,
  output ALU_SRC,
  output RegWrite,
  output SysCALL,
  output SignedExt,
  output RegDst,
  output BEQ,
  output BNE,
  output JR,
  output JMP,
  output JAL
);

  wire and_2_out, and_3_out, and_4_out, and_5_out, and_6_out, and_7_out, and_8_out, and_9_out, and_10_out,
       and_11_out, and_12_out, and_13_out, and_14_out, and_15_out, and_16_out, and_17_out, and_18_out,
       and_19_out, and_20_out, and_21_out, and_22_out, and_23_out, and_24_out, and_25_out, and_26_out,
       and_27_out, and_28_out, and_29_out, and_30_out, and_31_out, and_32_out, and_34_out, and_35_out,
       and_36_out, and_37_out, and_38_out, and_39_out, and_40_out, and_41_out, and_42_out, and_43_out,
       and_44_out, and_45_out, and_46_out, and_47_out, and_48_out, and_49_out, and_50_out, and_54_out,
       and_55_out, and_56_out, not_1_out, not_2_out, not_3_out, not_4_out, not_5_out, not_6_out, not_7_out,
       not_8_out, not_9_out, not_10_out, not_11_out, not_12_out, not_13_out, not_14_out, not_15_out,
       not_16_out, not_17_out, not_18_out, not_19_out, not_20_out, not_21_out, not_22_out, not_23_out,
       not_24_out, not_25_out, not_26_out, not_27_out, not_28_out, not_29_out, not_30_out, not_31_out,
       not_32_out, not_33_out, not_34_out, not_35_out, not_36_out, not_37_out, not_38_out, not_39_out,
       not_40_out, not_41_out, not_42_out, not_43_out, not_44_out, not_45_out, not_46_out, not_47_out,
       not_48_out, not_49_out, not_50_out, not_51_out, not_52_out, not_53_out, not_54_out, not_55_out,
       not_56_out, not_57_out, not_58_out, not_59_out, not_60_out, not_61_out, not_62_out, not_63_out,
       not_64_out, not_65_out, not_66_out, not_67_out, not_68_out, not_69_out, not_70_out, not_71_out,
       not_72_out, not_73_out, not_74_out, not_75_out, not_76_out, not_77_out, not_78_out, not_79_out,
       not_80_out, not_81_out, not_82_out, not_83_out, not_84_out, not_85_out, not_86_out, not_87_out,
       not_88_out, not_89_out, not_90_out, not_91_out, not_92_out, not_93_out, not_94_out, not_95_out,
       not_96_out, not_97_out, not_98_out, not_99_out, not_100_out, not_101_out, not_102_out, not_103_out,
       not_104_out, not_105_out, not_106_out, not_107_out, not_108_out, not_109_out, not_110_out,
       not_111_out, not_112_out, not_113_out, not_114_out, not_115_out, not_116_out, not_117_out,
       not_118_out, not_119_out, not_120_out, not_121_out, not_122_out, not_123_out, not_124_out,
       not_125_out, not_126_out, not_127_out, not_128_out, not_129_out, not_130_out, not_131_out,
       not_132_out, not_133_out, not_134_out, not_135_out, not_136_out, not_137_out, not_138_out,
       not_139_out, not_140_out, not_141_out, not_142_out, not_143_out, not_144_out, not_145_out,
       not_146_out, not_147_out, not_148_out, not_149_out, not_150_out, not_151_out, not_152_out,
       not_153_out, not_154_out, not_155_out, not_156_out, not_157_out, not_158_out, not_159_out,
       not_160_out, not_161_out, not_162_out, not_163_out, not_164_out, not_165_out, not_166_out,
       not_167_out, not_168_out, not_169_out, not_170_out, not_171_out, not_172_out, not_173_out,
       not_174_out, not_175_out, not_176_out, not_177_out, not_178_out, not_179_out, not_180_out,
       not_181_out, not_182_out, not_183_out, not_184_out, not_185_out, not_186_out, not_187_out,
       not_188_out, not_189_out, not_190_out, not_191_out, not_192_out, not_193_out, not_194_out,
       not_195_out, not_196_out, not_197_out, not_198_out, not_199_out, not_200_out, not_201_out,
       not_202_out, not_203_out, not_204_out, not_205_out, not_206_out, not_207_out, not_208_out,
       not_209_out, not_210_out, not_211_out, not_212_out, not_213_out, not_214_out, not_215_out,
       not_216_out, not_217_out, not_218_out, not_219_out, not_220_out, not_221_out, not_222_out,
       not_223_out, not_224_out, not_225_out, not_226_out, not_227_out, not_228_out, not_229_out,
       not_230_out, not_231_out, not_232_out, not_233_out, not_234_out, not_235_out, not_236_out,
       not_237_out, not_238_out, not_239_out, not_240_out, not_241_out, not_242_out, not_243_out,
       not_244_out, not_245_out, not_246_out, not_247_out, not_248_out, not_249_out, not_250_out,
       not_251_out, not_252_out, not_253_out, not_254_out, not_255_out, not_256_out, not_257_out,
       not_258_out, not_259_out, not_260_out, not_261_out, not_262_out, not_263_out, not_264_out,
       not_265_out, not_266_out, not_267_out, not_268_out, not_269_out, not_270_out, not_271_out,
       not_272_out, not_273_out, not_274_out, not_275_out, not_276_out, not_277_out, not_278_out,
       not_279_out, not_280_out, not_281_out, not_282_out, not_283_out, not_284_out, not_285_out,
       not_286_out, not_287_out, not_288_out, not_289_out, not_290_out, not_291_out, not_292_out,
       not_293_out, not_294_out, not_295_out, not_296_out, not_297_out, not_298_out, not_299_out,
       not_300_out, not_301_out, not_302_out, not_303_out, not_304_out, not_305_out, not_306_out,
       not_307_out, not_308_out, not_309_out, not_310_out, not_311_out, not_312_out, not_313_out,
       not_314_out, not_315_out, not_316_out, not_317_out, not_318_out, not_319_out, not_320_out,
       not_321_out, not_322_out, not_323_out, not_324_out, not_325_out, not_326_out, not_327_out,
       not_328_out, not_329_out, not_330_out, not_331_out, not_332_out, not_333_out, not_334_out,
       not_335_out, not_336_out, not_337_out, not_338_out, not_339_out, not_340_out, not_341_out,
       not_342_out, not_343_out, not_344_out, not_345_out, not_346_out, not_347_out, not_348_out,
       not_349_out, not_350_out, not_351_out, not_352_out, not_353_out, not_354_out, not_355_out,
       not_356_out, not_357_out, not_358_out, not_359_out, not_360_out, not_361_out, not_362_out,
       not_363_out, not_364_out, not_365_out, not_366_out, not_367_out, not_368_out, not_369_out,
       not_370_out, not_371_out, not_372_out, not_373_out, not_374_out, not_375_out, not_376_out,
       not_377_out, not_378_out, not_379_out, not_380_out, not_381_out, not_382_out;

  not not_1 (not_1_out, OP4);
  not not_2 (not_2_out, OP3);
  not not_3 (not_3_out, OP2);
  not not_4 (not_4_out, OP4);
  not not_5 (not_5_out, OP2);
  not not_6 (not_6_out, OP4);
  not not_7 (not_7_out, OP2);
  not not_8 (not_8_out, OP1);
  not not_9 (not_9_out, OP5);
  not not_10 (not_10_out, OP4);
  not not_11 (not_11_out, OP2);
  not not_12 (not_12_out, OP1);
  not not_13 (not_13_out, OP0);
  not not_14 (not_14_out, OP5);
  not not_15 (not_15_out, OP4);
  not not_16 (not_16_out, OP1);
  not not_17 (not_17_out, OP0);
  not not_18 (not_18_out, OP5);
  not not_19 (not_19_out, OP4);
  not not_20 (not_20_out, OP2);
  not not_21 (not_21_out, OP1);
  not not_22 (not_22_out, OP5);
  not not_23 (not_23_out, OP4);
  not not_24 (not_24_out, OP2);
  not not_25 (not_25_out, OP0);
  not not_26 (not_26_out, OP5);
  not not_27 (not_27_out, OP4);
  not not_28 (not_28_out, OP1);
  not not_29 (not_29_out, OP4);
  not not_30 (not_30_out, OP3);
  not not_31 (not_31_out, OP2);
  not not_32 (not_32_out, OP4);
  not not_33 (not_33_out, OP2);
  not not_34 (not_34_out, OP5);
  not not_35 (not_35_out, OP4);
  not not_36 (not_36_out, OP4);
  not not_37 (not_37_out, OP2);
  not not_38 (not_38_out, OP1);
  not not_39 (not_39_out, OP5);
  not not_40 (not_40_out, OP4);
  not not_41 (not_41_out, OP3);
  not not_42 (not_42_out, OP2);
  not not_43 (not_43_out, OP1);
  not not_44 (not_44_out, OP0);
  not not_45 (not_45_out, F5);
  not not_46 (not_46_out, F4);
  not not_47 (not_47_out, F3);
  not not_48 (not_48_out, F2);
  not not_49 (not_49_out, F1);
  not not_50 (not_50_out, F0);
  not not_51 (not_51_out, OP5);
  not not_52 (not_52_out, OP4);
  not not_53 (not_53_out, OP3);
  not not_54 (not_54_out, OP2);
  not not_55 (not_55_out, OP1);
  not not_56 (not_56_out, OP0);
  not not_57 (not_57_out, F5);
  not not_58 (not_58_out, F4);
  not not_59 (not_59_out, F3);
  not not_60 (not_60_out, F2);
  not not_61 (not_61_out, OP5);
  not not_62 (not_62_out, OP4);
  not not_63 (not_63_out, OP3);
  not not_64 (not_64_out, OP2);
  not not_65 (not_65_out, OP1);
  not not_66 (not_66_out, OP0);
  not not_67 (not_67_out, F5);
  not not_68 (not_68_out, F4);
  not not_69 (not_69_out, F3);
  not not_70 (not_70_out, F2);
  not not_71 (not_71_out, F0);
  not not_72 (not_72_out, OP5);
  not not_73 (not_73_out, OP4);
  not not_74 (not_74_out, OP3);
  not not_75 (not_75_out, OP2);
  not not_76 (not_76_out, OP1);
  not not_77 (not_77_out, OP0);
  not not_78 (not_78_out, F4);
  not not_79 (not_79_out, F3);
  not not_80 (not_80_out, F2);
  not not_81 (not_81_out, F1);
  not not_82 (not_82_out, F0);
  not not_83 (not_83_out, OP5);
  not not_84 (not_84_out, OP4);
  not not_85 (not_85_out, OP3);
  not not_86 (not_86_out, OP2);
  not not_87 (not_87_out, OP1);
  not not_88 (not_88_out, OP0);
  not not_89 (not_89_out, F4);
  not not_90 (not_90_out, F3);
  not not_91 (not_91_out, F2);
  not not_92 (not_92_out, F1);
  not not_93 (not_93_out, OP5);
  not not_94 (not_94_out, OP4);
  not not_95 (not_95_out, OP3);
  not not_96 (not_96_out, OP2);
  not not_97 (not_97_out, OP1);
  not not_98 (not_98_out, OP0);
  not not_99 (not_99_out, F4);
  not not_100 (not_100_out, F3);
  not not_101 (not_101_out, F2);
  not not_102 (not_102_out, F0);
  not not_103 (not_103_out, OP5);
  not not_104 (not_104_out, OP4);
  not not_105 (not_105_out, OP3);
  not not_106 (not_106_out, OP2);
  not not_107 (not_107_out, OP1);
  not not_108 (not_108_out, OP0);
  not not_109 (not_109_out, F4);
  not not_110 (not_110_out, F3);
  not not_111 (not_111_out, F1);
  not not_112 (not_112_out, F0);
  not not_113 (not_113_out, OP5);
  not not_114 (not_114_out, OP4);
  not not_115 (not_115_out, OP3);
  not not_116 (not_116_out, OP2);
  not not_117 (not_117_out, OP1);
  not not_118 (not_118_out, OP0);
  not not_119 (not_119_out, F4);
  not not_120 (not_120_out, F3);
  not not_121 (not_121_out, F1);
  not not_122 (not_122_out, OP5);
  not not_123 (not_123_out, OP4);
  not not_124 (not_124_out, OP3);
  not not_125 (not_125_out, OP2);
  not not_126 (not_126_out, OP1);
  not not_127 (not_127_out, OP0);
  not not_128 (not_128_out, F4);
  not not_129 (not_129_out, F3);
  not not_130 (not_130_out, OP5);
  not not_131 (not_131_out, OP4);
  not not_132 (not_132_out, OP3);
  not not_133 (not_133_out, OP2);
  not not_134 (not_134_out, OP1);
  not not_135 (not_135_out, OP0);
  not not_136 (not_136_out, F4);
  not not_137 (not_137_out, F2);
  not not_138 (not_138_out, F0);
  not not_139 (not_139_out, OP5);
  not not_140 (not_140_out, OP4);
  not not_141 (not_141_out, OP3);
  not not_142 (not_142_out, OP2);
  not not_143 (not_143_out, OP1);
  not not_144 (not_144_out, OP0);
  not not_145 (not_145_out, F4);
  not not_146 (not_146_out, F2);
  not not_147 (not_147_out, OP5);
  not not_148 (not_148_out, OP4);
  not not_149 (not_149_out, OP3);
  not not_150 (not_150_out, OP2);
  not not_151 (not_151_out, OP5);
  not not_152 (not_152_out, OP4);
  not not_153 (not_153_out, OP2);
  not not_154 (not_154_out, OP1);
  not not_155 (not_155_out, OP0);
  not not_156 (not_156_out, OP5);
  not not_157 (not_157_out, OP4);
  not not_158 (not_158_out, OP1);
  not not_159 (not_159_out, OP0);
  not not_160 (not_160_out, OP5);
  not not_161 (not_161_out, OP4);
  not not_162 (not_162_out, OP2);
  not not_163 (not_163_out, OP1);
  not not_164 (not_164_out, OP5);
  not not_165 (not_165_out, OP4);
  not not_166 (not_166_out, OP2);
  not not_167 (not_167_out, OP0);
  not not_168 (not_168_out, OP5);
  not not_169 (not_169_out, OP4);
  not not_170 (not_170_out, OP1);
  not not_171 (not_171_out, OP4);
  not not_172 (not_172_out, OP3);
  not not_173 (not_173_out, OP2);
  not not_174 (not_174_out, OP5);
  not not_175 (not_175_out, OP4);
  not not_176 (not_176_out, OP3);
  not not_177 (not_177_out, OP2);
  not not_178 (not_178_out, OP1);
  not not_179 (not_179_out, OP0);
  not not_180 (not_180_out, F4);
  not not_181 (not_181_out, F3);
  not not_182 (not_182_out, F0);
  not not_183 (not_183_out, OP5);
  not not_184 (not_184_out, OP4);
  not not_185 (not_185_out, OP5);
  not not_186 (not_186_out, OP4);
  not not_187 (not_187_out, OP3);
  not not_188 (not_188_out, OP2);
  not not_189 (not_189_out, OP1);
  not not_190 (not_190_out, OP0);
  not not_191 (not_191_out, F5);
  not not_192 (not_192_out, F4);
  not not_193 (not_193_out, F1);
  not not_194 (not_194_out, F0);
  not not_195 (not_195_out, OP5);
  not not_196 (not_196_out, OP4);
  not not_197 (not_197_out, OP2);
  not not_198 (not_198_out, OP1);
  not not_199 (not_199_out, OP0);
  not not_200 (not_200_out, OP5);
  not not_201 (not_201_out, OP4);
  not not_202 (not_202_out, OP2);
  not not_203 (not_203_out, OP1);
  not not_204 (not_204_out, OP5);
  not not_205 (not_205_out, OP4);
  not not_206 (not_206_out, OP2);
  not not_207 (not_207_out, OP0);
  not not_208 (not_208_out, OP4);
  not not_209 (not_209_out, OP2);
  not not_210 (not_210_out, OP1);
  not not_211 (not_211_out, OP5);
  not not_212 (not_212_out, OP4);
  not not_213 (not_213_out, OP3);
  not not_214 (not_214_out, OP2);
  not not_215 (not_215_out, OP1);
  not not_216 (not_216_out, OP0);
  not not_217 (not_217_out, F5);
  not not_218 (not_218_out, F4);
  not not_219 (not_219_out, F3);
  not not_220 (not_220_out, F2);
  not not_221 (not_221_out, F1);
  not not_222 (not_222_out, F0);
  not not_223 (not_223_out, OP5);
  not not_224 (not_224_out, OP4);
  not not_225 (not_225_out, OP3);
  not not_226 (not_226_out, OP2);
  not not_227 (not_227_out, OP1);
  not not_228 (not_228_out, OP0);
  not not_229 (not_229_out, F5);
  not not_230 (not_230_out, F4);
  not not_231 (not_231_out, F3);
  not not_232 (not_232_out, F2);
  not not_233 (not_233_out, OP5);
  not not_234 (not_234_out, OP4);
  not not_235 (not_235_out, OP3);
  not not_236 (not_236_out, OP2);
  not not_237 (not_237_out, OP1);
  not not_238 (not_238_out, OP0);
  not not_239 (not_239_out, F5);
  not not_240 (not_240_out, F4);
  not not_241 (not_241_out, F3);
  not not_242 (not_242_out, F2);
  not not_243 (not_243_out, F0);
  not not_244 (not_244_out, OP5);
  not not_245 (not_245_out, OP4);
  not not_246 (not_246_out, OP3);
  not not_247 (not_247_out, OP2);
  not not_248 (not_248_out, OP1);
  not not_249 (not_249_out, OP0);
  not not_250 (not_250_out, F4);
  not not_251 (not_251_out, F3);
  not not_252 (not_252_out, F2);
  not not_253 (not_253_out, F1);
  not not_254 (not_254_out, F0);
  not not_255 (not_255_out, OP5);
  not not_256 (not_256_out, OP4);
  not not_257 (not_257_out, OP3);
  not not_258 (not_258_out, OP2);
  not not_259 (not_259_out, OP1);
  not not_260 (not_260_out, OP0);
  not not_261 (not_261_out, F4);
  not not_262 (not_262_out, F3);
  not not_263 (not_263_out, F2);
  not not_264 (not_264_out, F1);
  not not_265 (not_265_out, OP5);
  not not_266 (not_266_out, OP4);
  not not_267 (not_267_out, OP3);
  not not_268 (not_268_out, OP2);
  not not_269 (not_269_out, OP1);
  not not_270 (not_270_out, OP0);
  not not_271 (not_271_out, F4);
  not not_272 (not_272_out, F3);
  not not_273 (not_273_out, F2);
  not not_274 (not_274_out, F0);
  not not_275 (not_275_out, OP5);
  not not_276 (not_276_out, OP4);
  not not_277 (not_277_out, OP3);
  not not_278 (not_278_out, OP2);
  not not_279 (not_279_out, OP1);
  not not_280 (not_280_out, OP0);
  not not_281 (not_281_out, F4);
  not not_282 (not_282_out, F3);
  not not_283 (not_283_out, F1);
  not not_284 (not_284_out, F0);
  not not_285 (not_285_out, OP5);
  not not_286 (not_286_out, OP4);
  not not_287 (not_287_out, OP3);
  not not_288 (not_288_out, OP2);
  not not_289 (not_289_out, OP1);
  not not_290 (not_290_out, OP0);
  not not_291 (not_291_out, F4);
  not not_292 (not_292_out, F3);
  not not_293 (not_293_out, F1);
  not not_294 (not_294_out, OP5);
  not not_295 (not_295_out, OP4);
  not not_296 (not_296_out, OP3);
  not not_297 (not_297_out, OP2);
  not not_298 (not_298_out, OP1);
  not not_299 (not_299_out, OP0);
  not not_300 (not_300_out, F4);
  not not_301 (not_301_out, F3);
  not not_302 (not_302_out, OP5);
  not not_303 (not_303_out, OP4);
  not not_304 (not_304_out, OP3);
  not not_305 (not_305_out, OP2);
  not not_306 (not_306_out, OP1);
  not not_307 (not_307_out, OP0);
  not not_308 (not_308_out, F4);
  not not_309 (not_309_out, F2);
  not not_310 (not_310_out, F0);
  not not_311 (not_311_out, OP5);
  not not_312 (not_312_out, OP4);
  not not_313 (not_313_out, OP3);
  not not_314 (not_314_out, OP2);
  not not_315 (not_315_out, OP1);
  not not_316 (not_316_out, OP0);
  not not_317 (not_317_out, F4);
  not not_318 (not_318_out, F2);
  not not_319 (not_319_out, OP5);
  not not_320 (not_320_out, OP4);
  not not_321 (not_321_out, OP3);
  not not_322 (not_322_out, OP2);
  not not_323 (not_323_out, OP1);
  not not_324 (not_324_out, OP0);
  not not_325 (not_325_out, F5);
  not not_326 (not_326_out, F4);
  not not_327 (not_327_out, F2);
  not not_328 (not_328_out, F1);
  not not_329 (not_329_out, F0);
  not not_330 (not_330_out, OP5);
  not not_331 (not_331_out, OP4);
  not not_332 (not_332_out, OP3);
  not not_333 (not_333_out, OP2);
  not not_334 (not_334_out, OP1);
  not not_335 (not_335_out, OP0);
  not not_336 (not_336_out, F4);
  not not_337 (not_337_out, F3);
  not not_338 (not_338_out, F0);
  not not_339 (not_339_out, OP5);
  not not_340 (not_340_out, OP4);
  not not_341 (not_341_out, OP3);
  not not_342 (not_342_out, OP1);
  not not_343 (not_343_out, OP0);
  not not_344 (not_344_out, OP5);
  not not_345 (not_345_out, OP4);
  not not_346 (not_346_out, OP3);
  not not_347 (not_347_out, OP1);
  not not_348 (not_348_out, OP5);
  not not_349 (not_349_out, OP4);
  not not_350 (not_350_out, OP3);
  not not_351 (not_351_out, OP2);
  not not_352 (not_352_out, OP1);
  not not_353 (not_353_out, OP0);
  not not_354 (not_354_out, F5);
  not not_355 (not_355_out, F4);
  not not_356 (not_356_out, F2);
  not not_357 (not_357_out, F1);
  not not_358 (not_358_out, F0);
  not not_359 (not_359_out, OP5);
  not not_360 (not_360_out, OP4);
  not not_361 (not_361_out, OP3);
  not not_362 (not_362_out, OP2);
  not not_363 (not_363_out, OP1);
  not not_364 (not_364_out, OP0);
  not not_365 (not_365_out, F5);
  not not_366 (not_366_out, F4);
  not not_367 (not_367_out, F2);
  not not_368 (not_368_out, F1);
  not not_369 (not_369_out, F0);
  not not_370 (not_370_out, OP5);
  not not_371 (not_371_out, OP4);
  not not_372 (not_372_out, OP3);
  not not_373 (not_373_out, OP2);
  not not_374 (not_374_out, OP0);
  not not_375 (not_375_out, OP5);
  not not_376 (not_376_out, OP4);
  not not_377 (not_377_out, OP3);
  not not_378 (not_378_out, OP2);
  not not_379 (not_379_out, OP5);
  not not_380 (not_380_out, OP4);
  not not_381 (not_381_out, OP3);
  not not_382 (not_382_out, OP2);
  and and_1 (MemToReg, OP5, not_1_out, not_2_out, not_3_out, OP1, OP0);
  and and_2 (and_2_out, OP5, not_4_out, OP3, not_5_out, OP1, OP0);
  and and_3 (and_3_out, OP5, not_6_out, OP3, not_7_out, not_8_out, OP0);
  and and_4 (and_4_out, not_9_out, not_10_out, OP3, not_11_out, not_12_out, not_13_out);
  and and_5 (and_5_out, not_14_out, not_15_out, OP3, OP2, not_16_out, not_17_out);
  and and_6 (and_6_out, not_18_out, not_19_out, OP3, not_20_out, not_21_out, OP0);
  and and_7 (and_7_out, not_22_out, not_23_out, OP3, not_24_out, OP1, not_25_out);
  and and_8 (and_8_out, not_26_out, not_27_out, OP3, OP2, not_28_out, OP0);
  and and_9 (and_9_out, OP5, not_29_out, not_30_out, not_31_out, OP1, OP0);
  and and_10 (and_10_out, OP5, not_32_out, OP3, not_33_out, OP1, OP0);
  and and_11 (and_11_out, not_34_out, not_35_out, OP3, OP2, OP1, OP0);
  and and_12 (and_12_out, OP5, not_36_out, OP3, not_37_out, not_38_out, OP0);
  and and_13 (and_13_out, not_39_out, not_40_out, not_41_out, not_42_out, not_43_out, not_44_out, not_45_out, not_46_out, not_47_out, not_48_out, not_49_out, not_50_out);
  and and_14 (and_14_out, not_51_out, not_52_out, not_53_out, not_54_out, not_55_out, not_56_out, not_57_out, not_58_out, not_59_out, not_60_out, F1, F0);
  and and_15 (and_15_out, not_61_out, not_62_out, not_63_out, not_64_out, not_65_out, not_66_out, not_67_out, not_68_out, not_69_out, not_70_out, F1, not_71_out);
  and and_16 (and_16_out, not_72_out, not_73_out, not_74_out, not_75_out, not_76_out, not_77_out, F5, not_78_out, not_79_out, not_80_out, not_81_out, not_82_out);
  and and_17 (and_17_out, not_83_out, not_84_out, not_85_out, not_86_out, not_87_out, not_88_out, F5, not_89_out, not_90_out, not_91_out, not_92_out, F0);
  and and_18 (and_18_out, not_93_out, not_94_out, not_95_out, not_96_out, not_97_out, not_98_out, F5, not_99_out, not_100_out, not_101_out, F1, not_102_out);
  and and_19 (and_19_out, not_103_out, not_104_out, not_105_out, not_106_out, not_107_out, not_108_out, F5, not_109_out, not_110_out, F2, not_111_out, not_112_out);
  and and_20 (and_20_out, not_113_out, not_114_out, not_115_out, not_116_out, not_117_out, not_118_out, F5, not_119_out, not_120_out, F2, not_121_out, F0);
  and and_21 (and_21_out, not_122_out, not_123_out, not_124_out, not_125_out, not_126_out, not_127_out, F5, not_128_out, not_129_out, F2, F1, F0);
  and and_22 (and_22_out, not_130_out, not_131_out, not_132_out, not_133_out, not_134_out, not_135_out, F5, not_136_out, F3, not_137_out, F1, not_138_out);
  and and_23 (and_23_out, not_139_out, not_140_out, not_141_out, not_142_out, not_143_out, not_144_out, F5, not_145_out, F3, not_146_out, F1, F0);
  and and_24 (and_24_out, not_147_out, not_148_out, not_149_out, not_150_out, OP1, OP0);
  and and_25 (and_25_out, not_151_out, not_152_out, OP3, not_153_out, not_154_out, not_155_out);
  and and_26 (and_26_out, not_156_out, not_157_out, OP3, OP2, not_158_out, not_159_out);
  and and_27 (and_27_out, not_160_out, not_161_out, OP3, not_162_out, not_163_out, OP0);
  and and_28 (and_28_out, not_164_out, not_165_out, OP3, not_166_out, OP1, not_167_out);
  and and_29 (and_29_out, not_168_out, not_169_out, OP3, OP2, not_170_out, OP0);
  and and_30 (and_30_out, OP5, not_171_out, not_172_out, not_173_out, OP1, OP0);
  and and_31 (and_31_out, not_174_out, not_175_out, not_176_out, not_177_out, not_178_out, not_179_out, F5, not_180_out, not_181_out, F2, F1, not_182_out);
  and and_32 (and_32_out, not_183_out, not_184_out, OP3, OP2, OP1, OP0);
  and and_33 (SysCALL, not_185_out, not_186_out, not_187_out, not_188_out, not_189_out, not_190_out, not_191_out, not_192_out, F3, F2, not_193_out, not_194_out);
  and and_34 (and_34_out, not_195_out, not_196_out, OP3, not_197_out, not_198_out, not_199_out);
  and and_35 (and_35_out, not_200_out, not_201_out, OP3, not_202_out, not_203_out, OP0);
  and and_36 (and_36_out, not_204_out, not_205_out, OP3, not_206_out, OP1, not_207_out);
  and and_37 (and_37_out, OP5, not_208_out, OP3, not_209_out, not_210_out, OP0);
  and and_38 (and_38_out, not_211_out, not_212_out, not_213_out, not_214_out, not_215_out, not_216_out, not_217_out, not_218_out, not_219_out, not_220_out, not_221_out, not_222_out);
  and and_39 (and_39_out, not_223_out, not_224_out, not_225_out, not_226_out, not_227_out, not_228_out, not_229_out, not_230_out, not_231_out, not_232_out, F1, F0);
  and and_40 (and_40_out, not_233_out, not_234_out, not_235_out, not_236_out, not_237_out, not_238_out, not_239_out, not_240_out, not_241_out, not_242_out, F1, not_243_out);
  and and_41 (and_41_out, not_244_out, not_245_out, not_246_out, not_247_out, not_248_out, not_249_out, F5, not_250_out, not_251_out, not_252_out, not_253_out, not_254_out);
  and and_42 (and_42_out, not_255_out, not_256_out, not_257_out, not_258_out, not_259_out, not_260_out, F5, not_261_out, not_262_out, not_263_out, not_264_out, F0);
  and and_43 (and_43_out, not_265_out, not_266_out, not_267_out, not_268_out, not_269_out, not_270_out, F5, not_271_out, not_272_out, not_273_out, F1, not_274_out);
  and and_44 (and_44_out, not_275_out, not_276_out, not_277_out, not_278_out, not_279_out, not_280_out, F5, not_281_out, not_282_out, F2, not_283_out, not_284_out);
  and and_45 (and_45_out, not_285_out, not_286_out, not_287_out, not_288_out, not_289_out, not_290_out, F5, not_291_out, not_292_out, F2, not_293_out, F0);
  and and_46 (and_46_out, not_294_out, not_295_out, not_296_out, not_297_out, not_298_out, not_299_out, F5, not_300_out, not_301_out, F2, F1, F0);
  and and_47 (and_47_out, not_302_out, not_303_out, not_304_out, not_305_out, not_306_out, not_307_out, F5, not_308_out, F3, not_309_out, F1, not_310_out);
  and and_48 (and_48_out, not_311_out, not_312_out, not_313_out, not_314_out, not_315_out, not_316_out, F5, not_317_out, F3, not_318_out, F1, F0);
  and and_49 (and_49_out, not_319_out, not_320_out, not_321_out, not_322_out, not_323_out, not_324_out, not_325_out, not_326_out, F3, not_327_out, not_328_out, not_329_out);
  and and_50 (and_50_out, not_330_out, not_331_out, not_332_out, not_333_out, not_334_out, not_335_out, F5, not_336_out, not_337_out, F2, F1, not_338_out);
  and and_51 (BEQ, not_339_out, not_340_out, not_341_out, OP2, not_342_out, not_343_out);
  and and_52 (BNE, not_344_out, not_345_out, not_346_out, OP2, not_347_out, OP0);
  and and_53 (JR, not_348_out, not_349_out, not_350_out, not_351_out, not_352_out, not_353_out, not_354_out, not_355_out, F3, not_356_out, not_357_out, not_358_out);
  and and_54 (and_54_out, not_359_out, not_360_out, not_361_out, not_362_out, not_363_out, not_364_out, not_365_out, not_366_out, F3, not_367_out, not_368_out, not_369_out);
  and and_55 (and_55_out, not_370_out, not_371_out, not_372_out, not_373_out, OP1, not_374_out);
  and and_56 (and_56_out, not_375_out, not_376_out, not_377_out, not_378_out, OP1, OP0);
  and and_57 (JAL, not_379_out, not_380_out, not_381_out, not_382_out, OP1, OP0);
  or or_1 (MemWrite, and_2_out, and_3_out);
  or or_2 (ALU_SRC, and_4_out, and_5_out, and_6_out, and_7_out, and_8_out, and_9_out, and_10_out, and_11_out, and_12_out);
  or or_3 (SignedExt, and_34_out, and_35_out, and_36_out, and_37_out);
  or or_4 (JMP, and_54_out, and_55_out, and_56_out);
  or or_5 (RegWrite, and_13_out, and_14_out, and_15_out, and_16_out, and_17_out, and_18_out, and_19_out, and_20_out, and_21_out, and_22_out, and_23_out, and_24_out, and_25_out, and_26_out, and_27_out, and_28_out, and_29_out, and_30_out, and_31_out, and_32_out);
  or or_6 (RegDst, and_38_out, and_39_out, and_40_out, and_41_out, and_42_out, and_43_out, and_44_out, and_45_out, and_46_out, and_47_out, and_48_out, and_49_out, and_50_out);
endmodule

// ALU
module MIPS_ALU (
  input  [4:0] shamt,
  input  [31:0] X,
  input  [31:0] Y,
  input  [3:0] AluOP,
  output Equal,
  output [31:0] Result,
  output [31:0] Result_2
);

  wire [0:0] comparator_1_lt, comparator_2_lt;
  wire [31:0] adder_1_out, AND_out, divider_1_out, divider_1_rem, multiplier_1_cout, multiplier_1_out,
       NOR_out, OR_out, shifter_1_out, shifter_2_out, shifter_3_out, subtractor_1_out, XOR_out;

  assign AND_out = X & Y;  // AND_Gate AND, 32 bits wide
  assign OR_out = X | Y;  // OR_Gate OR, 32 bits wide
  Shifter #(.width(32)) shifter_1 (.in(Y), .\dist (shamt), .out(shifter_1_out));
  Shifter #(.width(32), .shift("ar")) shifter_2 (.in(Y), .\dist (shamt), .out(shifter_2_out));
  Shifter #(.width(32), .shift("lr")) shifter_3 (.in(Y), .\dist (shamt), .out(shifter_3_out));
  Multiplier #(.width(32)) multiplier_1 (.a(X), .b(Y), .out(multiplier_1_out), .cout(multiplier_1_cout));  // open: cin
  Divider #(.width(32)) divider_1 (.a(X), .b(Y), .out(divider_1_out), .rem(divider_1_rem));  // open: upper
  Adder #(.width(32)) adder_1 (.a(X), .b(Y), .out(adder_1_out));  // open: cin, cout
  Subtractor #(.width(32)) subtractor_1 (.a(X), .b(Y), .out(subtractor_1_out));  // open: bin, bout
  assign XOR_out = X ^ Y;  // XOR_Gate XOR, 32 bits wide
  assign NOR_out = ~(X | Y);  // NOR_Gate NOR, 32 bits wide
  Comparator #(.width(32)) comparator_1 (.a(X), .b(Y), .eq(Equal), .lt(comparator_1_lt[0]));  // open: gt
  Comparator #(.width(32), .mode("unsigned")) comparator_2 (.a(X), .b(Y), .lt(comparator_2_lt[0]));  // open: gt, eq
  Multiplexer #(.select(4), .width(32), .enable("false")) multiplexer_1 (
    .in0(shifter_1_out), .in1(shifter_2_out), .in2(shifter_3_out), .in3(multiplier_1_out),
    .in4(divider_1_out), .in5(adder_1_out), .in6(subtractor_1_out), .in7(AND_out), .in8(OR_out),
    .in9(XOR_out), .in10(NOR_out), .in11({{31{1'b0}}, comparator_1_lt[0]}),
    .in12({{31{1'b0}}, comparator_2_lt[0]}), .in13({32{1'b0}}), .in14({32{1'b0}}), .in15({32{1'b0}}),
    .out(Result), .sel(AluOP));
  Multiplexer #(.select(4), .width(32), .enable("false")) multiplexer_2 (
    .in0({32{1'b0}}), .in1({32{1'b0}}), .in2({32{1'b0}}), .in3(multiplier_1_cout), .in4(divider_1_rem),
    .in5({32{1'b0}}), .in6({32{1'b0}}), .in7({32{1'b0}}), .in8({32{1'b0}}), .in9({32{1'b0}}),
    .in10({32{1'b0}}), .in11({32{1'b0}}), .in12({32{1'b0}}), .in13({32{1'b0}}), .in14({32{1'b0}}),
    .in15({32{1'b0}}), .out(Result_2), .sel(AluOP));

  // Other names for the same wires on the sheet: Result2[31:0] = Result_2; S[3:0] = AluOP

  // Notes on the sheet:
  //   不要改变此引脚区域内容，也不要改变ALU封装形式
  //   输入引脚
  //   输出引脚
endmodule

module MIPS_Regifile (
  input  [31:0] Din,
  input  Clk,
  input  WE,
  input  [4:0] R1_num,
  input  [4:0] W_num,
  input  [4:0] R2_num,
  output [31:0] R1,
  output [31:0] R2
);

  // RegisterFile registerfile_1: pin names not known; wires that end beside it: Din, Clk, WE, W_num, R1_num, R2_num, R1, R2
endmodule

module \理想流水线  (
);

  wire and_1_out, and_2_out, and_3_out, and_4_out, CLK, comparator_1_eq, d_ff_1_qn, ex_mem_1_mtr_2,
       ex_mem_1_mw_2, ex_mem_1_regd_2, ex_mem_1_regw_2, ex_mem_1_sys_2, Go, IR1, IR2, IR3, JMP,
       mem_wb_1_mtr_2, mem_wb_1_regd_2, not_1_out, not_2_out, not_4_out, PCEnable, REGW, RST, run, SignedExt,
       SYS, undriven, undriven_2, undriven_4, undriven_5, undriven_6, undriven_7, v, W1, W2, W3, \条件分支 ,
       \硬布线控制器_1_p5 , \硬布线控制器_1_p6 , \硬布线控制器_1_p7 , \硬布线控制器_1_p8 , \硬布线控制器_1_p9 , \硬布线控制器_1_p10 ,
       \硬布线控制器_1_p11 , \硬布线控制器_1_p12 , \硬布线控制器_1_p13 ;
  wire [3:0] undriven_3;
  wire [4:0] multiplexer_2_out, multiplexer_3_out, undriven_12, W_num;
  wire [15:0] \LoadUse次数 , \总周期数 , \插入气泡数 , \无条件分支数 , \条件分支成功数 ;
  wire [31:0] A, adder_1_out, B, bit_extender_1_out, bit_extender_2_out, ex_mem_1_a_2, ex_mem_1_alu_2,
       ex_mem_1_b_2, ex_mem_1_id_2, EX_PC, id_ex_1_p18, id_ex_1_p19, ID_PC, if_id_1_id_2, IF_PC, LedData,
       MEM_PC, mem_wb_1_alu_2, mem_wb_1_id_2, mem_wb_1_md_2, mips_alu_1_result, multiplexer_1_out,
       multiplexer_4_out, multiplexer_5_out, multiplexer_6_out, R2, ram_1_data, RDIN, rom_1_data, undriven_8,
       undriven_9, undriven_10, undriven_11, WB_PC;

  Button \u_总复位  (.out(RST));
  Button _1 (.out(IR1));
  Button _2 (.out(IR2));
  Button _3 (.out(IR3));
  Button \u_继续运行  (.out(Go));
  LED led_1 (.in(W1));
  LED led_2 (.in(W2));
  LED led_3 (.in(W3));
  not not_1 (not_1_out, run);
  Register #(.width(32)) PC (.D(adder_1_out), .en(run), .Q(IF_PC), .clk(CLK), .clr(RST));
  Comparator #(.width(32)) comparator_1 (.a(A), .b(32'h22), .eq(comparator_1_eq));  // open: gt, lt
  Hex_Digit_Display hex_digit_display_1 (.value(LedData[31:28]));  // open: dp
  not not_2 (not_2_out, comparator_1_eq);
  and and_1 (and_1_out, comparator_1_eq, SYS);
  Register #(.width(32)) register_1 (.D(multiplexer_1_out), .Q(LedData), .clk(CLK));  // open: en, clr
  Multiplexer #(.width(32), .enable("false")) multiplexer_1 (
    .in0(LedData), .in1(R2), .out(multiplexer_1_out), .sel(and_1_out));
  Hex_Digit_Display hex_digit_display_2 (.value(LedData[23:20]));  // open: dp
  Hex_Digit_Display hex_digit_display_3 (.value(LedData[27:24]));  // open: dp
  Adder #(.width(32)) adder_1 (.a(IF_PC), .b(32'h4), .out(adder_1_out));  // open: cin, cout
  D_Flip_Flop d_ff_1 (.clk(CLK), .D(Go), .Qn(d_ff_1_qn));  // open: Q, preset, en, reset
  Hex_Digit_Display hex_digit_display_4 (.value(LedData[15:12]));  // open: dp
  Hex_Digit_Display hex_digit_display_5 (.value(LedData[19:16]));  // open: dp
  ROM #(.addrWidth(10), .dataWidth(32)) rom_1 (.addr(IF_PC[11:2]), .data(rom_1_data));  // open: sel
  and and_2 (and_2_out, d_ff_1_qn, SYS, not_2_out);
  Hex_Digit_Display hex_digit_display_6 (.value(LedData[11:8]));  // open: dp
  Hex_Digit_Display hex_digit_display_7 (.value(LedData[7:4]));  // open: dp
  Clock clock_1 (.out(CLK));
  not not_3 (PCEnable, and_2_out);
  Hex_Digit_Display hex_digit_display_8 (.value(LedData[3:0]));  // open: dp
  IF_ID if_id_1 (
    .PC(adder_1_out), .ID(rom_1_data), .CLK(CLK), .PC_2(ID_PC), .ID_2(if_id_1_id_2), .\同步清零_气泡_高电平有效 (RST),
    .\使能端_低电平有效_stall_高电平有效 (not_1_out));
  // 硬布线控制器 硬布线控制器_1: pin names not known; wires that end beside it: JMP, SignedExt, if_id_1_id_2[31:26], if_id_1_id_2[5:0], \硬布线控制器_1_p5 , \硬布线控制器_1_p6 , \硬布线控制器_1_p7 , \硬布线控制器_1_p8 , \硬布线控制器_1_p9 , \硬布线控制器_1_p10 , \硬布线控制器_1_p11 , \硬布线控制器_1_p12 , \硬布线控制器_1_p13 
  // Probe on \总周期数 
  // Probe on \无条件分支数 
  // Probe on \条件分支成功数 
  // Probe on \插入气泡数 
  // Probe on \LoadUse次数 
  assign bit_extender_1_out = {{16{1'b0}}, if_id_1_id_2[15:0]};  // Bit_Extender bit_extender_1
  assign bit_extender_2_out = {{16{if_id_1_id_2[15]}}, if_id_1_id_2[15:0]};  // Bit_Extender bit_extender_2
  Comparator #(.width(32)) comparator_2 (.a(32'h22), .b(A), .eq(v));  // open: gt, lt
  // Probe on IF_PC[11:0]
  or or_1 (\条件分支 , \硬布线控制器_1_p6 , \硬布线控制器_1_p7 );
  Multiplexer #(.width(5), .enable("false")) multiplexer_2 (
    .in0(if_id_1_id_2[25:21]), .in1(5'b00010), .out(multiplexer_2_out), .sel(\硬布线控制器_1_p5 ));
  Multiplexer #(.width(5), .enable("false")) multiplexer_3 (
    .in0(if_id_1_id_2[20:16]), .in1(5'b00100), .out(multiplexer_3_out), .sel(\硬布线控制器_1_p5 ));
  Multiplexer #(.width(32), .enable("false")) multiplexer_4 (
    .in0(bit_extender_1_out), .in1(bit_extender_2_out), .out(multiplexer_4_out), .sel(SignedExt));
  // Probe on ID_PC[11:0]
  not not_4 (not_4_out, v);
  // Probe on MEM_PC[11:0]
  // Probe on EX_PC[11:0]
  // ID_EX id_ex_1: pin names not known; wires that end beside it: \硬布线控制器_1_p8 , \硬布线控制器_1_p9 , \硬布线控制器_1_p10 , \硬布线控制器_1_p11 , \硬布线控制器_1_p12 , \硬布线控制器_1_p13 , if_id_1_id_2[10:6], not_1_out, \硬布线控制器_1_p8 , \硬布线控制器_1_p9 , \硬布线控制器_1_p10 , \硬布线控制器_1_p11 , \硬布线控制器_1_p12 , \硬布线控制器_1_p13 , \硬布线控制器_1_p5 , ID_PC, if_id_1_id_2, id_ex_1_p18, id_ex_1_p19, multiplexer_4_out, if_id_1_id_2[10:6], CLK, RST
  MIPS_Regifile mips_regifile_1 (
    .Din(RDIN), .Clk(CLK), .R1(id_ex_1_p18), .R2(id_ex_1_p19), .WE(REGW), .W_num(W_num),
    .R1_num(multiplexer_2_out), .R2_num(multiplexer_3_out));
  // Probe on WB_PC[11:0]
  and and_3 (and_3_out, v, SYS);
  not not_5 (run, and_4_out);
  and and_4 (and_4_out, ~Go, SYS, not_4_out);  // AND_Gate
  Register #(.width(32)) register_2 (.D(multiplexer_5_out), .Q(LedData), .clk(CLK), .clr(RST));  // open: en
  Multiplexer #(.width(32), .enable("false")) multiplexer_5 (
    .in0(LedData), .in1(B), .out(multiplexer_5_out), .sel(and_3_out));
  Multiplexer #(.width(32), .enable("false")) multiplexer_6 (
    .in0(undriven_10), .in1(undriven_11), .out(multiplexer_6_out), .sel(undriven_4));
  MIPS_ALU mips_alu_1 (
    .X(undriven_9), .Y(multiplexer_6_out), .AluOP(undriven_3), .Result(mips_alu_1_result), .shamt(undriven_12));  // open: Equal, Result_2
  EX_MEM ex_mem_1 (
    .MTR(undriven), .MW(undriven_2), .REGW(undriven_5), .REGD(undriven_6), .SYS(undriven_7), .PC(EX_PC),
    .ID(undriven_8), .A(undriven_9), .B(undriven_10), .ALU(mips_alu_1_result), .CLK(CLK),
    .MTR_2(ex_mem_1_mtr_2), .MW_2(ex_mem_1_mw_2), .REGW_2(ex_mem_1_regw_2), .REGD_2(ex_mem_1_regd_2),
    .SYS_2(ex_mem_1_sys_2), .PC_2(MEM_PC), .ID_2(ex_mem_1_id_2), .A_2(ex_mem_1_a_2), .B_2(ex_mem_1_b_2),
    .ALU_2(ex_mem_1_alu_2), .\同步清零_气泡_高电平有效 (RST), .\使能端_低电平有效_stall_高电平有效 (not_1_out));  // open: JAL, JAL_2, blez, blezout, sh, shout, lui, luiout, xor, xorout
  Counter #(.width(16), .max('hffff)) counter_1 (
    .count(run), .Q(\总周期数 ), .clk(CLK), .clr(RST));  // open: load, D, carry
  Counter #(.width(16), .max('hffff)) counter_2 (
    .count(JMP), .Q(\无条件分支数 ), .clk(CLK), .clr(RST));  // open: load, D, carry
  Counter #(.width(16), .max('hffff)) counter_3 (
    .count(\条件分支 ), .Q(\条件分支成功数 ), .clk(CLK), .clr(RST));  // open: load, D, carry
  RAM #(.addrWidth(10), .dataWidth(32), .bus("separate")) ram_1 (
    .addr(ex_mem_1_alu_2[11:2]), .din(ex_mem_1_b_2), .data(ram_1_data), .str(ex_mem_1_mw_2), .clk(CLK),
    .clr(RST));  // open: sel, ld
  MEM_WB mem_wb_1 (
    .MTR(ex_mem_1_mtr_2), .REGW(ex_mem_1_regw_2), .REGD(ex_mem_1_regd_2), .SYS(ex_mem_1_sys_2), .PC(MEM_PC),
    .ID(ex_mem_1_id_2), .A(ex_mem_1_a_2), .MD(ram_1_data), .B(ex_mem_1_b_2), .ALU(ex_mem_1_alu_2), .CLK(CLK),
    .MTR_2(mem_wb_1_mtr_2), .REGW_2(REGW), .REGD_2(mem_wb_1_regd_2), .SYS_2(SYS), .PC_2(WB_PC),
    .ID_2(mem_wb_1_id_2), .A_2(A), .MD_2(mem_wb_1_md_2), .B_2(B), .ALU_2(mem_wb_1_alu_2),
    .\同步清零_气泡_高电平有效 (RST), .\使能端_低电平有效_stall_高电平有效 (not_1_out));  // open: JAL, JAL_2, blez, blezout, sh, shout, lui, luiout, xor, xorout
  Multiplexer #(.width(32), .enable("false")) multiplexer_7 (
    .in0(mem_wb_1_alu_2), .in1(mem_wb_1_md_2), .out(RDIN), .sel(mem_wb_1_mtr_2));
  Multiplexer #(.width(5), .enable("false")) multiplexer_8 (
    .in0(mem_wb_1_id_2[20:16]), .in1(mem_wb_1_id_2[15:11]), .out(W_num), .sel(mem_wb_1_regd_2));

  // Notes on the sheet:
  //   中断源
  //   中断等待指示
  //   指令存储器
  //   数码管输出
  //   contents of rom_1 (hex, n*v repeats v):
  //   20100000 20110001 20120002 20130003 36100000 36310001 36520002 36730003 ae100000 ae110004 ae120008
  //   ae13000c 2002000a 0 0 0 c
  //   OP
  //   Func
  //   rs
  //   rt
  //   rd
  //   流水调试日志用
  //   rt
  //   rd
endmodule

// 源寄存器使用情况
module \源寄存器使用情况  (
  input  OP0,
  input  OP1,
  input  OP2,
  input  OP3,
  input  OP4,
  input  OP5,
  input  F0,
  input  F1,
  input  F2,
  input  F3,
  input  F4,
  input  F5,
  output R1_Used,
  output R2_Used
);

  wire and_1_out, and_2_out, and_3_out, and_4_out, and_5_out, and_6_out, and_7_out, and_8_out, and_9_out,
       and_10_out, and_11_out, and_12_out, and_13_out, and_14_out, and_15_out, and_16_out, and_17_out,
       and_18_out, and_19_out, and_20_out, and_21_out, and_22_out, and_23_out, and_24_out, and_25_out,
       and_26_out, and_27_out, and_28_out, and_29_out, and_30_out, and_31_out, and_32_out, and_33_out,
       and_34_out, and_35_out, and_36_out, and_37_out, and_38_out, and_39_out, and_40_out, not_1_out,
       not_2_out, not_3_out, not_4_out, not_5_out, not_6_out, not_7_out, not_8_out, not_9_out, not_10_out,
       not_11_out, not_12_out, not_13_out, not_14_out, not_15_out, not_16_out, not_17_out, not_18_out,
       not_19_out, not_20_out, not_21_out, not_22_out, not_23_out, not_24_out, not_25_out, not_26_out,
       not_27_out, not_28_out, not_29_out, not_30_out, not_31_out, not_32_out, not_33_out, not_34_out,
       not_35_out, not_36_out, not_37_out, not_38_out, not_39_out, not_40_out, not_41_out, not_42_out,
       not_43_out, not_44_out, not_45_out, not_46_out, not_47_out, not_48_out, not_49_out, not_50_out,
       not_51_out, not_52_out, not_53_out, not_54_out, not_55_out, not_56_out, not_57_out, not_58_out,
       not_59_out, not_60_out, not_61_out, not_62_out, not_63_out, not_64_out, not_65_out, not_66_out,
       not_67_out, not_68_out, not_69_out, not_70_out, not_71_out, not_72_out, not_73_out, not_74_out,
       not_75_out, not_76_out, not_77_out, not_78_out, not_79_out, not_80_out, not_81_out, not_82_out,
       not_83_out, not_84_out, not_85_out, not_86_out, not_87_out, not_88_out, not_89_out, not_90_out,
       not_91_out, not_92_out, not_93_out, not_94_out, not_95_out, not_96_out, not_97_out, not_98_out,
       not_99_out, not_100_out, not_101_out, not_102_out, not_103_out, not_104_out, not_105_out, not_106_out,
       not_107_out, not_108_out, not_109_out, not_110_out, not_111_out, not_112_out, not_113_out,
       not_114_out, not_115_out, not_116_out, not_117_out, not_118_out, not_119_out, not_120_out,
       not_121_out, not_122_out, not_123_out, not_124_out, not_125_out, not_126_out, not_127_out,
       not_128_out, not_129_out, not_130_out, not_131_out, not_132_out, not_133_out, not_134_out,
       not_135_out, not_136_out, not_137_out, not_138_out, not_139_out, not_140_out, not_141_out,
       not_142_out, not_143_out, not_144_out, not_145_out, not_146_out, not_147_out, not_148_out,
       not_149_out, not_150_out, not_151_out, not_152_out, not_153_out, not_154_out, not_155_out,
       not_156_out, not_157_out, not_158_out, not_159_out, not_160_out, not_161_out, not_162_out,
       not_163_out, not_164_out, not_165_out, not_166_out, not_167_out, not_168_out, not_169_out,
       not_170_out, not_171_out, not_172_out, not_173_out, not_174_out, not_175_out, not_176_out,
       not_177_out, not_178_out, not_179_out, not_180_out, not_181_out, not_182_out, not_183_out,
       not_184_out, not_185_out, not_186_out, not_187_out, not_188_out, not_189_out, not_190_out,
       not_191_out, not_192_out, not_193_out, not_194_out, not_195_out, not_196_out, not_197_out,
       not_198_out, not_199_out, not_200_out, not_201_out, not_202_out, not_203_out, not_204_out,
       not_205_out, not_206_out, not_207_out, not_208_out, not_209_out, not_210_out, not_211_out,
       not_212_out, not_213_out, not_214_out, not_215_out, not_216_out, not_217_out, not_218_out,
       not_219_out, not_220_out, not_221_out, not_222_out, not_223_out, not_224_out, not_225_out,
       not_226_out, not_227_out, not_228_out, not_229_out, not_230_out, not_231_out, not_232_out,
       not_233_out, not_234_out, not_235_out, not_236_out, not_237_out, not_238_out, not_239_out,
       not_240_out, not_241_out, not_242_out, not_243_out, not_244_out, not_245_out, not_246_out,
       not_247_out, not_248_out, not_249_out, not_250_out, not_251_out, not_252_out, not_253_out,
       not_254_out, not_255_out, not_256_out, not_257_out, not_258_out, not_259_out, not_260_out,
       not_261_out, not_262_out, not_263_out, not_264_out, not_265_out, not_266_out, not_267_out,
       not_268_out, not_269_out, not_270_out, not_271_out, not_272_out, not_273_out, not_274_out,
       not_275_out, not_276_out, not_277_out, not_278_out, not_279_out, not_280_out, not_281_out,
       not_282_out, not_283_out, not_284_out, not_285_out, not_286_out, not_287_out, not_288_out, not_289_out;

  not not_1 (not_1_out, OP5);
  not not_2 (not_2_out, OP4);
  not not_3 (not_3_out, OP3);
  not not_4 (not_4_out, OP2);
  not not_5 (not_5_out, OP1);
  not not_6 (not_6_out, OP0);
  not not_7 (not_7_out, F4);
  not not_8 (not_8_out, F3);
  not not_9 (not_9_out, F2);
  not not_10 (not_10_out, F1);
  not not_11 (not_11_out, F0);
  not not_12 (not_12_out, OP5);
  not not_13 (not_13_out, OP4);
  not not_14 (not_14_out, OP3);
  not not_15 (not_15_out, OP2);
  not not_16 (not_16_out, OP1);
  not not_17 (not_17_out, OP0);
  not not_18 (not_18_out, F4);
  not not_19 (not_19_out, F3);
  not not_20 (not_20_out, F2);
  not not_21 (not_21_out, F1);
  not not_22 (not_22_out, OP5);
  not not_23 (not_23_out, OP4);
  not not_24 (not_24_out, OP3);
  not not_25 (not_25_out, OP2);
  not not_26 (not_26_out, OP1);
  not not_27 (not_27_out, OP0);
  not not_28 (not_28_out, F4);
  not not_29 (not_29_out, F3);
  not not_30 (not_30_out, F2);
  not not_31 (not_31_out, F0);
  not not_32 (not_32_out, OP5);
  not not_33 (not_33_out, OP4);
  not not_34 (not_34_out, OP3);
  not not_35 (not_35_out, OP2);
  not not_36 (not_36_out, OP1);
  not not_37 (not_37_out, OP0);
  not not_38 (not_38_out, F4);
  not not_39 (not_39_out, F3);
  not not_40 (not_40_out, F1);
  not not_41 (not_41_out, F0);
  not not_42 (not_42_out, OP5);
  not not_43 (not_43_out, OP4);
  not not_44 (not_44_out, OP3);
  not not_45 (not_45_out, OP2);
  not not_46 (not_46_out, OP1);
  not not_47 (not_47_out, OP0);
  not not_48 (not_48_out, F4);
  not not_49 (not_49_out, F3);
  not not_50 (not_50_out, F1);
  not not_51 (not_51_out, OP5);
  not not_52 (not_52_out, OP4);
  not not_53 (not_53_out, OP3);
  not not_54 (not_54_out, OP2);
  not not_55 (not_55_out, OP1);
  not not_56 (not_56_out, OP0);
  not not_57 (not_57_out, F4);
  not not_58 (not_58_out, F3);
  not not_59 (not_59_out, OP5);
  not not_60 (not_60_out, OP4);
  not not_61 (not_61_out, OP3);
  not not_62 (not_62_out, OP2);
  not not_63 (not_63_out, OP1);
  not not_64 (not_64_out, OP0);
  not not_65 (not_65_out, F4);
  not not_66 (not_66_out, F2);
  not not_67 (not_67_out, F0);
  not not_68 (not_68_out, OP5);
  not not_69 (not_69_out, OP4);
  not not_70 (not_70_out, OP3);
  not not_71 (not_71_out, OP2);
  not not_72 (not_72_out, OP1);
  not not_73 (not_73_out, OP0);
  not not_74 (not_74_out, F4);
  not not_75 (not_75_out, F2);
  not not_76 (not_76_out, OP5);
  not not_77 (not_77_out, OP4);
  not not_78 (not_78_out, OP3);
  not not_79 (not_79_out, OP2);
  not not_80 (not_80_out, OP1);
  not not_81 (not_81_out, OP0);
  not not_82 (not_82_out, F5);
  not not_83 (not_83_out, F4);
  not not_84 (not_84_out, F2);
  not not_85 (not_85_out, F1);
  not not_86 (not_86_out, F0);
  not not_87 (not_87_out, OP5);
  not not_88 (not_88_out, OP4);
  not not_89 (not_89_out, OP3);
  not not_90 (not_90_out, OP2);
  not not_91 (not_91_out, OP1);
  not not_92 (not_92_out, OP0);
  not not_93 (not_93_out, F5);
  not not_94 (not_94_out, F4);
  not not_95 (not_95_out, F1);
  not not_96 (not_96_out, F0);
  not not_97 (not_97_out, OP5);
  not not_98 (not_98_out, OP4);
  not not_99 (not_99_out, OP3);
  not not_100 (not_100_out, OP1);
  not not_101 (not_101_out, OP0);
  not not_102 (not_102_out, OP5);
  not not_103 (not_103_out, OP4);
  not not_104 (not_104_out, OP3);
  not not_105 (not_105_out, OP1);
  not not_106 (not_106_out, OP5);
  not not_107 (not_107_out, OP4);
  not not_108 (not_108_out, OP2);
  not not_109 (not_109_out, OP1);
  not not_110 (not_110_out, OP0);
  not not_111 (not_111_out, OP5);
  not not_112 (not_112_out, OP4);
  not not_113 (not_113_out, OP1);
  not not_114 (not_114_out, OP0);
  not not_115 (not_115_out, OP5);
  not not_116 (not_116_out, OP4);
  not not_117 (not_117_out, OP2);
  not not_118 (not_118_out, OP1);
  not not_119 (not_119_out, OP5);
  not not_120 (not_120_out, OP4);
  not not_121 (not_121_out, OP2);
  not not_122 (not_122_out, OP0);
  not not_123 (not_123_out, OP5);
  not not_124 (not_124_out, OP4);
  not not_125 (not_125_out, OP1);
  not not_126 (not_126_out, OP4);
  not not_127 (not_127_out, OP3);
  not not_128 (not_128_out, OP2);
  not not_129 (not_129_out, OP4);
  not not_130 (not_130_out, OP2);
  not not_131 (not_131_out, OP5);
  not not_132 (not_132_out, OP4);
  not not_133 (not_133_out, OP3);
  not not_134 (not_134_out, OP2);
  not not_135 (not_135_out, OP1);
  not not_136 (not_136_out, OP0);
  not not_137 (not_137_out, F4);
  not not_138 (not_138_out, F3);
  not not_139 (not_139_out, F0);
  not not_140 (not_140_out, OP4);
  not not_141 (not_141_out, OP2);
  not not_142 (not_142_out, OP1);
  not not_143 (not_143_out, OP5);
  not not_144 (not_144_out, OP4);
  not not_145 (not_145_out, OP3);
  not not_146 (not_146_out, OP0);
  not not_147 (not_147_out, OP5);
  not not_148 (not_148_out, OP4);
  not not_149 (not_149_out, OP3);
  not not_150 (not_150_out, OP2);
  not not_151 (not_151_out, OP1);
  not not_152 (not_152_out, OP0);
  not not_153 (not_153_out, F5);
  not not_154 (not_154_out, F4);
  not not_155 (not_155_out, F3);
  not not_156 (not_156_out, F2);
  not not_157 (not_157_out, F1);
  not not_158 (not_158_out, F0);
  not not_159 (not_159_out, OP5);
  not not_160 (not_160_out, OP4);
  not not_161 (not_161_out, OP3);
  not not_162 (not_162_out, OP2);
  not not_163 (not_163_out, OP1);
  not not_164 (not_164_out, OP0);
  not not_165 (not_165_out, F5);
  not not_166 (not_166_out, F4);
  not not_167 (not_167_out, F3);
  not not_168 (not_168_out, F2);
  not not_169 (not_169_out, OP5);
  not not_170 (not_170_out, OP4);
  not not_171 (not_171_out, OP3);
  not not_172 (not_172_out, OP2);
  not not_173 (not_173_out, OP1);
  not not_174 (not_174_out, OP0);
  not not_175 (not_175_out, F5);
  not not_176 (not_176_out, F4);
  not not_177 (not_177_out, F3);
  not not_178 (not_178_out, F2);
  not not_179 (not_179_out, F0);
  not not_180 (not_180_out, OP5);
  not not_181 (not_181_out, OP4);
  not not_182 (not_182_out, OP3);
  not not_183 (not_183_out, OP2);
  not not_184 (not_184_out, OP1);
  not not_185 (not_185_out, OP0);
  not not_186 (not_186_out, F4);
  not not_187 (not_187_out, F3);
  not not_188 (not_188_out, F2);
  not not_189 (not_189_out, F1);
  not not_190 (not_190_out, F0);
  not not_191 (not_191_out, OP5);
  not not_192 (not_192_out, OP4);
  not not_193 (not_193_out, OP3);
  not not_194 (not_194_out, OP2);
  not not_195 (not_195_out, OP1);
  not not_196 (not_196_out, OP0);
  not not_197 (not_197_out, F4);
  not not_198 (not_198_out, F3);
  not not_199 (not_199_out, F2);
  not not_200 (not_200_out, F1);
  not not_201 (not_201_out, OP5);
  not not_202 (not_202_out, OP4);
  not not_203 (not_203_out, OP3);
  not not_204 (not_204_out, OP2);
  not not_205 (not_205_out, OP1);
  not not_206 (not_206_out, OP0);
  not not_207 (not_207_out, F4);
  not not_208 (not_208_out, F3);
  not not_209 (not_209_out, F2);
  not not_210 (not_210_out, F0);
  not not_211 (not_211_out, OP5);
  not not_212 (not_212_out, OP4);
  not not_213 (not_213_out, OP3);
  not not_214 (not_214_out, OP2);
  not not_215 (not_215_out, OP1);
  not not_216 (not_216_out, OP0);
  not not_217 (not_217_out, F4);
  not not_218 (not_218_out, F3);
  not not_219 (not_219_out, F1);
  not not_220 (not_220_out, F0);
  not not_221 (not_221_out, OP5);
  not not_222 (not_222_out, OP4);
  not not_223 (not_223_out, OP3);
  not not_224 (not_224_out, OP2);
  not not_225 (not_225_out, OP1);
  not not_226 (not_226_out, OP0);
  not not_227 (not_227_out, F4);
  not not_228 (not_228_out, F3);
  not not_229 (not_229_out, F1);
  not not_230 (not_230_out, OP5);
  not not_231 (not_231_out, OP4);
  not not_232 (not_232_out, OP3);
  not not_233 (not_233_out, OP2);
  not not_234 (not_234_out, OP1);
  not not_235 (not_235_out, OP0);
  not not_236 (not_236_out, F4);
  not not_237 (not_237_out, F3);
  not not_238 (not_238_out, OP5);
  not not_239 (not_239_out, OP4);
  not not_240 (not_240_out, OP3);
  not not_241 (not_241_out, OP2);
  not not_242 (not_242_out, OP1);
  not not_243 (not_243_out, OP0);
  not not_244 (not_244_out, F4);
  not not_245 (not_245_out, F2);
  not not_246 (not_246_out, F0);
  not not_247 (not_247_out, OP5);
  not not_248 (not_248_out, OP4);
  not not_249 (not_249_out, OP3);
  not not_250 (not_250_out, OP2);
  not not_251 (not_251_out, OP1);
  not not_252 (not_252_out, OP0);
  not not_253 (not_253_out, F4);
  not not_254 (not_254_out, F2);
  not not_255 (not_255_out, OP5);
  not not_256 (not_256_out, OP4);
  not not_257 (not_257_out, OP3);
  not not_258 (not_258_out, OP2);
  not not_259 (not_259_out, OP1);
  not not_260 (not_260_out, OP0);
  not not_261 (not_261_out, F5);
  not not_262 (not_262_out, F4);
  not not_263 (not_263_out, F1);
  not not_264 (not_264_out, F0);
  not not_265 (not_265_out, OP5);
  not not_266 (not_266_out, OP4);
  not not_267 (not_267_out, OP3);
  not not_268 (not_268_out, OP1);
  not not_269 (not_269_out, OP0);
  not not_270 (not_270_out, OP5);
  not not_271 (not_271_out, OP4);
  not not_272 (not_272_out, OP3);
  not not_273 (not_273_out, OP1);
  not not_274 (not_274_out, OP4);
  not not_275 (not_275_out, OP2);
  not not_276 (not_276_out, OP5);
  not not_277 (not_277_out, OP4);
  not not_278 (not_278_out, OP3);
  not not_279 (not_279_out, OP2);
  not not_280 (not_280_out, OP1);
  not not_281 (not_281_out, OP0);
  not not_282 (not_282_out, F4);
  not not_283 (not_283_out, F3);
  not not_284 (not_284_out, F0);
  not not_285 (not_285_out, OP5);
  not not_286 (not_286_out, OP4);
  not not_287 (not_287_out, OP4);
  not not_288 (not_288_out, OP2);
  not not_289 (not_289_out, OP1);
  and and_1 (and_1_out, not_1_out, not_2_out, not_3_out, not_4_out, not_5_out, not_6_out, F5, not_7_out, not_8_out, not_9_out, not_10_out, not_11_out);
  and and_2 (and_2_out, not_12_out, not_13_out, not_14_out, not_15_out, not_16_out, not_17_out, F5, not_18_out, not_19_out, not_20_out, not_21_out, F0);
  and and_3 (and_3_out, not_22_out, not_23_out, not_24_out, not_25_out, not_26_out, not_27_out, F5, not_28_out, not_29_out, not_30_out, F1, not_31_out);
  and and_4 (and_4_out, not_32_out, not_33_out, not_34_out, not_35_out, not_36_out, not_37_out, F5, not_38_out, not_39_out, F2, not_40_out, not_41_out);
  and and_5 (and_5_out, not_42_out, not_43_out, not_44_out, not_45_out, not_46_out, not_47_out, F5, not_48_out, not_49_out, F2, not_50_out, F0);
  and and_6 (and_6_out, not_51_out, not_52_out, not_53_out, not_54_out, not_55_out, not_56_out, F5, not_57_out, not_58_out, F2, F1, F0);
  and and_7 (and_7_out, not_59_out, not_60_out, not_61_out, not_62_out, not_63_out, not_64_out, F5, not_65_out, F3, not_66_out, F1, not_67_out);
  and and_8 (and_8_out, not_68_out, not_69_out, not_70_out, not_71_out, not_72_out, not_73_out, F5, not_74_out, F3, not_75_out, F1, F0);
  and and_9 (and_9_out, not_76_out, not_77_out, not_78_out, not_79_out, not_80_out, not_81_out, not_82_out, not_83_out, F3, not_84_out, not_85_out, not_86_out);
  and and_10 (and_10_out, not_87_out, not_88_out, not_89_out, not_90_out, not_91_out, not_92_out, not_93_out, not_94_out, F3, F2, not_95_out, not_96_out);
  and and_11 (and_11_out, not_97_out, not_98_out, not_99_out, OP2, not_100_out, not_101_out);
  and and_12 (and_12_out, not_102_out, not_103_out, not_104_out, OP2, not_105_out, OP0);
  and and_13 (and_13_out, not_106_out, not_107_out, OP3, not_108_out, not_109_out, not_110_out);
  and and_14 (and_14_out, not_111_out, not_112_out, OP3, OP2, not_113_out, not_114_out);
  and and_15 (and_15_out, not_115_out, not_116_out, OP3, not_117_out, not_118_out, OP0);
  and and_16 (and_16_out, not_119_out, not_120_out, OP3, not_121_out, OP1, not_122_out);
  and and_17 (and_17_out, not_123_out, not_124_out, OP3, OP2, not_125_out, OP0);
  and and_18 (and_18_out, OP5, not_126_out, not_127_out, not_128_out, OP1, OP0);
  and and_19 (and_19_out, OP5, not_129_out, OP3, not_130_out, OP1, OP0);
  and and_20 (and_20_out, not_131_out, not_132_out, not_133_out, not_134_out, not_135_out, not_136_out, F5, not_137_out, not_138_out, F2, F1, not_139_out);
  and and_21 (and_21_out, OP5, not_140_out, OP3, not_141_out, not_142_out, OP0);
  and and_22 (and_22_out, not_143_out, not_144_out, not_145_out, OP2, OP1, not_146_out);
  and and_23 (and_23_out, not_147_out, not_148_out, not_149_out, not_150_out, not_151_out, not_152_out, not_153_out, not_154_out, not_155_out, not_156_out, not_157_out, not_158_out);
  and and_24 (and_24_out, not_159_out, not_160_out, not_161_out, not_162_out, not_163_out, not_164_out, not_165_out, not_166_out, not_167_out, not_168_out, F1, F0);
  and and_25 (and_25_out, not_169_out, not_170_out, not_171_out, not_172_out, not_173_out, not_174_out, not_175_out, not_176_out, not_177_out, not_178_out, F1, not_179_out);
  and and_26 (and_26_out, not_180_out, not_181_out, not_182_out, not_183_out, not_184_out, not_185_out, F5, not_186_out, not_187_out, not_188_out, not_189_out, not_190_out);
  and and_27 (and_27_out, not_191_out, not_192_out, not_193_out, not_194_out, not_195_out, not_196_out, F5, not_197_out, not_198_out, not_199_out, not_200_out, F0);
  and and_28 (and_28_out, not_201_out, not_202_out, not_203_out, not_204_out, not_205_out, not_206_out, F5, not_207_out, not_208_out, not_209_out, F1, not_210_out);
  and and_29 (and_29_out, not_211_out, not_212_out, not_213_out, not_214_out, not_215_out, not_216_out, F5, not_217_out, not_218_out, F2, not_219_out, not_220_out);
  and and_30 (and_30_out, not_221_out, not_222_out, not_223_out, not_224_out, not_225_out, not_226_out, F5, not_227_out, not_228_out, F2, not_229_out, F0);
  and and_31 (and_31_out, not_230_out, not_231_out, not_232_out, not_233_out, not_234_out, not_235_out, F5, not_236_out, not_237_out, F2, F1, F0);
  and and_32 (and_32_out, not_238_out, not_239_out, not_240_out, not_241_out, not_242_out, not_243_out, F5, not_244_out, F3, not_245_out, F1, not_246_out);
  and and_33 (and_33_out, not_247_out, not_248_out, not_249_out, not_250_out, not_251_out, not_252_out, F5, not_253_out, F3, not_254_out, F1, F0);
  and and_34 (and_34_out, not_255_out, not_256_out, not_257_out, not_258_out, not_259_out, not_260_out, not_261_out, not_262_out, F3, F2, not_263_out, not_264_out);
  and and_35 (and_35_out, not_265_out, not_266_out, not_267_out, OP2, not_268_out, not_269_out);
  and and_36 (and_36_out, not_270_out, not_271_out, not_272_out, OP2, not_273_out, OP0);
  and and_37 (and_37_out, OP5, not_274_out, OP3, not_275_out, OP1, OP0);
  and and_38 (and_38_out, not_276_out, not_277_out, not_278_out, not_279_out, not_280_out, not_281_out, F5, not_282_out, not_283_out, F2, F1, not_284_out);
  and and_39 (and_39_out, not_285_out, not_286_out, OP3, OP2, OP1, OP0);
  and and_40 (and_40_out, OP5, not_287_out, OP3, not_288_out, not_289_out, OP0);
  or or_1 (R1_Used, and_1_out, and_2_out, and_3_out, and_4_out, and_5_out, and_6_out, and_7_out, and_8_out, and_9_out, and_10_out, and_11_out, and_12_out, and_13_out, and_14_out, and_15_out, and_16_out, and_17_out, and_18_out, and_19_out, and_20_out, and_21_out, and_22_out);
  or or_2 (R2_Used, and_23_out, and_24_out, and_25_out, and_26_out, and_27_out, and_28_out, and_29_out, and_30_out, and_31_out, and_32_out, and_33_out, and_34_out, and_35_out, and_36_out, and_37_out, and_38_out, and_39_out, and_40_out);
endmodule

module \数据相关检测  (
  input  [5:0] OP,
  input  [4:0] EX_WriteReg_num,
  input  EX_RegWrite,
  input  [4:0] MEM_WriteReg_num,
  input  MEM_RegWrite,
  input  [5:0] Func,
  input  [4:0] ID_R1_num,
  input  [4:0] ID_R2_num,
  output \数据相关 ,
  output \R1冲突 ,
  output R1EX,
  output \Mem相关 ,
  output \R2冲突 ,
  output R2EX,
  output \EX相关 
);

  wire and_1_out, and_2_out, and_3_out, and_4_out, and_5_out, and_6_out, and_7_out, and_8_out, and_9_out,
       and_10_out, comparator_1_eq, comparator_2_eq, comparator_3_eq, comparator_4_eq, comparator_5_eq,
       comparator_6_eq, or_3_out, or_4_out, \源寄存器使用情况_1_p13 , \源寄存器使用情况_1_p14 ;

  // 源寄存器使用情况 源寄存器使用情况_1: pin names not known; wires that end beside it: OP[0], OP[1], OP[2], OP[3], OP[4], OP[5], Func[0], Func[1], Func[2], Func[3], Func[4], Func[5], \源寄存器使用情况_1_p13 , \源寄存器使用情况_1_p14 
  Comparator #(.width(5)) comparator_1 (.a(ID_R1_num), .b({5{1'b0}}), .eq(comparator_1_eq));  // open: gt, lt
  Comparator #(.width(5)) comparator_2 (.a(ID_R2_num), .b({5{1'b0}}), .eq(comparator_2_eq));  // open: gt, lt
  Comparator #(.width(5)) comparator_3 (.a(ID_R1_num), .b(MEM_WriteReg_num), .eq(comparator_3_eq));  // open: gt, lt
  Comparator #(.width(5)) comparator_4 (.a(ID_R1_num), .b(EX_WriteReg_num), .eq(comparator_4_eq));  // open: gt, lt
  Comparator #(.width(5)) comparator_5 (.a(ID_R2_num), .b(MEM_WriteReg_num), .eq(comparator_5_eq));  // open: gt, lt
  Comparator #(.width(5)) comparator_6 (.a(ID_R2_num), .b(EX_WriteReg_num), .eq(comparator_6_eq));  // open: gt, lt
  and and_1 (and_1_out, comparator_3_eq, MEM_RegWrite);
  and and_2 (and_2_out, comparator_4_eq, EX_RegWrite);
  and and_3 (and_3_out, comparator_5_eq, MEM_RegWrite);
  and and_4 (and_4_out, comparator_6_eq, EX_RegWrite);
  and and_5 (and_5_out, \源寄存器使用情况_1_p13 , and_1_out);
  and and_6 (and_6_out, \源寄存器使用情况_1_p13 , and_2_out);
  and and_7 (and_7_out, \源寄存器使用情况_1_p14 , and_3_out);
  and and_8 (and_8_out, \源寄存器使用情况_1_p14 , and_4_out);
  and and_9 (and_9_out, ~comparator_1_eq, and_5_out);  // AND_Gate
  and and_10 (and_10_out, ~comparator_2_eq, and_7_out);  // AND_Gate
  or or_1 (\Mem相关 , and_9_out, and_10_out);
  and and_11 (R1EX, ~comparator_1_eq, and_6_out);  // AND_Gate
  or or_2 (\EX相关 , R1EX, R2EX);
  and and_12 (R2EX, ~comparator_2_eq, and_8_out);  // AND_Gate
  or or_3 (or_3_out, and_5_out, and_6_out);
  or or_4 (or_4_out, and_7_out, and_8_out);
  and and_13 (\R1冲突 , ~comparator_1_eq, or_3_out);  // AND_Gate
  and and_14 (\R2冲突 , ~comparator_2_eq, or_4_out);  // AND_Gate
  or or_5 (\数据相关 , \R1冲突 , \R2冲突 );

  // Other names for the same wires on the sheet: OP_CODE[5:0] = OP
endmodule

// IF/ID
module IF_ID (
  input  [31:0] PC,
  input  [31:0] ID,
  input  CLK,
  input  \同步清零_气泡_高电平有效 ,
  input  \使能端_低电平有效_stall_高电平有效 ,
  output [31:0] PC_2,
  output [31:0] ID_2
);

  wire not_1_out;
  wire [31:0] multiplexer_1_out, multiplexer_2_out;

  Multiplexer #(.width(32), .enable("false")) multiplexer_1 (
    .in0(PC), .in1({32{1'b0}}), .out(multiplexer_1_out), .sel(\同步清零_气泡_高电平有效 ));
  Multiplexer #(.width(32), .enable("false")) multiplexer_2 (
    .in0(ID), .in1({32{1'b0}}), .out(multiplexer_2_out), .sel(\同步清零_气泡_高电平有效 ));
  not not_1 (not_1_out, \使能端_低电平有效_stall_高电平有效 );
  Register #(.width(32)) register_1 (.D(multiplexer_1_out), .en(not_1_out), .Q(PC_2), .clk(CLK));  // open: clr
  Register #(.width(32)) register_2 (.D(multiplexer_2_out), .en(not_1_out), .Q(ID_2), .clk(CLK));  // open: clr
endmodule

// ID/EX
module ID_EX (
  input  JMP,
  input  BEQ,
  input  JR,
  input  BNE,
  input  MTR,
  input  MW,
  input  [3:0] ALUOP,
  input  ALU_SRC,
  input  REGW,
  input  JAL,
  input  REGD,
  input  SYS,
  input  [31:0] PC,
  input  [31:0] ID,
  input  [31:0] A,
  input  [31:0] B,
  input  [31:0] IMM,
  input  [4:0] SHM,
  input  [1:0] forward,
  input  [1:0] forward1,
  input  blez,
  input  sh,
  input  lui,
  input  \xor ,
  input  CLK,
  input  \同步清零_气泡_高电平有效 ,
  input  \使能端_低电平有效_stall_高电平有效 ,
  output JMP_2,
  output BEQ_2,
  output JR_2,
  output BNE_2,
  output MTR_2,
  output MW_2,
  output [3:0] ALUOP_2,
  output ALU_SRC_2,
  output REGW_2,
  output JAL_2,
  output REGD_2,
  output SYS_2,
  output [31:0] PC_2,
  output [31:0] ID_2,
  output [31:0] A_2,
  output [31:0] B_2,
  output [31:0] IMM_2,
  output [4:0] SHM_2,
  output [1:0] forwardout,
  output [1:0] forward1out,
  output blezout,
  output shout,
  output luiout,
  output xorout
);

  wire multiplexer_1_out, multiplexer_2_out, multiplexer_3_out, multiplexer_4_out, multiplexer_5_out,
       multiplexer_6_out, multiplexer_8_out, multiplexer_9_out, multiplexer_10_out, multiplexer_11_out,
       multiplexer_12_out, multiplexer_21_out, multiplexer_22_out, multiplexer_23_out, multiplexer_24_out,
       not_1_out;
  wire [1:0] multiplexer_19_out, multiplexer_20_out;
  wire [3:0] multiplexer_7_out;
  wire [4:0] multiplexer_18_out;
  wire [31:0] multiplexer_13_out, multiplexer_14_out, multiplexer_15_out, multiplexer_16_out,
       multiplexer_17_out;

  Multiplexer #(.enable("false")) multiplexer_1 (.in0(JMP), .in1(1'b0), .out(multiplexer_1_out), .sel(\同步清零_气泡_高电平有效 ));
  Multiplexer #(.enable("false")) multiplexer_2 (.in0(BEQ), .in1(1'b0), .out(multiplexer_2_out), .sel(\同步清零_气泡_高电平有效 ));
  Multiplexer #(.enable("false")) multiplexer_3 (.in0(JR), .in1(1'b0), .out(multiplexer_3_out), .sel(\同步清零_气泡_高电平有效 ));
  Multiplexer #(.enable("false")) multiplexer_4 (.in0(BNE), .in1(1'b0), .out(multiplexer_4_out), .sel(\同步清零_气泡_高电平有效 ));
  Multiplexer #(.enable("false")) multiplexer_5 (.in0(MTR), .in1(1'b0), .out(multiplexer_5_out), .sel(\同步清零_气泡_高电平有效 ));
  Multiplexer #(.enable("false")) multiplexer_6 (.in0(MW), .in1(1'b0), .out(multiplexer_6_out), .sel(\同步清零_气泡_高电平有效 ));
  Multiplexer #(.width(4), .enable("false")) multiplexer_7 (
    .in0(ALUOP), .in1(4'b0000), .out(multiplexer_7_out), .sel(\同步清零_气泡_高电平有效 ));
  Multiplexer #(.enable("false")) multiplexer_8 (
    .in0(ALU_SRC), .in1(1'b0), .out(multiplexer_8_out), .sel(\同步清零_气泡_高电平有效 ));
  Multiplexer #(.enable("false")) multiplexer_9 (
    .in0(REGW), .in1(1'b0), .out(multiplexer_9_out), .sel(\同步清零_气泡_高电平有效 ));
  Multiplexer #(.enable("false")) multiplexer_10 (
    .in0(JAL), .in1(1'b0), .out(multiplexer_10_out), .sel(\同步清零_气泡_高电平有效 ));
  Multiplexer #(.enable("false")) multiplexer_11 (
    .in0(REGD), .in1(1'b0), .out(multiplexer_11_out), .sel(\同步清零_气泡_高电平有效 ));
  Multiplexer #(.enable("false")) multiplexer_12 (
    .in0(SYS), .in1(1'b0), .out(multiplexer_12_out), .sel(\同步清零_气泡_高电平有效 ));
  Multiplexer #(.width(32), .enable("false")) multiplexer_13 (
    .in0(PC), .in1({32{1'b0}}), .out(multiplexer_13_out), .sel(\同步清零_气泡_高电平有效 ));
  Multiplexer #(.width(32), .enable("false")) multiplexer_14 (
    .in0(ID), .in1({32{1'b0}}), .out(multiplexer_14_out), .sel(\同步清零_气泡_高电平有效 ));
  Multiplexer #(.width(32), .enable("false")) multiplexer_15 (
    .in0(A), .in1({32{1'b0}}), .out(multiplexer_15_out), .sel(\同步清零_气泡_高电平有效 ));
  Multiplexer #(.width(32), .enable("false")) multiplexer_16 (
    .in0(B), .in1({32{1'b0}}), .out(multiplexer_16_out), .sel(\同步清零_气泡_高电平有效 ));
  Multiplexer #(.width(32), .enable("false")) multiplexer_17 (
    .in0(IMM), .in1({32{1'b0}}), .out(multiplexer_17_out), .sel(\同步清零_气泡_高电平有效 ));
  Multiplexer #(.width(5), .enable("false")) multiplexer_18 (
    .in0(SHM), .in1({5{1'b0}}), .out(multiplexer_18_out), .sel(\同步清零_气泡_高电平有效 ));
  Multiplexer #(.width(2), .enable("false")) multiplexer_19 (
    .in0(forward), .in1(2'b00), .out(multiplexer_19_out), .sel(\同步清零_气泡_高电平有效 ));
  Multiplexer #(.width(2), .enable("false")) multiplexer_20 (
    .in0(forward1), .in1(2'b00), .out(multiplexer_20_out), .sel(\同步清零_气泡_高电平有效 ));
  Multiplexer #(.enable("false")) multiplexer_21 (
    .in0(blez), .in1(1'b0), .out(multiplexer_21_out), .sel(\同步清零_气泡_高电平有效 ));
  Multiplexer #(.enable("false")) multiplexer_22 (
    .in0(sh), .in1(1'b0), .out(multiplexer_22_out), .sel(\同步清零_气泡_高电平有效 ));
  Multiplexer #(.enable("false")) multiplexer_23 (
    .in0(lui), .in1(1'b0), .out(multiplexer_23_out), .sel(\同步清零_气泡_高电平有效 ));
  Multiplexer #(.enable("false")) multiplexer_24 (
    .in0(\xor ), .in1(1'b0), .out(multiplexer_24_out), .sel(\同步清零_气泡_高电平有效 ));
  not not_1 (not_1_out, \使能端_低电平有效_stall_高电平有效 );
  Register #(.width(1)) register_1 (.D(multiplexer_1_out), .en(not_1_out), .Q(JMP_2), .clk(CLK));  // open: clr
  Register #(.width(1)) register_2 (.D(multiplexer_2_out), .en(not_1_out), .Q(BEQ_2), .clk(CLK));  // open: clr
  Register #(.width(1)) register_3 (.D(multiplexer_3_out), .en(not_1_out), .Q(JR_2), .clk(CLK));  // open: clr
  Register #(.width(1)) register_4 (.D(multiplexer_4_out), .en(not_1_out), .Q(BNE_2), .clk(CLK));  // open: clr
  Register #(.width(1)) register_5 (.D(multiplexer_5_out), .en(not_1_out), .Q(MTR_2), .clk(CLK));  // open: clr
  Register #(.width(1)) register_6 (.D(multiplexer_6_out), .en(not_1_out), .Q(MW_2), .clk(CLK));  // open: clr
  Register #(.width(4)) register_7 (.D(multiplexer_7_out), .en(not_1_out), .Q(ALUOP_2), .clk(CLK));  // open: clr
  Register #(.width(1)) register_8 (.D(multiplexer_8_out), .en(not_1_out), .Q(ALU_SRC_2), .clk(CLK));  // open: clr
  Register #(.width(1)) register_9 (.D(multiplexer_9_out), .en(not_1_out), .Q(REGW_2), .clk(CLK));  // open: clr
  Register #(.width(1)) register_10 (.D(multiplexer_10_out), .en(not_1_out), .Q(JAL_2), .clk(CLK));  // open: clr
  Register #(.width(1)) register_11 (.D(multiplexer_11_out), .en(not_1_out), .Q(REGD_2), .clk(CLK));  // open: clr
  Register #(.width(1)) register_12 (.D(multiplexer_12_out), .en(not_1_out), .Q(SYS_2), .clk(CLK));  // open: clr
  Register #(.width(32)) register_13 (.D(multiplexer_13_out), .en(not_1_out), .Q(PC_2), .clk(CLK));  // open: clr
  Register #(.width(32)) register_14 (.D(multiplexer_14_out), .en(not_1_out), .Q(ID_2), .clk(CLK));  // open: clr
  Register #(.width(32)) register_15 (.D(multiplexer_15_out), .en(not_1_out), .Q(A_2), .clk(CLK));  // open: clr
  Register #(.width(32)) register_16 (.D(multiplexer_16_out), .en(not_1_out), .Q(B_2), .clk(CLK));  // open: clr
  Register #(.width(32)) register_17 (.D(multiplexer_17_out), .en(not_1_out), .Q(IMM_2), .clk(CLK));  // open: clr
  Register #(.width(5)) register_18 (.D(multiplexer_18_out), .en(not_1_out), .Q(SHM_2), .clk(CLK));  // open: clr
  Register #(.width(2)) register_19 (.D(multiplexer_19_out), .en(not_1_out), .Q(forwardout), .clk(CLK));  // open: clr
  Register #(.width(2)) register_20 (.D(multiplexer_20_out), .en(not_1_out), .Q(forward1out), .clk(CLK));  // open: clr
  Register #(.width(1)) register_21 (.D(multiplexer_21_out), .en(not_1_out), .Q(blezout), .clk(CLK));  // open: clr
  Register #(.width(1)) register_22 (.D(multiplexer_22_out), .en(not_1_out), .Q(shout), .clk(CLK));  // open: clr
  Register #(.width(1)) register_23 (.D(multiplexer_23_out), .en(not_1_out), .Q(luiout), .clk(CLK));  // open: clr
  Register #(.width(1)) register_24 (.D(multiplexer_24_out), .en(not_1_out), .Q(xorout), .clk(CLK));  // open: clr
endmodule
// EX/MEM
module EX_MEM (
  input  MTR,
  input  MW,
  input  REGW,
  input  JAL,
  input  REGD,
  input  SYS,
  input  [31:0] PC,
  input  [31:0] ID,
  input  [31:0] A,
  input  [31:0] B,
  input  [31:0] ALU,
  input  blez,
  input  sh,
  input  lui,
  input  \xor ,
  input  CLK,
  input  \同步清零_气泡_高电平有效 ,
  input  \使能端_低电平有效_stall_高电平有效 ,
  output MTR_2,
  output MW_2,
  output REGW_2,
  output JAL_2,
  output REGD_2,
  output SYS_2,
  output [31:0] PC_2,
  output [31:0] ID_2,
  output [31:0] A_2,
  output [31:0] B_2,
  output [31:0] ALU_2,
  output blezout,
  output shout,
  output luiout,
  output xorout
);

  wire multiplexer_1_out, multiplexer_2_out, multiplexer_3_out, multiplexer_4_out, multiplexer_5_out,
       multiplexer_6_out, multiplexer_12_out, multiplexer_13_out, multiplexer_14_out, multiplexer_15_out,
       not_1_out;
  wire [31:0] multiplexer_7_out, multiplexer_8_out, multiplexer_9_out, multiplexer_10_out, multiplexer_11_out;

  Multiplexer #(.enable("false")) multiplexer_1 (.in0(MTR), .in1(1'b0), .out(multiplexer_1_out), .sel(\同步清零_气泡_高电平有效 ));
  Multiplexer #(.enable("false")) multiplexer_2 (.in0(MW), .in1(1'b0), .out(multiplexer_2_out), .sel(\同步清零_气泡_高电平有效 ));
  Multiplexer #(.enable("false")) multiplexer_3 (
    .in0(REGW), .in1(1'b0), .out(multiplexer_3_out), .sel(\同步清零_气泡_高电平有效 ));
  Multiplexer #(.enable("false")) multiplexer_4 (.in0(JAL), .in1(1'b0), .out(multiplexer_4_out), .sel(\同步清零_气泡_高电平有效 ));
  Multiplexer #(.enable("false")) multiplexer_5 (
    .in0(REGD), .in1(1'b0), .out(multiplexer_5_out), .sel(\同步清零_气泡_高电平有效 ));
  Multiplexer #(.enable("false")) multiplexer_6 (.in0(SYS), .in1(1'b0), .out(multiplexer_6_out), .sel(\同步清零_气泡_高电平有效 ));
  Multiplexer #(.width(32), .enable("false")) multiplexer_7 (
    .in0(PC), .in1({32{1'b0}}), .out(multiplexer_7_out), .sel(\同步清零_气泡_高电平有效 ));
  Multiplexer #(.width(32), .enable("false")) multiplexer_8 (
    .in0(ID), .in1({32{1'b0}}), .out(multiplexer_8_out), .sel(\同步清零_气泡_高电平有效 ));
  Multiplexer #(.width(32), .enable("false")) multiplexer_9 (
    .in0(A), .in1({32{1'b0}}), .out(multiplexer_9_out), .sel(\同步清零_气泡_高电平有效 ));
  Multiplexer #(.width(32), .enable("false")) multiplexer_10 (
    .in0(B), .in1({32{1'b0}}), .out(multiplexer_10_out), .sel(\同步清零_气泡_高电平有效 ));
  Multiplexer #(.width(32), .enable("false")) multiplexer_11 (
    .in0(ALU), .in1({32{1'b0}}), .out(multiplexer_11_out), .sel(\同步清零_气泡_高电平有效 ));
  Multiplexer #(.enable("false")) multiplexer_12 (
    .in0(blez), .in1(1'b0), .out(multiplexer_12_out), .sel(\同步清零_气泡_高电平有效 ));
  Multiplexer #(.enable("false")) multiplexer_13 (
    .in0(sh), .in1(1'b0), .out(multiplexer_13_out), .sel(\同步清零_气泡_高电平有效 ));
  Multiplexer #(.enable("false")) multiplexer_14 (
    .in0(lui), .in1(1'b0), .out(multiplexer_14_out), .sel(\同步清零_气泡_高电平有效 ));
  Multiplexer #(.enable("false")) multiplexer_15 (
    .in0(\xor ), .in1(1'b0), .out(multiplexer_15_out), .sel(\同步清零_气泡_高电平有效 ));
  Register #(.width(1)) register_1 (.D(multiplexer_1_out), .en(not_1_out), .Q(MTR_2), .clk(CLK));  // open: clr
  Register #(.width(1)) register_2 (.D(multiplexer_2_out), .en(not_1_out), .Q(MW_2), .clk(CLK));  // open: clr
  Register #(.width(1)) register_3 (.D(multiplexer_3_out), .en(not_1_out), .Q(REGW_2), .clk(CLK));  // open: clr
  Register #(.width(1)) register_4 (.D(multiplexer_4_out), .en(not_1_out), .Q(JAL_2), .clk(CLK));  // open: clr
  Register #(.width(1)) register_5 (.D(multiplexer_5_out), .en(not_1_out), .Q(REGD_2), .clk(CLK));  // open: clr
  Register #(.width(1)) register_6 (.D(multiplexer_6_out), .en(not_1_out), .Q(SYS_2), .clk(CLK));  // open: clr
  Register #(.width(32)) register_7 (.D(multiplexer_7_out), .en(not_1_out), .Q(PC_2), .clk(CLK));  // open: clr
  Register #(.width(32)) register_8 (.D(multiplexer_8_out), .en(not_1_out), .Q(ID_2), .clk(CLK));  // open: clr
  Register #(.width(32)) register_9 (.D(multiplexer_9_out), .en(not_1_out), .Q(A_2), .clk(CLK));  // open: clr
  Register #(.width(32)) register_10 (.D(multiplexer_10_out), .en(not_1_out), .Q(B_2), .clk(CLK));  // open: clr
  Register #(.width(32)) register_11 (.D(multiplexer_11_out), .en(not_1_out), .Q(ALU_2), .clk(CLK));  // open: clr
  Register #(.width(1)) register_12 (.D(multiplexer_12_out), .en(not_1_out), .Q(blezout), .clk(CLK));  // open: clr
  Register #(.width(1)) register_13 (.D(multiplexer_13_out), .en(not_1_out), .Q(shout), .clk(CLK));  // open: clr
  Register #(.width(1)) register_14 (.D(multiplexer_14_out), .en(not_1_out), .Q(luiout), .clk(CLK));  // open: clr
  Register #(.width(1)) register_15 (.D(multiplexer_15_out), .en(not_1_out), .Q(xorout), .clk(CLK));  // open: clr
  not not_1 (not_1_out, \使能端_低电平有效_stall_高电平有效 );
endmodule

// MEM/WB
module MEM_WB (
  input  MTR,
  input  REGW,
  input  JAL,
  input  REGD,
  input  SYS,
  input  [31:0] PC,
  input  [31:0] ID,
  input  [31:0] A,
  input  [31:0] MD,
  input  [31:0] B,
  input  [31:0] ALU,
  input  blez,
  input  sh,
  input  lui,
  input  \xor ,
  input  CLK,
  input  \同步清零_气泡_高电平有效 ,
  input  \使能端_低电平有效_stall_高电平有效 ,
  output MTR_2,
  output REGW_2,
  output JAL_2,
  output REGD_2,
  output SYS_2,
  output [31:0] PC_2,
  output [31:0] ID_2,
  output [31:0] A_2,
  output [31:0] MD_2,
  output [31:0] B_2,
  output [31:0] ALU_2,
  output blezout,
  output shout,
  output luiout,
  output xorout
);

  wire multiplexer_1_out, multiplexer_2_out, multiplexer_3_out, multiplexer_4_out, multiplexer_5_out,
       multiplexer_12_out, multiplexer_13_out, multiplexer_14_out, multiplexer_15_out, not_1_out;
  wire [31:0] multiplexer_6_out, multiplexer_7_out, multiplexer_8_out, multiplexer_9_out, multiplexer_10_out,
       multiplexer_11_out;

  Multiplexer #(.enable("false")) multiplexer_1 (.in0(MTR), .in1(1'b0), .out(multiplexer_1_out), .sel(\同步清零_气泡_高电平有效 ));
  Multiplexer #(.enable("false")) multiplexer_2 (
    .in0(REGW), .in1(1'b0), .out(multiplexer_2_out), .sel(\同步清零_气泡_高电平有效 ));
  Multiplexer #(.enable("false")) multiplexer_3 (.in0(JAL), .in1(1'b0), .out(multiplexer_3_out), .sel(\同步清零_气泡_高电平有效 ));
  Multiplexer #(.enable("false")) multiplexer_4 (
    .in0(REGD), .in1(1'b0), .out(multiplexer_4_out), .sel(\同步清零_气泡_高电平有效 ));
  Multiplexer #(.enable("false")) multiplexer_5 (.in0(SYS), .in1(1'b0), .out(multiplexer_5_out), .sel(\同步清零_气泡_高电平有效 ));
  Multiplexer #(.width(32), .enable("false")) multiplexer_6 (
    .in0(PC), .in1({32{1'b0}}), .out(multiplexer_6_out), .sel(\同步清零_气泡_高电平有效 ));
  Multiplexer #(.width(32), .enable("false")) multiplexer_7 (
    .in0(ID), .in1({32{1'b0}}), .out(multiplexer_7_out), .sel(\同步清零_气泡_高电平有效 ));
  Multiplexer #(.width(32), .enable("false")) multiplexer_8 (
    .in0(A), .in1({32{1'b0}}), .out(multiplexer_8_out), .sel(\同步清零_气泡_高电平有效 ));
  Multiplexer #(.width(32), .enable("false")) multiplexer_9 (
    .in0(MD), .in1({32{1'b0}}), .out(multiplexer_9_out), .sel(\同步清零_气泡_高电平有效 ));
  Multiplexer #(.width(32), .enable("false")) multiplexer_10 (
    .in0(B), .in1({32{1'b0}}), .out(multiplexer_10_out), .sel(\同步清零_气泡_高电平有效 ));
  Multiplexer #(.width(32), .enable("false")) multiplexer_11 (
    .in0(ALU), .in1({32{1'b0}}), .out(multiplexer_11_out), .sel(\同步清零_气泡_高电平有效 ));
  Multiplexer #(.enable("false")) multiplexer_12 (
    .in0(blez), .in1(1'b0), .out(multiplexer_12_out), .sel(\同步清零_气泡_高电平有效 ));
  Multiplexer #(.enable("false")) multiplexer_13 (
    .in0(sh), .in1(1'b0), .out(multiplexer_13_out), .sel(\同步清零_气泡_高电平有效 ));
  Multiplexer #(.enable("false")) multiplexer_14 (
    .in0(lui), .in1(1'b0), .out(multiplexer_14_out), .sel(\同步清零_气泡_高电平有效 ));
  Multiplexer #(.enable("false")) multiplexer_15 (
    .in0(\xor ), .in1(1'b0), .out(multiplexer_15_out), .sel(\同步清零_气泡_高电平有效 ));
  not not_1 (not_1_out, \使能端_低电平有效_stall_高电平有效 );
  Register #(.width(1)) register_1 (.D(multiplexer_1_out), .en(not_1_out), .Q(MTR_2), .clk(CLK));  // open: clr
  Register #(.width(1)) register_2 (.D(multiplexer_2_out), .en(not_1_out), .Q(REGW_2), .clk(CLK));  // open: clr
  Register #(.width(1)) register_3 (.D(multiplexer_3_out), .en(not_1_out), .Q(JAL_2), .clk(CLK));  // open: clr
  Register #(.width(1)) register_4 (.D(multiplexer_4_out), .en(not_1_out), .Q(REGD_2), .clk(CLK));  // open: clr
  Register #(.width(1)) register_5 (.D(multiplexer_5_out), .en(not_1_out), .Q(SYS_2), .clk(CLK));  // open: clr
  Register #(.width(32)) register_6 (.D(multiplexer_6_out), .en(not_1_out), .Q(PC_2), .clk(CLK));  // open: clr
  Register #(.width(32)) register_7 (.D(multiplexer_7_out), .en(not_1_out), .Q(ID_2), .clk(CLK));  // open: clr
  Register #(.width(32)) register_8 (.D(multiplexer_8_out), .en(not_1_out), .Q(A_2), .clk(CLK));  // open: clr
  Register #(.width(32)) register_9 (.D(multiplexer_9_out), .en(not_1_out), .Q(MD_2), .clk(CLK));  // open: clr
  Register #(.width(32)) register_10 (.D(multiplexer_10_out), .en(not_1_out), .Q(B_2), .clk(CLK));  // open: clr
  Register #(.width(32)) register_11 (.D(multiplexer_11_out), .en(not_1_out), .Q(ALU_2), .clk(CLK));  // open: clr
  Register #(.width(1)) register_12 (.D(multiplexer_12_out), .en(not_1_out), .Q(blezout), .clk(CLK));  // open: clr
  Register #(.width(1)) register_13 (.D(multiplexer_13_out), .en(not_1_out), .Q(shout), .clk(CLK));  // open: clr
  Register #(.width(1)) register_14 (.D(multiplexer_14_out), .en(not_1_out), .Q(luiout), .clk(CLK));  // open: clr
  Register #(.width(1)) register_15 (.D(multiplexer_15_out), .en(not_1_out), .Q(xorout), .clk(CLK));  // open: clr
endmodule

module \分支相关流水线  (
);

  wire and_1_out, and_2_out, and_3_out, and_4_out, CLK, comparator_1_eq, d_ff_1_qn, ex_mem_1_jal_2,
       ex_mem_1_mtr_2, ex_mem_1_mw_2, ex_mem_1_regd_2, ex_mem_1_regw_2, ex_mem_1_sys_2, Go, IR1, IR2, IR3,
       JAL1, JMP, JMP1, JR, JR1, jump, mem_wb_1_jal_2, mem_wb_1_mtr_2, mem_wb_1_regd_2, mips_alu_1_equal,
       not_1_out, not_2_out, or_1_out, PCEnable, REGW, RST, SignedExt, SYS, undriven, undriven_2, undriven_3,
       undriven_5, undriven_6, undriven_7, undriven_8, undriven_10, W1, W2, W3, \分支 , \无条件分支 , \条件分支 ,
       \硬布线控制器_1_p6 , \硬布线控制器_1_p7 , \硬布线控制器_1_p8 , \硬布线控制器_1_p9 , \硬布线控制器_1_p10 , \硬布线控制器_1_p11 ,
       \硬布线控制器_1_p12 , \硬布线控制器_1_p13 , \硬布线控制器_1_p14 , \硬布线控制器_1_p15 ;
  wire [3:0] undriven_4;
  wire [4:0] multiplexer_3_out, multiplexer_4_out, multiplexer_10_out, undriven_11, W_num;
  wire [15:0] \LoadUse次数 , \总周期数 , \插入气泡数 , \无条件分支数 , \条件分支成功数 ;
  wire [31:0] A, A1, adder_2_out, B, bit_extender_1_out, bit_extender_2_out, ex_mem_1_a_2, ex_mem_1_alu_2,
       ex_mem_1_b_2, ex_mem_1_id_2, EX_PC, ID, id_ex_1_p26, id_ex_1_p27, ID_PC, if_id_1_id_2, IF_PC, IMM,
       LedData, MEM_PC, mem_wb_1_alu_2, mem_wb_1_id_2, mem_wb_1_md_2, mips_alu_1_result, multiplexer_1_out,
       multiplexer_2_out, multiplexer_5_out, multiplexer_6_out, multiplexer_7_out, multiplexer_9_out, PC,
       PCnext, ram_1_data, RDIN, rom_1_data, shifter_1_out, undriven_9, WB_PC;

  Button \u_总复位  (.out(RST));
  Button _1 (.out(IR1));
  Button _2 (.out(IR2));
  Button _3 (.out(IR3));
  Button \u_继续运行  (.out(Go));
  LED led_1 (.in(W1));
  LED led_2 (.in(W2));
  LED led_3 (.in(W3));
  not not_1 (not_1_out, PCEnable);
  Register #(.width(32)) u_PC (.D(PC), .en(PCEnable), .Q(IF_PC), .clk(CLK), .clr(RST));
  Hex_Digit_Display hex_digit_display_1 (.value(LedData[31:28]));  // open: dp
  Adder #(.width(32)) adder_1 (.a(IF_PC), .b(32'h4), .out(PCnext));  // open: cin, cout
  Hex_Digit_Display hex_digit_display_2 (.value(LedData[27:24]));  // open: dp
  Hex_Digit_Display hex_digit_display_3 (.value(LedData[23:20]));  // open: dp
  or or_1 (or_1_out, RST, \分支 );
  Comparator #(.width(32)) comparator_1 (.a(A), .b(32'h22), .eq(comparator_1_eq));  // open: gt, lt
  not not_2 (not_2_out, comparator_1_eq);
  and and_1 (and_1_out, comparator_1_eq, SYS);
  Multiplexer #(.width(32), .enable("false")) multiplexer_1 (
    .in0(LedData), .in1(B), .out(multiplexer_1_out), .sel(and_1_out));
  Hex_Digit_Display hex_digit_display_4 (.value(LedData[19:16]));  // open: dp
  Hex_Digit_Display hex_digit_display_5 (.value(LedData[15:12]));  // open: dp
  ROM #(.addrWidth(10), .dataWidth(32)) rom_1 (.addr(IF_PC[11:2]), .data(rom_1_data));  // open: sel
  Register #(.width(32)) register_1 (.D(multiplexer_1_out), .Q(LedData), .clk(CLK));  // open: en, clr
  Hex_Digit_Display hex_digit_display_6 (.value(LedData[11:8]));  // open: dp
  Hex_Digit_Display hex_digit_display_7 (.value(LedData[7:4]));  // open: dp
  Clock clock_1 (.out(CLK));
  Shifter #(.width(32)) shifter_1 (.in(IMM), .\dist (5'b00010), .out(shifter_1_out));
  D_Flip_Flop d_ff_1 (.clk(CLK), .D(Go), .Qn(d_ff_1_qn));  // open: Q, preset, en, reset
  Hex_Digit_Display hex_digit_display_8 (.value(LedData[3:0]));  // open: dp
  IF_ID if_id_1 (
    .PC(PCnext), .ID(rom_1_data), .CLK(CLK), .PC_2(ID_PC), .ID_2(if_id_1_id_2), .\同步清零_气泡_高电平有效 (or_1_out),
    .\使能端_低电平有效_stall_高电平有效 (not_1_out));
  not not_3 (PCEnable, and_2_out);
  and and_2 (and_2_out, d_ff_1_qn, SYS, not_2_out);
  // 硬布线控制器 硬布线控制器_1: pin names not known; wires that end beside it: JMP, JR, SignedExt, if_id_1_id_2[31:26], if_id_1_id_2[5:0], \硬布线控制器_1_p6 , \硬布线控制器_1_p7 , \硬布线控制器_1_p8 , \硬布线控制器_1_p9 , \硬布线控制器_1_p10 , \硬布线控制器_1_p11 , \硬布线控制器_1_p12 , \硬布线控制器_1_p13 , \硬布线控制器_1_p14 , \硬布线控制器_1_p15 
  Adder #(.width(32)) adder_2 (.a(EX_PC), .b(shifter_1_out), .out(adder_2_out));  // open: cin, cout
  // Probe on \总周期数 
  // Probe on \无条件分支数 
  // Probe on \条件分支成功数 
  // Probe on \插入气泡数 
  // Probe on \LoadUse次数 
  assign bit_extender_1_out = {{16{1'b0}}, if_id_1_id_2[15:0]};  // Bit_Extender bit_extender_1
  assign bit_extender_2_out = {{16{if_id_1_id_2[15]}}, if_id_1_id_2[15:0]};  // Bit_Extender bit_extender_2
  Multiplexer #(.width(32), .enable("false")) multiplexer_2 (
    .in0(PCnext), .in1(adder_2_out), .out(multiplexer_2_out), .sel(\条件分支 ));
  // Probe on IF_PC[11:0]
  Multiplexer #(.width(5), .enable("false")) multiplexer_3 (
    .in0(if_id_1_id_2[25:21]), .in1(5'b00010), .out(multiplexer_3_out), .sel(\硬布线控制器_1_p6 ));
  Multiplexer #(.width(5), .enable("false")) multiplexer_4 (
    .in0(if_id_1_id_2[20:16]), .in1(5'b00100), .out(multiplexer_4_out), .sel(\硬布线控制器_1_p6 ));
  Multiplexer #(.width(32), .enable("false")) multiplexer_5 (
    .in0(bit_extender_1_out), .in1(bit_extender_2_out), .out(multiplexer_5_out), .sel(SignedExt));
  // Probe on ID_PC[11:0]
  // Probe on EX_PC[11:0]
  // Probe on MEM_PC[11:0]
  // ID_EX id_ex_1: pin names not known; wires that end beside it: \硬布线控制器_1_p7 , \硬布线控制器_1_p8 , \硬布线控制器_1_p9 , \硬布线控制器_1_p10 , \硬布线控制器_1_p11 , \硬布线控制器_1_p12 , \硬布线控制器_1_p13 , \硬布线控制器_1_p14 , \硬布线控制器_1_p15 , if_id_1_id_2[10:6], not_1_out, JMP, \硬布线控制器_1_p7 , JR, \硬布线控制器_1_p8 , \硬布线控制器_1_p9 , \硬布线控制器_1_p10 , \硬布线控制器_1_p11 , \硬布线控制器_1_p12 , \硬布线控制器_1_p13 , \硬布线控制器_1_p14 , \硬布线控制器_1_p15 , \硬布线控制器_1_p6 , ID_PC, if_id_1_id_2, id_ex_1_p26, id_ex_1_p27, multiplexer_5_out, if_id_1_id_2[10:6], CLK, or_1_out
  MIPS_Regifile mips_regifile_1 (
    .Din(RDIN), .Clk(CLK), .R1(id_ex_1_p26), .R2(id_ex_1_p27), .WE(REGW), .W_num(W_num),
    .R1_num(multiplexer_3_out), .R2_num(multiplexer_4_out));
  // Probe on WB_PC[11:0]
  Multiplexer #(.width(32), .enable("false")) multiplexer_6 (
    .in0(multiplexer_2_out), .in1({EX_PC[31:28], ID[25:0], 2'b00}), .out(multiplexer_6_out), .sel(jump));
  Counter #(.width(16), .max('hffff)) counter_1 (
    .count(PCEnable), .Q(\总周期数 ), .clk(CLK), .clr(RST));  // open: load, D, carry
  Multiplexer #(.width(32), .enable("false")) multiplexer_7 (
    .in0(undriven_9), .in1(IMM), .out(multiplexer_7_out), .sel(undriven_5));
  Multiplexer #(.width(32), .enable("false")) multiplexer_8 (.in0(multiplexer_6_out), .in1(A1), .out(PC), .sel(JR1));
  Counter #(.width(16), .max('hffff)) counter_2 (
    .count(\无条件分支 ), .Q(\无条件分支数 ), .clk(CLK), .clr(RST));  // open: load, D, carry
  Counter #(.width(16), .max('hffff)) counter_3 (
    .count(\条件分支 ), .Q(\条件分支成功数 ), .clk(CLK), .clr(RST));  // open: load, D, carry
  or or_2 (jump, JMP1, JAL1);
  and and_3 (and_3_out, undriven_10, mips_alu_1_equal);
  and and_4 (and_4_out, undriven, ~mips_alu_1_equal);  // AND_Gate
  MIPS_ALU mips_alu_1 (
    .X(A1), .Y(multiplexer_7_out), .AluOP(undriven_4), .Equal(mips_alu_1_equal), .Result(mips_alu_1_result),
    .shamt(undriven_11));  // open: Result_2
  or or_3 (\无条件分支 , jump, JR1);
  or or_4 (\条件分支 , and_3_out, and_4_out);
  EX_MEM ex_mem_1 (
    .MTR(undriven_2), .MW(undriven_3), .REGW(undriven_6), .JAL(JAL1), .REGD(undriven_7), .SYS(undriven_8),
    .PC(EX_PC), .ID(ID), .A(A1), .B(undriven_9), .ALU(mips_alu_1_result), .CLK(CLK), .MTR_2(ex_mem_1_mtr_2),
    .MW_2(ex_mem_1_mw_2), .REGW_2(ex_mem_1_regw_2), .JAL_2(ex_mem_1_jal_2), .REGD_2(ex_mem_1_regd_2),
    .SYS_2(ex_mem_1_sys_2), .PC_2(MEM_PC), .ID_2(ex_mem_1_id_2), .A_2(ex_mem_1_a_2), .B_2(ex_mem_1_b_2),
    .ALU_2(ex_mem_1_alu_2), .\同步清零_气泡_高电平有效 (RST), .\使能端_低电平有效_stall_高电平有效 (not_1_out));  // open: blez, blezout, sh, shout, lui, luiout, xor, xorout
  or or_5 (\分支 , \无条件分支 , \条件分支 );
  RAM #(.addrWidth(10), .dataWidth(32), .bus("separate")) ram_1 (
    .addr(ex_mem_1_alu_2[11:2]), .din(ex_mem_1_b_2), .data(ram_1_data), .str(ex_mem_1_mw_2), .clk(CLK),
    .clr(RST));  // open: sel, ld
  MEM_WB mem_wb_1 (
    .MTR(ex_mem_1_mtr_2), .REGW(ex_mem_1_regw_2), .JAL(ex_mem_1_jal_2), .REGD(ex_mem_1_regd_2),
    .SYS(ex_mem_1_sys_2), .PC(MEM_PC), .ID(ex_mem_1_id_2), .A(ex_mem_1_a_2), .MD(ram_1_data),
    .B(ex_mem_1_b_2), .ALU(ex_mem_1_alu_2), .CLK(CLK), .MTR_2(mem_wb_1_mtr_2), .REGW_2(REGW),
    .JAL_2(mem_wb_1_jal_2), .REGD_2(mem_wb_1_regd_2), .SYS_2(SYS), .PC_2(WB_PC), .ID_2(mem_wb_1_id_2),
    .A_2(A), .MD_2(mem_wb_1_md_2), .B_2(B), .ALU_2(mem_wb_1_alu_2), .\同步清零_气泡_高电平有效 (RST),
    .\使能端_低电平有效_stall_高电平有效 (not_1_out));  // open: blez, blezout, sh, shout, lui, luiout, xor, xorout
  Multiplexer #(.width(32), .enable("false")) multiplexer_9 (
    .in0(mem_wb_1_alu_2), .in1(mem_wb_1_md_2), .out(multiplexer_9_out), .sel(mem_wb_1_mtr_2));
  Multiplexer #(.width(5), .enable("false")) multiplexer_10 (
    .in0(mem_wb_1_id_2[20:16]), .in1(mem_wb_1_id_2[15:11]), .out(multiplexer_10_out), .sel(mem_wb_1_regd_2));
  Multiplexer #(.width(32), .enable("false")) multiplexer_11 (
    .in0(multiplexer_9_out), .in1(WB_PC), .out(RDIN), .sel(mem_wb_1_jal_2));
  Multiplexer #(.width(5), .enable("false")) multiplexer_12 (
    .in0(multiplexer_10_out), .in1({5{1'b1}}), .out(W_num), .sel(mem_wb_1_jal_2));

  // Other names for the same wires on the sheet: PCO[31:0] = EX_PC

  // Notes on the sheet:
  //   中断源
  //   中断等待指示
  //   指令存储器
  //   数码管输出
  //   contents of rom_1 (hex, n*v repeats v):
  //   20110020 20020022 8000c06 20110000 20110000 2002000a 10000003 20110000 20110000 2002000a 14110003
  //   20110000 20110000 2002000a c000c14 2002000a 0 0 0 c 2231ffff 0 0 0 112020 0 0 0 c 1620fff6 3e00008
  //   OP
  //   Func
  //   rs
  //   rt
  //   rd
  //   流水调试日志用
  //   rt
  //   rd
endmodule

module \气泡流水线  (
);

  wire and_1_out, and_2_out, and_3_out, and_4_out, and_5_out, and_6_out, and_7_out, and_8_out, Beq, Bne, CLK,
       Cmp, comparator_1_eq, d_ff_1_qn, Equal, ex_mem_1_mtr_2, ex_mem_1_mw_2, ex_mem_1_sys_2, EX_REGD, EX_RW,
       Go, ID_SYS, IR1, IR2, IR3, JAL1, JMP, JMP1, JR, jump, MEM_JAL, MEM_REGD, MEM_RW, mem_wb_1_jal_2,
       mem_wb_1_mtr_2, mem_wb_1_regd_2, nand_1_out, not_1_out, not_2_out, or_1_out, or_4_out, PCEnable, REGW,
       RST, SignedExt, SYS, undriven, undriven_2, undriven_4, undriven_5, W1, W2, W3, \分支 , \数据相关 ,
       \数据相关检测_1_p9 , \数据相关检测_1_p10 , \数据相关检测_1_p12 , \数据相关检测_1_p13 , \无条件分支 , \条件分支 , \硬布线控制器_1_p7 ,
       \硬布线控制器_1_p8 , \硬布线控制器_1_p9 , \硬布线控制器_1_p10 , \硬布线控制器_1_p11 , \硬布线控制器_1_p12 , \硬布线控制器_1_p13 ,
       \硬布线控制器_1_p14 , \硬布线控制器_1_p15 ;
  wire [1:0] En;
  wire [3:0] undriven_3;
  wire [4:0] multiplexer_1_out, multiplexer_2_out, multiplexer_3_out, multiplexer_4_out, multiplexer_5_out,
       multiplexer_6_out, multiplexer_9_out, multiplexer_10_out, multiplexer_15_out, undriven_7, W_num;
  wire [5:0] FUNC;
  wire [15:0] \LoadUse次数 , \总周期数 , \插入气泡数 , \无条件分支数 , \条件分支成功数 ;
  wire [31:0] A, A1, adder_2_out, Addr2, B, bit_extender_1_out, bit_extender_2_out, EX_ID, ex_mem_1_a_2,
       ex_mem_1_alu_2, ex_mem_1_b_2, EX_PC, ID_PC, IF_PC, IMM, LedData, MEM_ID, MEM_PC, mem_wb_1_alu_2,
       mem_wb_1_id_2, mem_wb_1_md_2, mips_alu_1_result, mips_regifile_1_r1, mips_regifile_1_r2,
       multiplexer_11_out, multiplexer_12_out, multiplexer_13_out, multiplexer_14_out, PC, PCnext,
       ram_1_data, RDIN, rom_1_data, shifter_1_out, undriven_6, WB_PC;
  wire [31:6] ID32;

  and and_1 (and_1_out, PCEnable, ~\数据相关 );  // AND_Gate
  Button \u_总复位  (.out(RST));
  Button _1 (.out(IR1));
  Button _2 (.out(IR2));
  Button _3 (.out(IR3));
  Register #(.width(32)) u_PC (.D(PC), .en(and_1_out), .Q(IF_PC), .clk(CLK), .clr(RST));
  Button \u_继续运行  (.out(Go));
  LED led_1 (.in(W1));
  Hex_Digit_Display hex_digit_display_1 (.value(LedData[31:28]));  // open: dp
  LED led_2 (.in(W2));
  LED led_3 (.in(W3));
  Multiplexer #(.width(5), .enable("false")) multiplexer_1 (
    .in0(MEM_ID[20:16]), .in1(MEM_ID[15:11]), .out(multiplexer_1_out), .sel(MEM_REGD));
  Shifter #(.width(32)) shifter_1 (.in(IMM), .\dist (5'b00010), .out(shifter_1_out));
  and and_2 (and_2_out, Bne, ~Equal);  // AND_Gate
  and and_3 (and_3_out, Equal, Beq);
  Hex_Digit_Display hex_digit_display_2 (.value(LedData[27:24]));  // open: dp
  Hex_Digit_Display hex_digit_display_3 (.value(LedData[23:20]));  // open: dp
  Multiplexer #(.width(5), .enable("false")) multiplexer_2 (
    .in0(multiplexer_1_out), .in1({5{1'b1}}), .out(multiplexer_2_out), .sel(MEM_JAL));
  Adder #(.width(32)) adder_1 (.a(IF_PC), .b(32'h4), .out(PCnext));  // open: cin, cout
  Hex_Digit_Display hex_digit_display_4 (.value(LedData[19:16]));  // open: dp
  Hex_Digit_Display hex_digit_display_5 (.value(LedData[15:12]));  // open: dp
  ROM #(.addrWidth(10), .dataWidth(32)) rom_1 (.addr(IF_PC[11:2]), .data(rom_1_data));  // open: sel
  or or_1 (or_1_out, RST, \分支 );
  Adder #(.width(32)) adder_2 (.a(shifter_1_out), .b(EX_PC), .out(adder_2_out));  // open: cin, cout
  or or_2 (En[0], JMP1, Cmp);
  or or_3 (Cmp, and_2_out, and_3_out);
  Hex_Digit_Display hex_digit_display_6 (.value(LedData[7:4]));  // open: dp
  Hex_Digit_Display hex_digit_display_7 (.value(LedData[11:8]));  // open: dp
  Clock clock_1 (.out(CLK));
  Multiplexer #(.width(5), .enable("false")) multiplexer_3 (
    .in0(EX_ID[20:16]), .in1(EX_ID[15:11]), .out(multiplexer_3_out), .sel(EX_REGD));
  Multiplexer #(.width(5), .enable("false")) multiplexer_4 (
    .in0(ID32[25:21]), .in1(5'b00010), .out(multiplexer_4_out), .sel(ID_SYS));
  Hex_Digit_Display hex_digit_display_8 (.value(LedData[3:0]));  // open: dp
  Multiplexer #(.width(5), .enable("false")) multiplexer_5 (
    .in0(multiplexer_3_out), .in1({5{1'b1}}), .out(multiplexer_5_out), .sel(JAL1));
  nand nand_1 (nand_1_out, PCEnable, ~\数据相关 );  // NAND_Gate
  IF_ID if_id_1 (
    .PC(PCnext), .ID(rom_1_data), .CLK(CLK), .PC_2(ID_PC), .ID_2({ID32, FUNC}), .\同步清零_气泡_高电平有效 (or_1_out),
    .\使能端_低电平有效_stall_高电平有效 (nand_1_out));
  Multiplexer #(.width(5), .enable("false")) multiplexer_6 (
    .in0(ID32[20:16]), .in1(5'b00100), .out(multiplexer_6_out), .sel(ID_SYS));
  not not_1 (not_1_out, PCEnable);
  Multiplexer #(.width(32), .enable("false")) multiplexer_7 (
    .in0({EX_PC[31:28], EX_ID[25:0], 2'b00}), .in1(adder_2_out), .out(Addr2), .sel(Cmp));
  Multiplexer #(.select(2), .width(32), .enable("false")) multiplexer_8 (
    .in0(PCnext), .in1(Addr2), .in2(A1), .in3(A1), .out(PC), .sel(En));
  // 数据相关检测 数据相关检测_1: pin names not known; wires that end beside it: ID32[31:26], multiplexer_5_out, EX_RW, multiplexer_2_out, MEM_RW, FUNC, multiplexer_4_out, multiplexer_6_out, \数据相关检测_1_p9 , \数据相关检测_1_p10 , \数据相关 , \数据相关检测_1_p12 , \数据相关检测_1_p13 
  // Probe on \总周期数 
  // Probe on \无条件分支数 
  // Probe on \条件分支成功数 
  // Probe on \插入气泡数 
  // Probe on \LoadUse次数 
  // 硬布线控制器 硬布线控制器_1: pin names not known; wires that end beside it: JMP, JR, SignedExt, ID32[31:26], FUNC, ID_SYS, \硬布线控制器_1_p7 , \硬布线控制器_1_p8 , \硬布线控制器_1_p9 , \硬布线控制器_1_p10 , \硬布线控制器_1_p11 , \硬布线控制器_1_p12 , \硬布线控制器_1_p13 , \硬布线控制器_1_p14 , \硬布线控制器_1_p15 
  Multiplexer #(.width(5), .enable("false")) multiplexer_9 (
    .in0(ID32[25:21]), .in1(5'b00010), .out(multiplexer_9_out), .sel(ID_SYS));
  Multiplexer #(.width(5), .enable("false")) multiplexer_10 (
    .in0(ID32[20:16]), .in1(5'b00100), .out(multiplexer_10_out), .sel(ID_SYS));
  assign bit_extender_1_out = {{16{1'b0}}, {ID32[15:6], FUNC}};  // Bit_Extender bit_extender_1
  assign bit_extender_2_out = {{16{ID32[15]}}, {ID32[15:6], FUNC}};  // Bit_Extender bit_extender_2
  or or_4 (or_4_out, or_1_out, \数据相关 );
  // Probe on IF_PC[11:0]
  // Probe on ID_PC[11:0]
  // Probe on \数据相关检测_1_p9 
  // Probe on \数据相关检测_1_p10 
  // Probe on \数据相关检测_1_p12 
  // Probe on \数据相关检测_1_p13 
  Multiplexer #(.width(32), .enable("false")) multiplexer_11 (
    .in0(bit_extender_1_out), .in1(bit_extender_2_out), .out(multiplexer_11_out), .sel(SignedExt));
  Comparator #(.width(32)) comparator_1 (.a(A), .b(32'h22), .eq(comparator_1_eq));  // open: gt, lt
  and and_4 (and_4_out, comparator_1_eq, SYS);
  // Probe on EX_PC[11:0]
  MIPS_Regifile mips_regifile_1 (
    .Din(RDIN), .Clk(CLK), .R1(mips_regifile_1_r1), .R2(mips_regifile_1_r2), .WE(REGW), .W_num(W_num),
    .R1_num(multiplexer_9_out), .R2_num(multiplexer_10_out));
  not not_2 (not_2_out, comparator_1_eq);
  Multiplexer #(.width(32), .enable("false")) multiplexer_12 (
    .in0(LedData), .in1(B), .out(multiplexer_12_out), .sel(and_4_out));
  Register #(.width(32)) register_1 (.D(multiplexer_12_out), .Q(LedData), .clk(CLK));  // open: en, clr
  // Probe on WB_PC[11:0]
  // Probe on MEM_PC[11:0]
  // ID_EX id_ex_1: pin names not known; wires that end beside it: \硬布线控制器_1_p7 , \硬布线控制器_1_p8 , \硬布线控制器_1_p9 , \硬布线控制器_1_p10 , \硬布线控制器_1_p11 , \硬布线控制器_1_p12 , \硬布线控制器_1_p13 , \硬布线控制器_1_p14 , \硬布线控制器_1_p15 , ID32[10:6], not_1_out, JMP, \硬布线控制器_1_p7 , JR, \硬布线控制器_1_p8 , \硬布线控制器_1_p9 , \硬布线控制器_1_p10 , \硬布线控制器_1_p11 , \硬布线控制器_1_p12 , \硬布线控制器_1_p13 , \硬布线控制器_1_p14 , \硬布线控制器_1_p15 , ID_SYS, ID_PC, {ID32, FUNC}, mips_regifile_1_r1, mips_regifile_1_r2, multiplexer_11_out, ID32[10:6], CLK, or_4_out
  D_Flip_Flop d_ff_1 (.clk(CLK), .D(Go), .Qn(d_ff_1_qn));  // open: Q, preset, en, reset
  not not_3 (PCEnable, and_5_out);
  and and_5 (and_5_out, d_ff_1_qn, SYS, not_2_out);
  Multiplexer #(.width(32), .enable("false")) multiplexer_13 (
    .in0(undriven_6), .in1(IMM), .out(multiplexer_13_out), .sel(undriven_4));
  or or_5 (jump, JMP1, JAL1);
  MIPS_ALU mips_alu_1 (
    .X(A1), .Y(multiplexer_13_out), .AluOP(undriven_3), .Equal(Equal), .Result(mips_alu_1_result),
    .shamt(undriven_7));  // open: Result_2
  and and_6 (and_6_out, Beq, Equal);
  and and_7 (and_7_out, Bne, ~Equal);  // AND_Gate
  EX_MEM ex_mem_1 (
    .MTR(undriven), .MW(undriven_2), .REGW(EX_RW), .JAL(JAL1), .REGD(EX_REGD), .SYS(undriven_5), .PC(EX_PC),
    .ID(EX_ID), .A(A1), .B(undriven_6), .ALU(mips_alu_1_result), .CLK(CLK), .MTR_2(ex_mem_1_mtr_2),
    .MW_2(ex_mem_1_mw_2), .REGW_2(MEM_RW), .JAL_2(MEM_JAL), .REGD_2(MEM_REGD), .SYS_2(ex_mem_1_sys_2),
    .PC_2(MEM_PC), .ID_2(MEM_ID), .A_2(ex_mem_1_a_2), .B_2(ex_mem_1_b_2), .ALU_2(ex_mem_1_alu_2),
    .\同步清零_气泡_高电平有效 (RST), .\使能端_低电平有效_stall_高电平有效 (not_1_out));  // open: blez, blezout, sh, shout, lui, luiout, xor, xorout
  or or_6 (\无条件分支 , jump, En[1]);
  or or_7 (\条件分支 , and_6_out, and_7_out);
  or or_8 (\分支 , \无条件分支 , \条件分支 );
  and and_8 (and_8_out, \数据相关 , PCEnable);
  RAM #(.addrWidth(10), .dataWidth(32), .bus("separate")) ram_1 (
    .addr(ex_mem_1_alu_2[11:2]), .din(ex_mem_1_b_2), .data(ram_1_data), .str(ex_mem_1_mw_2), .clk(CLK),
    .clr(RST));  // open: sel, ld
  Counter #(.width(16), .max('hffff)) counter_1 (
    .count(and_8_out), .Q(\插入气泡数 ), .clk(CLK), .clr(RST));  // open: load, D, carry
  Counter #(.width(16), .max('hffff)) counter_2 (
    .count(PCEnable), .Q(\总周期数 ), .clk(CLK), .clr(RST));  // open: load, D, carry
  MEM_WB mem_wb_1 (
    .MTR(ex_mem_1_mtr_2), .REGW(MEM_RW), .JAL(MEM_JAL), .REGD(MEM_REGD), .SYS(ex_mem_1_sys_2), .PC(MEM_PC),
    .ID(MEM_ID), .A(ex_mem_1_a_2), .MD(ram_1_data), .B(ex_mem_1_b_2), .ALU(ex_mem_1_alu_2), .CLK(CLK),
    .MTR_2(mem_wb_1_mtr_2), .REGW_2(REGW), .JAL_2(mem_wb_1_jal_2), .REGD_2(mem_wb_1_regd_2), .SYS_2(SYS),
    .PC_2(WB_PC), .ID_2(mem_wb_1_id_2), .A_2(A), .MD_2(mem_wb_1_md_2), .B_2(B), .ALU_2(mem_wb_1_alu_2),
    .\同步清零_气泡_高电平有效 (RST), .\使能端_低电平有效_stall_高电平有效 (not_1_out));  // open: blez, blezout, sh, shout, lui, luiout, xor, xorout
  Counter #(.width(16), .max('hffff)) counter_3 (
    .count(\无条件分支 ), .Q(\无条件分支数 ), .clk(CLK), .clr(RST));  // open: load, D, carry
  Multiplexer #(.width(32), .enable("false")) multiplexer_14 (
    .in0(mem_wb_1_alu_2), .in1(mem_wb_1_md_2), .out(multiplexer_14_out), .sel(mem_wb_1_mtr_2));
  Counter #(.width(16), .max('hffff)) counter_4 (
    .count(\条件分支 ), .Q(\条件分支成功数 ), .clk(CLK), .clr(RST));  // open: load, D, carry
  Multiplexer #(.width(5), .enable("false")) multiplexer_15 (
    .in0(mem_wb_1_id_2[20:16]), .in1(mem_wb_1_id_2[15:11]), .out(multiplexer_15_out), .sel(mem_wb_1_regd_2));
  Multiplexer #(.width(5), .enable("false")) multiplexer_16 (
    .in0(multiplexer_15_out), .in1({5{1'b1}}), .out(W_num), .sel(mem_wb_1_jal_2));
  Multiplexer #(.width(32), .enable("false")) multiplexer_17 (
    .in0(multiplexer_14_out), .in1(WB_PC), .out(RDIN), .sel(mem_wb_1_jal_2));

  // Other names for the same wires on the sheet: PCO[31:0] = EX_PC; PC_choose = En[0]; JR1 = En[1]; ID32[5:0] = FUNC;
  //   ID_RT[4:0] = ID32[20:16]; ID_RS[4:0] = ID32[25:21]; OP[5:0] = ID32[31:26]

  // Notes on the sheet:
  //   中断源
  //   rt
  //   rd
  //   中断等待指示
  //   指令存储器
  //   数码管输出
  //   rt
  //   rd
  //   contents of rom_1 (hex, n*v repeats v):
  //   20110004 ae310000 8e320000 2252fffc 20100000 22110001 2118020 22520004 ae500000 22310001 2118020
  //   22520004 ae500000 22310001 2118020 22520004 ae500000 22310001 2118020 22520004 ae500000 22310001
  //   2118020 22520004 ae500000 22310001 2118020 22520004 ae500000 22310001 2118020 22520004 ae500000
  //   2002000a 20100000 20100000 20100000 c
  //   OP
  //   Func
  //   rs
  //   rt
  //   流水调试日志用
  //   rt
  //   rd
endmodule

module \重定向流水线  (
);

  wire and_1_out, and_2_out, and_3_out, and_4_out, and_5_out, and_6_out, and_7_out, Beq, BLEZ, Bne, CLK, Cmp,
       comparator_1_eq, d_ff_1_qn, Equal, ex_mem_1_mw_2, ex_mem_1_sys_2, EX_MTR, EX_REGD, EX_RW, Go, ID_SYS,
       IR1, IR2, IR3, JAL1, JMP, JMP1, JR, jump, loaduse, LUI, MEM_JAL, MEM_REGD, MEM_RW, mem_wb_1_jal_2,
       mem_wb_1_mtr_2, mem_wb_1_regd_2, MEMTOREG, nand_1_out, not_1_out, not_2_out, or_1_out, or_4_out,
       PCEnable, REGW, RST, SH, SignedExt, SYS, undriven, undriven_3, undriven_4, W1, W2, W3, XOR, \分支 ,
       \无条件分支 , \条件分支 , \硬布线控制器_1_p11 , \硬布线控制器_1_p12 , \硬布线控制器_1_p13 , \硬布线控制器_1_p14 , \硬布线控制器_1_p15 ,
       \硬布线控制器_1_p16 , \硬布线控制器_1_p17 , \硬布线控制器_1_p18 , \硬布线控制器_1_p19 ;
  wire [1:0] En, f1, f2, forward1, forward2;
  wire [3:0] undriven_2;
  wire [4:0] multiplexer_1_out, multiplexer_2_out, multiplexer_3_out, multiplexer_4_out, multiplexer_5_out,
       multiplexer_6_out, multiplexer_9_out, multiplexer_10_out, multiplexer_16_out, undriven_5, W_num;
  wire [5:0] FUNC;
  wire [15:0] \LoadUse次数 , \总周期数 , \无条件分支数 , \条件分支成功数 ;
  wire [31:0] A, A1, adder_2_out, Addr2, Ain, ALUresult, ALUresult2, B, B1, Bin, bit_extender_1_out,
       bit_extender_2_out, EX_ID, ex_mem_1_a_2, ex_mem_1_b_2, EX_PC, ID_PC, IF_PC, IMM, LedData, MEM_ID,
       MEM_PC, mem_wb_1_id_2, Memdata, mips_alu_1_result, mips_regifile_1_r1, mips_regifile_1_r2,
       multiplexer_11_out, multiplexer_12_out, multiplexer_13_out, multiplexer_15_out, PC, PCnext,
       ram_1_data, RDIN, rom_1_data, shifter_1_out, WB_PC;
  wire [31:6] ID32;

  and and_1 (and_1_out, PCEnable, ~loaduse);  // AND_Gate
  Button \u_总复位  (.out(RST));
  Button _1 (.out(IR1));
  Button _2 (.out(IR2));
  Button _3 (.out(IR3));
  Register #(.width(32)) u_PC (.D(PC), .en(and_1_out), .Q(IF_PC), .clk(CLK), .clr(RST));
  Button \u_继续运行  (.out(Go));
  Hex_Digit_Display hex_digit_display_1 (.value(LedData[31:28]));  // open: dp
  LED led_1 (.in(W1));
  LED led_2 (.in(W2));
  LED led_3 (.in(W3));
  Multiplexer #(.width(5), .enable("false")) multiplexer_1 (
    .in0(MEM_ID[20:16]), .in1(MEM_ID[15:11]), .out(multiplexer_1_out), .sel(MEM_REGD));
  Shifter #(.width(32)) shifter_1 (.in(IMM), .\dist (5'b00010), .out(shifter_1_out));
  and and_2 (and_2_out, Bne, ~Equal);  // AND_Gate
  and and_3 (and_3_out, Equal, Beq);
  Hex_Digit_Display hex_digit_display_2 (.value(LedData[27:24]));  // open: dp
  Hex_Digit_Display hex_digit_display_3 (.value(LedData[23:20]));  // open: dp
  Multiplexer #(.width(5), .enable("false")) multiplexer_2 (
    .in0(multiplexer_1_out), .in1({5{1'b1}}), .out(multiplexer_2_out), .sel(MEM_JAL));
  Adder #(.width(32)) adder_1 (.a(IF_PC), .b(32'h4), .out(PCnext));  // open: cin, cout
  Hex_Digit_Display hex_digit_display_4 (.value(LedData[19:16]));  // open: dp
  Hex_Digit_Display hex_digit_display_5 (.value(LedData[15:12]));  // open: dp
  ROM #(.addrWidth(10), .dataWidth(32)) rom_1 (.addr(IF_PC[11:2]), .data(rom_1_data));  // open: sel
  or or_1 (or_1_out, RST, \分支 );
  Adder #(.width(32)) adder_2 (.a(shifter_1_out), .b(EX_PC), .out(adder_2_out));  // open: cin, cout
  or or_2 (En[0], JMP1, Cmp);
  or or_3 (Cmp, and_2_out, and_3_out);
  Hex_Digit_Display hex_digit_display_6 (.value(LedData[7:4]));  // open: dp
  Hex_Digit_Display hex_digit_display_7 (.value(LedData[11:8]));  // open: dp
  Clock clock_1 (.out(CLK));
  Multiplexer #(.width(5), .enable("false")) multiplexer_3 (
    .in0(EX_ID[20:16]), .in1(EX_ID[15:11]), .out(multiplexer_3_out), .sel(EX_REGD));
  Multiplexer #(.width(5), .enable("false")) multiplexer_4 (
    .in0(ID32[25:21]), .in1(5'b00010), .out(multiplexer_4_out), .sel(ID_SYS));
  Hex_Digit_Display hex_digit_display_8 (.value(LedData[3:0]));  // open: dp
  Multiplexer #(.width(5), .enable("false")) multiplexer_5 (
    .in0(multiplexer_3_out), .in1({5{1'b1}}), .out(multiplexer_5_out), .sel(JAL1));
  nand nand_1 (nand_1_out, PCEnable, ~loaduse);  // NAND_Gate
  IF_ID if_id_1 (
    .PC(PCnext), .ID(rom_1_data), .CLK(CLK), .PC_2(ID_PC), .ID_2({ID32, FUNC}), .\同步清零_气泡_高电平有效 (or_1_out),
    .\使能端_低电平有效_stall_高电平有效 (nand_1_out));
  Multiplexer #(.width(5), .enable("false")) multiplexer_6 (
    .in0(ID32[20:16]), .in1(5'b00100), .out(multiplexer_6_out), .sel(ID_SYS));
  not not_1 (not_1_out, PCEnable);
  Multiplexer #(.width(32), .enable("false")) multiplexer_7 (
    .in0({EX_PC[31:28], EX_ID[25:0], 2'b00}), .in1(adder_2_out), .out(Addr2), .sel(Cmp));
  Multiplexer #(.select(2), .width(32), .enable("false")) multiplexer_8 (
    .in0(PCnext), .in1(Addr2), .in2(A1), .in3(A1), .out(PC), .sel(En));
  _1 u_1_1 (
    .OP(ID32[31:26]), .EX_WriteReg_num(multiplexer_5_out), .EX_RegWrite(EX_RW), .forwordA(f1),
    .MEM_WriteReg_num(multiplexer_2_out), .MEM_RegWrite(MEM_RW), .forwordB(f2), .Func(FUNC),
    .ID_R1_num(multiplexer_4_out), .ID_R2_num(multiplexer_6_out), .LoadUse(loaduse), .EX_MTR(EX_MTR),
    .MEM_MTR(MEMTOREG));
  // Probe on \总周期数 
  // Probe on \无条件分支数 
  // Probe on \条件分支成功数 
  // Probe on \LoadUse次数 
  // Probe on \LoadUse次数 
  // 硬布线控制器 硬布线控制器_1: pin names not known; wires that end beside it: JMP, JR, SignedExt, XOR, LUI, SH, BLEZ, ID32[31:26], FUNC, ID_SYS, \硬布线控制器_1_p11 , \硬布线控制器_1_p12 , \硬布线控制器_1_p13 , \硬布线控制器_1_p14 , \硬布线控制器_1_p15 , \硬布线控制器_1_p16 , \硬布线控制器_1_p17 , \硬布线控制器_1_p18 , \硬布线控制器_1_p19 
  Multiplexer #(.width(5), .enable("false")) multiplexer_9 (
    .in0(ID32[25:21]), .in1(5'b00010), .out(multiplexer_9_out), .sel(ID_SYS));
  Multiplexer #(.width(5), .enable("false")) multiplexer_10 (
    .in0(ID32[20:16]), .in1(5'b00100), .out(multiplexer_10_out), .sel(ID_SYS));
  assign bit_extender_1_out = {{16{1'b0}}, {ID32[15:6], FUNC}};  // Bit_Extender bit_extender_1
  assign bit_extender_2_out = {{16{ID32[15]}}, {ID32[15:6], FUNC}};  // Bit_Extender bit_extender_2
  or or_4 (or_4_out, or_1_out, loaduse);
  // Probe on ID_PC[11:0]
  // Probe on IF_PC[11:0]
  Multiplexer #(.width(32), .enable("false")) multiplexer_11 (
    .in0(bit_extender_1_out), .in1(bit_extender_2_out), .out(multiplexer_11_out), .sel(SignedExt));
  Comparator #(.width(32)) comparator_1 (.a(A), .b(32'h22), .eq(comparator_1_eq));  // open: gt, lt
  and and_4 (and_4_out, comparator_1_eq, SYS);
  // Probe on EX_PC[11:0]
  MIPS_Regifile mips_regifile_1 (
    .Din(RDIN), .Clk(CLK), .R1(mips_regifile_1_r1), .R2(mips_regifile_1_r2), .WE(REGW), .W_num(W_num),
    .R1_num(multiplexer_9_out), .R2_num(multiplexer_10_out));
  not not_2 (not_2_out, comparator_1_eq);
  Multiplexer #(.width(32), .enable("false")) multiplexer_12 (
    .in0(LedData), .in1(B), .out(multiplexer_12_out), .sel(and_4_out));
  Register #(.width(32)) register_1 (.D(multiplexer_12_out), .Q(LedData), .clk(CLK));  // open: en, clr
  // Probe on MEM_PC[11:0]
  // Probe on WB_PC[11:0]
  // ID_EX id_ex_1: pin names not known; wires that end beside it: \硬布线控制器_1_p11 , \硬布线控制器_1_p12 , \硬布线控制器_1_p13 , \硬布线控制器_1_p14 , \硬布线控制器_1_p15 , \硬布线控制器_1_p16 , \硬布线控制器_1_p17 , \硬布线控制器_1_p18 , \硬布线控制器_1_p19 , ID32[10:6], f2, not_1_out, f2, JMP, \硬布线控制器_1_p11 , JR, \硬布线控制器_1_p12 , \硬布线控制器_1_p13 , \硬布线控制器_1_p14 , \硬布线控制器_1_p15 , \硬布线控制器_1_p16 , \硬布线控制器_1_p17 , \硬布线控制器_1_p18 , \硬布线控制器_1_p19 , ID_SYS, ID_PC, {ID32, FUNC}, mips_regifile_1_r1, mips_regifile_1_r2, multiplexer_11_out, ID32[10:6], f1, CLK, or_4_out
  D_Flip_Flop d_ff_1 (.clk(CLK), .D(Go), .Qn(d_ff_1_qn));  // open: Q, preset, en, reset
  and and_5 (and_5_out, d_ff_1_qn, SYS, not_2_out);
  not not_3 (PCEnable, and_5_out);
  Multiplexer #(.width(32), .enable("false")) multiplexer_13 (
    .in0(Bin), .in1(IMM), .out(multiplexer_13_out), .sel(undriven_3));
  or or_5 (jump, JMP1, JAL1);
  MIPS_ALU mips_alu_1 (
    .X(Ain), .Y(multiplexer_13_out), .AluOP(undriven_2), .Equal(Equal), .Result(mips_alu_1_result),
    .shamt(undriven_5));  // open: Result_2
  and and_6 (and_6_out, Beq, Equal);
  and and_7 (and_7_out, Bne, ~Equal);  // AND_Gate
  EX_MEM ex_mem_1 (
    .MTR(EX_MTR), .MW(undriven), .REGW(EX_RW), .JAL(JAL1), .REGD(EX_REGD), .SYS(undriven_4), .PC(EX_PC),
    .ID(EX_ID), .A(Ain), .B(Bin), .ALU(mips_alu_1_result), .CLK(CLK), .MTR_2(MEMTOREG), .MW_2(ex_mem_1_mw_2),
    .REGW_2(MEM_RW), .JAL_2(MEM_JAL), .REGD_2(MEM_REGD), .SYS_2(ex_mem_1_sys_2), .PC_2(MEM_PC),
    .ID_2(MEM_ID), .A_2(ex_mem_1_a_2), .B_2(ex_mem_1_b_2), .ALU_2(ALUresult), .\同步清零_气泡_高电平有效 (RST),
    .\使能端_低电平有效_stall_高电平有效 (not_1_out));  // open: blez, blezout, sh, shout, lui, luiout, xor, xorout
  or or_6 (\无条件分支 , jump, En[1]);
  or or_7 (\条件分支 , and_6_out, and_7_out);
  or or_8 (\分支 , \无条件分支 , \条件分支 );
  RAM #(.addrWidth(10), .dataWidth(32), .bus("separate")) ram_1 (
    .addr(ALUresult[11:2]), .din(ex_mem_1_b_2), .data(ram_1_data), .str(ex_mem_1_mw_2), .clk(CLK), .clr(RST));  // open: sel, ld
  Multiplexer #(.select(2), .width(32), .enable("false")) multiplexer_14 (
    .in0(A1), .in1(ALUresult2), .in2(Memdata), .in3(ALUresult), .out(Ain), .sel(forward1));
  Counter #(.width(16), .max('hffff)) counter_1 (
    .count(loaduse), .Q(\LoadUse次数 ), .clk(CLK), .clr(RST));  // open: load, D, carry
  Counter #(.width(16), .max('hffff)) counter_2 (
    .count(PCEnable), .Q(\总周期数 ), .clk(CLK), .clr(RST));  // open: load, D, carry
  MEM_WB mem_wb_1 (
    .MTR(MEMTOREG), .REGW(MEM_RW), .JAL(MEM_JAL), .REGD(MEM_REGD), .SYS(ex_mem_1_sys_2), .PC(MEM_PC),
    .ID(MEM_ID), .A(ex_mem_1_a_2), .MD(ram_1_data), .B(ex_mem_1_b_2), .ALU(ALUresult), .CLK(CLK),
    .MTR_2(mem_wb_1_mtr_2), .REGW_2(REGW), .JAL_2(mem_wb_1_jal_2), .REGD_2(mem_wb_1_regd_2), .SYS_2(SYS),
    .PC_2(WB_PC), .ID_2(mem_wb_1_id_2), .A_2(A), .MD_2(Memdata), .B_2(B), .ALU_2(ALUresult2),
    .\同步清零_气泡_高电平有效 (RST), .\使能端_低电平有效_stall_高电平有效 (not_1_out));  // open: blez, blezout, sh, shout, lui, luiout, xor, xorout
  Counter #(.width(16), .max('hffff)) counter_3 (
    .count(\无条件分支 ), .Q(\无条件分支数 ), .clk(CLK), .clr(RST));  // open: load, D, carry
  Multiplexer #(.width(32), .enable("false")) multiplexer_15 (
    .in0(ALUresult2), .in1(Memdata), .out(multiplexer_15_out), .sel(mem_wb_1_mtr_2));
  Counter #(.width(16), .max('hffff)) counter_4 (
    .count(\条件分支 ), .Q(\条件分支成功数 ), .clk(CLK), .clr(RST));  // open: load, D, carry
  Multiplexer #(.width(5), .enable("false")) multiplexer_16 (
    .in0(mem_wb_1_id_2[20:16]), .in1(mem_wb_1_id_2[15:11]), .out(multiplexer_16_out), .sel(mem_wb_1_regd_2));
  Multiplexer #(.select(2), .width(32), .enable("false")) multiplexer_17 (
    .in0(B1), .in1(ALUresult2), .in2(Memdata), .in3(ALUresult), .out(Bin), .sel(forward2));
  Multiplexer #(.width(5), .enable("false")) multiplexer_18 (
    .in0(multiplexer_16_out), .in1({5{1'b1}}), .out(W_num), .sel(mem_wb_1_jal_2));
  Multiplexer #(.width(32), .enable("false")) multiplexer_19 (
    .in0(multiplexer_15_out), .in1(WB_PC), .out(RDIN), .sel(mem_wb_1_jal_2));

  // Other names for the same wires on the sheet: PCO[31:0] = EX_PC; PC_choose = En[0]; JR1 = En[1]; ID32[5:0] = FUNC;
  //   ID_RT[4:0] = ID32[20:16]; ID_RS[4:0] = ID32[25:21]; OP[5:0] = ID32[31:26]; 插入气泡数[15:0] = \LoadUse次数 

  // Notes on the sheet:
  //   中断源
  //   rt
  //   rd
  //   中断等待指示
  //   指令存储器
  //   数码管输出
  //   rt
  //   rd
  //   contents of rom_1 (hex, n*v repeats v):
  //   20110001 8100005 20110001 20120002 20130003 8100009 20110001 20120002 20130003 810000d 20110001
  //   20120002 20130003 8100011 20110001 20120002 20130003 c1000ba 20100001 20110001 118fc0 112020
  //   20020022 c 118882 12200001 8100015 112020 20020022 c 20110001 118880 112020 20020022 c 12200001
  //   810001f 20110001 118fc0 112020 20020022 c 1188c3 112020 20020022 c 118903 112020 20020022 c 118903
  //   112020 20020022 c 118903 112020 20020022 c 118903 112020 20020022 c 118903 112020 20020022 c 118903
  //   112020 20020022 c 118903 112020 20020022 c 20100001 109fc0 139fc3 8021 2012000c 24160003 26100001
  //   3210000f 20080008 20090001 139900 2709825 132020 20020022 c 1094022 1500fff9 22100001 2018000f
  //   2188024 108700 20080008 20090001 139902 2709825 132021 20020022 c 1094022 1500fff9 108702 2c9b022
  //   12c00001 8100050 4020 1084027 84400 3508ffff 82021 20020022 c 2010ffff 20110000 ae300000 22100001
  //   22310004 ae300000 22100001 22310004 ae300000 22100001 22310004 ae300000 22100001 22310004 ae300000
  //   22100001 22310004 ae300000 22100001 22310004 ae300000 22100001 22310004 ae300000 22100001 22310004
  //   ae300000 22100001 22310004 ae300000 22100001 22310004 ae300000 22100001 22310004 ae300000 22100001
  //   22310004 ae300000 22100001 22310004 ae300000 22100001 22310004 ae300000 22100001 22310004 ae300000
  //   22100001 22310004 22100001 8020 2011003c 8e130000 8e340000 274402a 11000002 ae330000 ae140000
  //   2231fffc 1611fff8 102020 20020022 c 22100004 2011003c 1611fff2 20020032 c 2002000a c 20100000
  //   22100001 102020 20020022 c 22100002 102020 20020022 c 22100003 102020 20020022 c 22100004 102020
  //   20020022 c 22100005 102020 20020022 c 22100006 102020 20020022 c 22100007 102020 20020022 c 22100008
  //   102020 20020022 20020022 c 3e00008 20090000 200b0020 20110001 20120001 a5310000 112020 20020022 c
  //   2328820 21290002 216bffff 1560fff8 200b0010 20090000 8d310000 112020 20020022 c 21290004 216bffff
  //   1560fff9 2002000a c 2008ffff 20117777 112020 20020022 c 200b0010 2288826 112020 20020022 c 216bffff
  //   1560fffa 2002000a c 2011fff1 112020 20020022 c 22310001 1a20fffb 2002000a c 200b0008 3c11fedc
  //   3631ffff 112020 20020022 c 3c11ba98 112020 c 3c117654 112020 c 3c113210 112020 c 216bffff 1560fff0
  //   2002000a c
  //   OP
  //   Func
  //   rs
  //   rt
  //   流水调试日志用
  //   rt
  //   rd
endmodule

module personal (
  input  OP0,
  input  OP1,
  input  OP2,
  input  OP3,
  input  OP4,
  input  OP5,
  input  F0,
  input  F1,
  input  F2,
  input  F3,
  input  F4,
  input  F5,
  output XOR,
  output LUI,
  output SH,
  output BLEZ
);

  wire not_1_out, not_2_out, not_3_out, not_4_out, not_5_out, not_6_out, not_7_out, not_8_out, not_9_out,
       not_10_out, not_11_out, not_12_out, not_13_out, not_14_out, not_15_out, not_16_out, not_17_out,
       not_18_out;

  not not_1 (not_1_out, OP5);
  not not_2 (not_2_out, OP4);
  not not_3 (not_3_out, OP3);
  not not_4 (not_4_out, OP2);
  not not_5 (not_5_out, OP1);
  not not_6 (not_6_out, OP0);
  not not_7 (not_7_out, F4);
  not not_8 (not_8_out, F3);
  not not_9 (not_9_out, F0);
  not not_10 (not_10_out, OP5);
  not not_11 (not_11_out, OP4);
  not not_12 (not_12_out, OP4);
  not not_13 (not_13_out, OP2);
  not not_14 (not_14_out, OP1);
  not not_15 (not_15_out, OP5);
  not not_16 (not_16_out, OP4);
  not not_17 (not_17_out, OP3);
  not not_18 (not_18_out, OP0);
  and and_1 (XOR, not_1_out, not_2_out, not_3_out, not_4_out, not_5_out, not_6_out, F5, not_7_out, not_8_out, F2, F1, not_9_out);
  and and_2 (LUI, not_10_out, not_11_out, OP3, OP2, OP1, OP0);
  and and_3 (SH, OP5, not_12_out, OP3, not_13_out, not_14_out, OP0);
  and and_4 (BLEZ, not_15_out, not_16_out, not_17_out, OP2, OP1, not_18_out);
endmodule

module \重定向personal  (
);

  wire and_1_out, and_2_out, and_3_out, and_5_out, and_6_out, and_7_out, and_8_out, Beq, BLEZ, BLEZ1, Bne,
       CLK, Cmp, Cmp1, comparator_1_eq, comparator_2_eq, Equal, ex_mem_1_blezout, ex_mem_1_luiout,
       ex_mem_1_mw_2, ex_mem_1_sys_2, ex_mem_1_xorout, EX_MTR, EX_REGD, EX_RW, Go, id_ex_1_alu_src_2,
       id_ex_1_mw_2, id_ex_1_sys_2, ID_SYS, IR1, IR2, IR3, JAL1, JAL4, JMP, JMP1, JR, jump, loaduse, LUI,
       LUI1, LUI4, MEM_JAL, MEM_REGD, MEM_RW, mem_wb_1_mtr_2, mem_wb_1_regd_2, MEMTOREG, nand_1_out,
       not_1_out, not_2_out, or_1_out, or_4_out, PCEnable, REGW, RST, SH, SH1, SH3, SignedExt, SYS, W1, W2,
       W3, XOR, xor1, XOR4, \分支 , \无条件分支 , \条件分支 , \硬布线控制器_1_alu_src , \硬布线控制器_1_beq , \硬布线控制器_1_bne ,
       \硬布线控制器_1_jal , \硬布线控制器_1_memtoreg , \硬布线控制器_1_memwrite , \硬布线控制器_1_regdst , \硬布线控制器_1_regwrite ;
  wire [1:0] En, f1, f2, forward1, forward2;
  wire [3:0] id_ex_1_aluop_2, \硬布线控制器_1_alu_op ;
  wire [4:0] id_ex_1_shm_2, multiplexer_1_out, multiplexer_2_out, multiplexer_3_out, multiplexer_4_out,
       multiplexer_5_out, multiplexer_8_out, multiplexer_9_out, multiplexer_10_out, multiplexer_19_out, W_num;
  wire [5:0] FUNC;
  wire [15:0] \LoadUse次数 , \总周期数 , \无条件分支数 , \条件分支成功数 ;
  wire [31:0] A, A1, adder_2_out, Addr2, Ain, ALUre, ALUre22, ALUresult, ALUresult2, B, B1, Bin,
       bit_extender_1_out, bit_extender_2_out, EX_ID, ex_mem_1_a_2, EX_PC, ID_PC, IF_PC, IMM, LedData,
       MEM_ID, MEM_PC, mem_wb_1_id_2, Memdata, mips_regifile_1_r1, mips_regifile_1_r2, multiplexer_11_out,
       multiplexer_12_out, multiplexer_13_out, multiplexer_14_out, multiplexer_18_out, PC, pc_44, PCnext,
       R22, R222, ram_1_data, RDIN, rom_1_data, shifter_1_out, shifter_2_out, shifter_3_out, undriven;
  wire [31:6] ID32;

  and and_1 (and_1_out, PCEnable, ~loaduse);  // AND_Gate
  Button \u_总复位  (.out(RST));
  Button _1 (.out(IR1));
  Button _2 (.out(IR2));
  Button _3 (.out(IR3));
  Register #(.width(32)) u_PC (.D(PC), .en(and_1_out), .Q(IF_PC), .clk(CLK), .clr(RST));
  Comparator #(.width(32)) comparator_1 (.a(ALUre), .b(32'h1), .eq(comparator_1_eq));  // open: gt, lt
  Button \u_继续运行  (.out(Go));
  Hex_Digit_Display hex_digit_display_1 (.value(LedData[31:28]));  // open: dp
  LED led_1 (.in(W1));
  LED led_2 (.in(W2));
  LED led_3 (.in(W3));
  Multiplexer #(.width(5), .enable("false")) multiplexer_1 (
    .in0(MEM_ID[20:16]), .in1(MEM_ID[15:11]), .out(multiplexer_1_out), .sel(MEM_REGD));
  Shifter #(.width(32)) shifter_1 (.in(IMM), .\dist (5'b00010), .out(shifter_1_out));
  and and_2 (and_2_out, Bne, ~Equal);  // AND_Gate
  and and_3 (and_3_out, Equal, Beq);
  and and_4 (Cmp1, comparator_1_eq, BLEZ1);
  Hex_Digit_Display hex_digit_display_2 (.value(LedData[23:20]));  // open: dp
  Hex_Digit_Display hex_digit_display_3 (.value(LedData[27:24]));  // open: dp
  Multiplexer #(.width(5), .enable("false")) multiplexer_2 (
    .in0(multiplexer_1_out), .in1({5{1'b1}}), .out(multiplexer_2_out), .sel(MEM_JAL));
  Adder #(.width(32)) adder_1 (.a(IF_PC), .b(32'h4), .out(PCnext));  // open: cin, cout
  Adder #(.width(32)) adder_2 (.a(shifter_1_out), .b(EX_PC), .out(adder_2_out));  // open: cin, cout
  Hex_Digit_Display hex_digit_display_4 (.value(LedData[15:12]));  // open: dp
  Hex_Digit_Display hex_digit_display_5 (.value(LedData[19:16]));  // open: dp
  ROM #(.addrWidth(10), .dataWidth(32)) rom_1 (.addr(IF_PC[11:2]), .data(rom_1_data));  // open: sel
  or or_1 (or_1_out, RST, \分支 );
  or or_2 (Cmp, and_2_out, and_3_out, Cmp1);
  Hex_Digit_Display hex_digit_display_6 (.value(LedData[7:4]));  // open: dp
  Hex_Digit_Display hex_digit_display_7 (.value(LedData[11:8]));  // open: dp
  Clock clock_1 (.out(CLK));
  Multiplexer #(.width(5), .enable("false")) multiplexer_3 (
    .in0(EX_ID[20:16]), .in1(EX_ID[15:11]), .out(multiplexer_3_out), .sel(EX_REGD));
  Multiplexer #(.width(5), .enable("false")) multiplexer_4 (
    .in0(ID32[25:21]), .in1(5'b00010), .out(multiplexer_4_out), .sel(ID_SYS));
  or or_3 (En[0], JMP1, Cmp);
  Hex_Digit_Display hex_digit_display_8 (.value(LedData[3:0]));  // open: dp
  Multiplexer #(.width(5), .enable("false")) multiplexer_5 (
    .in0(multiplexer_3_out), .in1({5{1'b1}}), .out(multiplexer_5_out), .sel(JAL1));
  nand nand_1 (nand_1_out, PCEnable, ~loaduse);  // NAND_Gate
  IF_ID if_id_1 (
    .PC(PCnext), .ID(rom_1_data), .CLK(CLK), .PC_2(ID_PC), .ID_2({ID32, FUNC}), .\同步清零_气泡_高电平有效 (or_1_out),
    .\使能端_低电平有效_stall_高电平有效 (nand_1_out));
  Multiplexer #(.width(32), .enable("false")) multiplexer_6 (
    .in0({EX_PC[31:28], EX_ID[25:0], 2'b00}), .in1(adder_2_out), .out(Addr2), .sel(Cmp));
  Multiplexer #(.select(2), .width(32), .enable("false")) multiplexer_7 (
    .in0(PCnext), .in1(Addr2), .in2(A1), .in3(A1), .out(PC), .sel(En));
  Multiplexer #(.width(5), .enable("false")) multiplexer_8 (
    .in0(ID32[20:16]), .in1(5'b00100), .out(multiplexer_8_out), .sel(ID_SYS));
  not not_1 (not_1_out, PCEnable);
  _1 u_1_1 (
    .OP(ID32[31:26]), .EX_WriteReg_num(multiplexer_5_out), .EX_RegWrite(EX_RW), .forwordA(f1),
    .MEM_WriteReg_num(multiplexer_2_out), .MEM_RegWrite(MEM_RW), .forwordB(f2), .Func(FUNC),
    .ID_R1_num(multiplexer_4_out), .ID_R2_num(multiplexer_8_out), .LoadUse(loaduse), .EX_MTR(EX_MTR),
    .MEM_MTR(MEMTOREG));
  // Probe on \总周期数 
  // Probe on \无条件分支数 
  // Probe on \条件分支成功数 
  // Probe on \LoadUse次数 
  // Probe on \LoadUse次数 
  \硬布线控制器  \u_硬布线控制器_1  (
    .Func(FUNC), .OP(ID32[31:26]), .ALU_OP(\硬布线控制器_1_alu_op ), .MemToReg(\硬布线控制器_1_memtoreg ),
    .MemWrite(\硬布线控制器_1_memwrite ), .ALU_SRC(\硬布线控制器_1_alu_src ), .RegWrite(\硬布线控制器_1_regwrite ),
    .SysCALL(ID_SYS), .SignedExt(SignedExt), .RegDst(\硬布线控制器_1_regdst ), .JR(JR), .JMP(JMP),
    .Beq(\硬布线控制器_1_beq ), .JAL(\硬布线控制器_1_jal ), .Bne(\硬布线控制器_1_bne ), .XOR(XOR), .LUI(LUI), .SH(SH),
    .BLEZ(BLEZ));
  Multiplexer #(.width(5), .enable("false")) multiplexer_9 (
    .in0(ID32[25:21]), .in1(5'b00010), .out(multiplexer_9_out), .sel(ID_SYS));
  Multiplexer #(.width(5), .enable("false")) multiplexer_10 (
    .in0(ID32[20:16]), .in1(5'b00100), .out(multiplexer_10_out), .sel(ID_SYS));
  assign bit_extender_1_out = {{16{1'b0}}, {ID32[15:6], FUNC}};  // Bit_Extender bit_extender_1
  assign bit_extender_2_out = {{16{ID32[15]}}, {ID32[15:6], FUNC}};  // Bit_Extender bit_extender_2
  or or_4 (or_4_out, or_1_out, loaduse);
  // Probe on IF_PC[11:0]
  // Probe on ID_PC[11:0]
  Multiplexer #(.width(32), .enable("false")) multiplexer_11 (
    .in0(bit_extender_1_out), .in1(bit_extender_2_out), .out(multiplexer_11_out), .sel(SignedExt));
  Comparator #(.width(32)) comparator_2 (.a(A), .b(32'h22), .eq(comparator_2_eq));  // open: gt, lt
  and and_5 (and_5_out, comparator_2_eq, SYS);
  Multiplexer #(.width(32), .enable("false")) multiplexer_12 (
    .in0(LedData), .in1(B), .out(multiplexer_12_out), .sel(and_5_out));
  // Probe on EX_PC[11:0]
  MIPS_Regifile mips_regifile_1 (
    .Din(RDIN), .Clk(CLK), .R1(mips_regifile_1_r1), .R2(mips_regifile_1_r2), .WE(REGW), .W_num(W_num),
    .R1_num(multiplexer_9_out), .R2_num(multiplexer_10_out));
  not not_2 (not_2_out, comparator_2_eq);
  Register #(.width(32)) register_1 (.D(multiplexer_12_out), .Q(LedData), .clk(CLK));  // open: en, clr
  // Probe on pc_44[11:0]
  // Probe on MEM_PC[11:0]
  ID_EX id_ex_1 (
    .JMP(JMP), .BEQ(\硬布线控制器_1_beq ), .JR(JR), .BNE(\硬布线控制器_1_bne ), .MTR(\硬布线控制器_1_memtoreg ),
    .MW(\硬布线控制器_1_memwrite ), .ALUOP(\硬布线控制器_1_alu_op ), .ALU_SRC(\硬布线控制器_1_alu_src ),
    .REGW(\硬布线控制器_1_regwrite ), .JAL(\硬布线控制器_1_jal ), .REGD(\硬布线控制器_1_regdst ), .SYS(ID_SYS), .PC(ID_PC),
    .ID({ID32, FUNC}), .A(mips_regifile_1_r1), .B(mips_regifile_1_r2), .IMM(multiplexer_11_out),
    .SHM(ID32[10:6]), .CLK(CLK), .JMP_2(JMP1), .BEQ_2(Beq), .JR_2(En[1]), .BNE_2(Bne), .MTR_2(EX_MTR),
    .MW_2(id_ex_1_mw_2), .ALUOP_2(id_ex_1_aluop_2), .ALU_SRC_2(id_ex_1_alu_src_2), .REGW_2(EX_RW),
    .JAL_2(JAL1), .REGD_2(EX_REGD), .SYS_2(id_ex_1_sys_2), .PC_2(EX_PC), .ID_2(EX_ID), .A_2(A1), .B_2(B1),
    .IMM_2(IMM), .SHM_2(id_ex_1_shm_2), .\同步清零_气泡_高电平有效 (or_4_out), .\使能端_低电平有效_stall_高电平有效 (not_1_out),
    .forward(f2), .forwardout(forward2), .forward1(f1), .forward1out(forward1), .blez(BLEZ), .blezout(BLEZ1),
    .sh(SH), .shout(SH1), .lui(LUI), .luiout(LUI1), .\xor (XOR), .xorout(xor1));
  and and_6 (and_6_out, ~Go, SYS, not_2_out);  // AND_Gate
  not not_3 (PCEnable, and_6_out);
  Multiplexer #(.width(32), .enable("false")) multiplexer_13 (
    .in0(Bin), .in1(IMM), .out(multiplexer_13_out), .sel(id_ex_1_alu_src_2));
  Shifter #(.width(32)) shifter_2 (.in(IMM), .\dist (5'b10000), .out(shifter_2_out));
  or or_5 (jump, JMP1, JAL1);
  MIPS_ALU mips_alu_1 (
    .X(Ain), .Y(multiplexer_14_out), .AluOP(id_ex_1_aluop_2), .Equal(Equal), .Result(ALUre),
    .shamt(id_ex_1_shm_2));  // open: Result_2
  Multiplexer #(.width(32), .enable("false")) multiplexer_14 (
    .in0(multiplexer_13_out), .in1(32'h1), .out(multiplexer_14_out), .sel(BLEZ1));
  Multiplexer #(.width(32), .enable("false")) multiplexer_15 (
    .in0(ALUre), .in1(shifter_2_out), .out(ALUre22), .sel(LUI1));
  and and_7 (and_7_out, Beq, Equal);
  and and_8 (and_8_out, Bne, ~Equal);  // AND_Gate
  EX_MEM ex_mem_1 (
    .MTR(EX_MTR), .MW(id_ex_1_mw_2), .REGW(EX_RW), .JAL(JAL1), .REGD(EX_REGD), .SYS(id_ex_1_sys_2),
    .PC(EX_PC), .ID(EX_ID), .A(Ain), .B(Bin), .ALU(ALUre22), .CLK(CLK), .MTR_2(MEMTOREG),
    .MW_2(ex_mem_1_mw_2), .REGW_2(MEM_RW), .JAL_2(MEM_JAL), .REGD_2(MEM_REGD), .SYS_2(ex_mem_1_sys_2),
    .PC_2(MEM_PC), .ID_2(MEM_ID), .A_2(ex_mem_1_a_2), .B_2(R22), .ALU_2(ALUresult), .\同步清零_气泡_高电平有效 (RST),
    .\使能端_低电平有效_stall_高电平有效 (not_1_out), .blez(BLEZ1), .blezout(ex_mem_1_blezout), .sh(SH1), .shout(SH3),
    .lui(LUI1), .luiout(ex_mem_1_luiout), .\xor (xor1), .xorout(ex_mem_1_xorout));
  or or_6 (\无条件分支 , jump, En[1]);
  or or_7 (\条件分支 , and_7_out, Cmp1, and_8_out);
  or or_8 (\分支 , \无条件分支 , \条件分支 );
  RAM #(.addrWidth(10), .dataWidth(32), .bus("separate")) ram_1 (
    .addr(ALUresult[11:2]), .din(R222), .data(ram_1_data), .str(ex_mem_1_mw_2), .clk(CLK), .clr(RST));  // open: sel, ld
  Multiplexer #(.select(2), .width(32), .enable("false")) multiplexer_16 (
    .in0(A1), .in1(ALUresult2), .in2(Memdata), .in3(ALUresult), .out(Ain), .sel(forward1));
  Multiplexer #(.width(32), .enable("false")) multiplexer_17 (
    .in0(R22), .in1({{16{1'b0}}, R22[15:0]}), .out(R222), .sel(SH3));
  Counter #(.width(16), .max('hffff)) counter_1 (
    .count(loaduse), .Q(\LoadUse次数 ), .clk(CLK), .clr(RST));  // open: load, D, carry
  Counter #(.width(16), .max('hffff)) counter_2 (
    .count(PCEnable), .Q(\总周期数 ), .clk(CLK), .clr(RST));  // open: load, D, carry
  MEM_WB mem_wb_1 (
    .MTR(MEMTOREG), .REGW(MEM_RW), .JAL(MEM_JAL), .REGD(MEM_REGD), .SYS(ex_mem_1_sys_2), .PC(MEM_PC),
    .ID(MEM_ID), .A(ex_mem_1_a_2), .MD(ram_1_data), .B(R22), .ALU(ALUresult), .CLK(CLK),
    .MTR_2(mem_wb_1_mtr_2), .REGW_2(REGW), .JAL_2(JAL4), .REGD_2(mem_wb_1_regd_2), .SYS_2(SYS), .PC_2(pc_44),
    .ID_2(mem_wb_1_id_2), .A_2(A), .MD_2(Memdata), .B_2(B), .ALU_2(ALUresult2), .\同步清零_气泡_高电平有效 (RST),
    .\使能端_低电平有效_stall_高电平有效 (not_1_out), .blez(ex_mem_1_blezout), .sh(SH3), .lui(ex_mem_1_luiout),
    .luiout(LUI4), .\xor (ex_mem_1_xorout), .xorout(XOR4));  // open: blezout, shout
  Counter #(.width(16), .max('hffff)) counter_3 (
    .count(\无条件分支 ), .Q(\无条件分支数 ), .clk(CLK), .clr(RST));  // open: load, D, carry
  Multiplexer #(.width(32), .enable("false")) multiplexer_18 (
    .in0(ALUresult2), .in1(Memdata), .out(multiplexer_18_out), .sel(mem_wb_1_mtr_2));
  Counter #(.width(16), .max('hffff)) counter_4 (
    .count(\条件分支 ), .Q(\条件分支成功数 ), .clk(CLK), .clr(RST));  // open: load, D, carry
  Multiplexer #(.width(5), .enable("false")) multiplexer_19 (
    .in0(mem_wb_1_id_2[20:16]), .in1(mem_wb_1_id_2[15:11]), .out(multiplexer_19_out), .sel(mem_wb_1_regd_2));
  Multiplexer #(.select(2), .width(32), .enable("false")) multiplexer_20 (
    .in0(B1), .in1(ALUresult2), .in2(Memdata), .in3(ALUresult), .out(Bin), .sel(forward2));
  Multiplexer #(.width(5), .enable("false")) multiplexer_21 (
    .in0(multiplexer_19_out), .in1({5{1'b1}}), .out(W_num), .sel(JAL4));
  Multiplexer #(.select(3), .width(32), .enable("false")) multiplexer_22 (
    .in0(undriven), .in1(undriven), .in2(shifter_3_out), .in3({32{1'b0}}), .in4(pc_44), .in5({32{1'b0}}),
    .in7({32{1'b0}}), .sel({JAL4, LUI4, XOR4}));  // open: in6, out
  Multiplexer #(.width(32), .enable("false")) multiplexer_23 (
    .in0(multiplexer_18_out), .in1(pc_44), .out(RDIN), .sel(JAL4));
  Shifter #(.width(32)) shifter_3 (.in(ALUresult2), .\dist (5'b10000), .out(shifter_3_out));

  // Other names for the same wires on the sheet: PCO[31:0] = EX_PC; PC_choose = En[0]; JR1 = En[1]; ID32[5:0] = FUNC;
  //   ID_RT[4:0] = ID32[20:16]; ID_RS[4:0] = ID32[25:21]; OP[5:0] = ID32[31:26]; WB_PC[31:0] = pc_44;
  //   Y1[31:0] = ALUresult2; 插入气泡数[15:0] = \LoadUse次数 

  // Notes on the sheet:
  //   中断源
  //   rt
  //   rd
  //   中断等待指示
  //   指令存储器
  //   数码管输出
  //   rt
  //   rd
  //   contents of rom_1 (hex, n*v repeats v):
  //   20110001 8100005 20110001 20120002 20130003 8100009 20110001 20120002 20130003 810000d 20110001
  //   20120002 20130003 8100011 20110001 20120002 20130003 c1000fa 20100001 20110001 118fc0 112020
  //   20020022 c 118882 12200001 8100015 112020 20020022 c 20110001 118880 112020 20020022 c 12200001
  //   810001f 20110001 118fc0 112020 20020022 c 1188c3 112020 20020022 c 118903 112020 20020022 c 118903
  //   112020 20020022 c 118903 112020 20020022 c 118903 112020 20020022 c 118903 112020 20020022 c 118903
  //   112020 20020022 c 118903 112020 20020022 c 20100001 109fc0 139fc3 8021 2012000c 24160003 26100001
  //   3210000f 20080008 20090001 139900 2709825 132020 20020022 c 1094022 1500fff9 22100001 2018000f
  //   2188024 108700 20080008 20090001 139902 2709825 132021 20020022 c 1094022 1500fff9 108702 2c9b022
  //   12c00001 8100050 4020 1084027 84400 3508ffff 82021 20020022 c 2010ffff 20110000 ae300000 22100001
  //   22310004 ae300000 22100001 22310004 ae300000 22100001 22310004 ae300000 22100001 22310004 ae300000
  //   22100001 22310004 ae300000 22100001 22310004 ae300000 22100001 22310004 ae300000 22100001 22310004
  //   ae300000 22100001 22310004 ae300000 22100001 22310004 ae300000 22100001 22310004 ae300000 22100001
  //   22310004 ae300000 22100001 22310004 ae300000 22100001 22310004 ae300000 22100001 22310004 ae300000
  //   22100001 22310004 22100001 8020 2011003c 8e130000 8e340000 274402a 11000002 ae330000 ae140000
  //   2231fffc 1611fff8 102020 20020022 c 22100004 2011003c 1611fff2 20020032 c 2008ffff 20117777 112020
  //   20020022 c 200b0010 2288826 112020 20020022 c 216bffff 1560fffa 2002000a c 200b0008 3c11fedc
  //   3631ffff 112020 20020022 c 3c11ba98 112020 c 3c117654 112020 c 3c113210 112020 c 216bffff 1560fff0
  //   2002000a c 20090000 200b0020 20110001 20120001 a5310000 112020 20020022 c 2328820 21290002 216bffff
  //   1560fff8 200b0010 20090000 8d310000 112020 20020022 c 21290004 216bffff 1560fff9 2002000a c 2011fff1
  //   112020 20020022 c 22310001 1a20fffb 2002000a c 2002000a c 20100000 22100001 102020 20020022 c
  //   22100002 102020 20020022 c 22100003 102020 20020022 c 22100004 102020 20020022 c 22100005 102020
  //   20020022 c 22100006 102020 20020022 c 22100007 102020 20020022 c 22100008 102020 20020022 20020022 c
  //   3e00008
  //   OP
  //   Func
  //   rs
  //   rt
  //   流水调试日志用
  //   rt
  //   rd
endmodule

module _1 (
  input  [5:0] OP,
  input  [4:0] EX_WriteReg_num,
  input  EX_RegWrite,
  input  [4:0] MEM_WriteReg_num,
  input  MEM_RegWrite,
  input  [5:0] Func,
  input  [4:0] ID_R1_num,
  input  [4:0] ID_R2_num,
  input  EX_MTR,
  input  MEM_MTR,
  output [1:0] forwordA,
  output [1:0] forwordB,
  output LoadUse
);

  wire and_1_out, and_2_out, and_3_out, and_4_out, and_5_out, and_6_out, and_7_out, and_8_out, and_9_out,
       and_10_out, comparator_1_eq, comparator_2_eq, comparator_3_eq, comparator_4_eq, comparator_5_eq,
       comparator_6_eq, nor_1_out, nor_2_out, not_1_out, \源寄存器使用情况_1_r1_used , \源寄存器使用情况_1_r2_used ;

  not not_1 (not_1_out, MEM_MTR);
  \源寄存器使用情况  \u_源寄存器使用情况_1  (
    .OP0(OP[0]), .OP1(OP[1]), .OP2(OP[2]), .OP3(OP[3]), .OP4(OP[4]), .OP5(OP[5]), .F0(Func[0]), .F1(Func[1]),
    .F2(Func[2]), .F3(Func[3]), .F4(Func[4]), .F5(Func[5]), .R1_Used(\源寄存器使用情况_1_r1_used ),
    .R2_Used(\源寄存器使用情况_1_r2_used ));
  Comparator #(.width(5)) comparator_1 (.a(ID_R1_num), .b({5{1'b0}}), .eq(comparator_1_eq));  // open: gt, lt
  Comparator #(.width(5)) comparator_2 (.a(ID_R2_num), .b({5{1'b0}}), .eq(comparator_2_eq));  // open: gt, lt
  Comparator #(.width(5)) comparator_3 (.a(ID_R1_num), .b(MEM_WriteReg_num), .eq(comparator_3_eq));  // open: gt, lt
  Comparator #(.width(5)) comparator_4 (.a(ID_R1_num), .b(EX_WriteReg_num), .eq(comparator_4_eq));  // open: gt, lt
  Comparator #(.width(5)) comparator_5 (.a(ID_R2_num), .b(MEM_WriteReg_num), .eq(comparator_5_eq));  // open: gt, lt
  Comparator #(.width(5)) comparator_6 (.a(ID_R2_num), .b(EX_WriteReg_num), .eq(comparator_6_eq));  // open: gt, lt
  and and_1 (and_1_out, ~comparator_1_eq, MEM_RegWrite, \源寄存器使用情况_1_r1_used , comparator_3_eq);  // AND_Gate
  and and_2 (and_2_out, ~comparator_1_eq, EX_RegWrite, \源寄存器使用情况_1_r1_used , comparator_4_eq);  // AND_Gate
  and and_3 (and_3_out, ~comparator_2_eq, MEM_RegWrite, \源寄存器使用情况_1_r2_used , comparator_5_eq);  // AND_Gate
  and and_4 (and_4_out, ~comparator_2_eq, EX_RegWrite, \源寄存器使用情况_1_r2_used , comparator_6_eq);  // AND_Gate
  and and_5 (and_5_out, MEM_MTR, and_1_out);
  and and_6 (and_6_out, not_1_out, and_1_out);
  and and_7 (and_7_out, not_1_out, and_3_out);
  and and_8 (and_8_out, MEM_MTR, and_3_out);
  and and_9 (and_9_out, and_2_out, EX_MTR);
  and and_10 (and_10_out, and_4_out, EX_MTR);
  nor nor_1 (nor_1_out, and_5_out, and_6_out, and_2_out);
  nor nor_2 (nor_2_out, and_7_out, and_4_out, and_8_out);
  or or_1 (LoadUse, and_9_out, and_10_out);
  Priority_Encoder #(.select(2), .disabled(0)) priority_encoder_1 (
    .in0(nor_1_out), .in1(and_6_out), .in2(and_5_out), .in3(and_2_out), .out(forwordA));  // open: gs, en_out, en_in
  Priority_Encoder #(.select(2), .disabled(0)) priority_encoder_2 (
    .in0(nor_2_out), .in1(and_7_out), .in2(and_8_out), .in3(and_4_out), .out(forwordB));  // open: gs, en_out, en_in

  // Other names for the same wires on the sheet: OP_CODE[5:0] = OP

  // Notes on the sheet:
  //   R1&EX
  //   R1&MEM
  //   R2&MEM
  //   R2&EX
  //   A中用到WB.MEM
  //   A中需要用到WB..ALU
  //   A要用到MEM.ALU
  //   B中用到WB.ALU
  //   B中用到MEM.ALU
  //   B中用到WB.MEM
endmodule

module \单周期中断  (
);

  wire and_1_out, and_2_out, and_3_out, and_4_out, and_5_out, and_6_out, and_7_out, Beq, BLEZ, Bne, CLK, Cmp,
       comparator_1_eq, comparator_2_eq, d_ff_1_qn, Equal, go, IR1, IR2, IR3, JAL, JMP, LUI, MemWrite,
       not_1_out, PCEnable, RST, SH, SignedExt, syscall, W1, W2, W3, XOR, \硬布线控制器_1_memtoreg ,
       \硬布线控制器_1_regdst , \硬布线控制器_1_regwrite ;
  wire [1:0] En;
  wire [1:1] \硬布线控制器_1_alu_src ;
  wire [3:0] \硬布线控制器_1_alu_op ;
  wire [4:0] multiplexer_3_out, multiplexer_4_out, multiplexer_6_out, multiplexer_7_out;
  wire [15:0] \总周期数 , \无条件分支数 , \条件分支成功数 ;
  wire [25:0] addr;
  wire [31:0] adder_2_out, Addr2, bit_extender_1_out, bit_extender_2_out, LedData, multiplexer_1_out,
       multiplexer_2_out, multiplexer_5_out, multiplexer_10_out, multiplexer_12_out, pc_4, PC_q, R1, R2, R22,
       ram_1_data, result, shifter_1_out, shifter_2_out, Y;
  wire [31:26] rom_1_data;

  Button \u_总复位  (.out(RST));
  Button _1 (.out(IR1));
  Button _2 (.out(IR2));
  Button _3 (.out(IR3));
  Button u_go (.out(go));
  LED led_1 (.in(W1));
  LED led_2 (.in(W2));
  LED led_3 (.in(W3));
  Hex_Digit_Display hex_digit_display_1 (.value(LedData[31:28]));  // open: dp
  Hex_Digit_Display hex_digit_display_2 (.value(LedData[27:24]));  // open: dp
  Comparator #(.width(32)) comparator_1 (.a(R1), .b(32'h22), .eq(comparator_1_eq));  // open: gt, lt
  and and_1 (and_1_out, comparator_1_eq, syscall);
  Comparator #(.width(32)) comparator_2 (.a(result), .b(32'h1), .eq(comparator_2_eq));  // open: gt, lt
  Hex_Digit_Display hex_digit_display_3 (.value(LedData[19:16]));  // open: dp
  Hex_Digit_Display hex_digit_display_4 (.value(LedData[23:20]));  // open: dp
  not not_1 (not_1_out, comparator_1_eq);
  Register #(.width(32)) register_1 (.D(multiplexer_1_out), .Q(LedData), .clk(CLK));  // open: en, clr
  Multiplexer #(.width(32), .enable("false")) multiplexer_1 (
    .in0(LedData), .in1(R2), .out(multiplexer_1_out), .sel(and_1_out));
  Multiplexer #(.select(2), .width(32), .enable("false")) multiplexer_2 (
    .in0(pc_4), .in1(Addr2), .in2(R1), .in3(R1), .out(multiplexer_2_out), .sel(En));
  and and_2 (and_2_out, Bne, ~Equal);  // AND_Gate
  and and_3 (and_3_out, Equal, Beq);
  and and_4 (and_4_out, comparator_2_eq, BLEZ);
  Hex_Digit_Display hex_digit_display_5 (.value(LedData[15:12]));  // open: dp
  Hex_Digit_Display hex_digit_display_6 (.value(LedData[11:8]));  // open: dp
  D_Flip_Flop d_ff_1 (.clk(CLK), .D(go), .Qn(d_ff_1_qn));  // open: Q, preset, en, reset
  Hex_Digit_Display hex_digit_display_7 (.value(LedData[7:4]));  // open: dp
  Hex_Digit_Display hex_digit_display_8 (.value(LedData[3:0]));  // open: dp
  Clock clock_1 (.out(CLK));
  and and_5 (and_5_out, d_ff_1_qn, syscall, not_1_out);
  Register #(.width(32)) PC (.D(multiplexer_2_out), .en(PCEnable), .Q(PC_q), .clk(CLK), .clr(RST));
  or or_1 (Cmp, and_2_out, and_3_out, and_4_out);
  not not_2 (PCEnable, and_5_out);
  Adder #(.width(32)) adder_1 (.a(PC_q), .b(32'h4), .out(pc_4));  // open: cin, cout
  or or_2 (En[0], JMP, Cmp);
  // Probe on \总周期数 
  // Probe on \条件分支成功数 
  // Probe on \无条件分支数 
  ROM #(.addrWidth(10), .dataWidth(32)) rom_1 (.addr(PC_q[11:2]), .data({rom_1_data, addr}));  // open: sel
  assign bit_extender_1_out = {{16{1'b0}}, addr[15:0]};  // Bit_Extender bit_extender_1
  assign bit_extender_2_out = {{16{addr[15]}}, addr[15:0]};  // Bit_Extender bit_extender_2
  \硬布线控制器  \u_硬布线控制器_1  (
    .Func(addr[5:0]), .OP(rom_1_data), .ALU_OP(\硬布线控制器_1_alu_op ), .MemToReg(\硬布线控制器_1_memtoreg ),
    .MemWrite(MemWrite), .ALU_SRC(\硬布线控制器_1_alu_src [1]), .RegWrite(\硬布线控制器_1_regwrite ), .SysCALL(syscall),
    .SignedExt(SignedExt), .RegDst(\硬布线控制器_1_regdst ), .JR(En[1]), .JMP(JMP), .Beq(Beq), .JAL(JAL),
    .Bne(Bne), .XOR(XOR), .LUI(LUI), .SH(SH), .BLEZ(BLEZ));
  Multiplexer #(.width(5), .enable("false")) multiplexer_3 (
    .in0(addr[20:16]), .in1(5'b00100), .out(multiplexer_3_out), .sel(syscall));
  Multiplexer #(.width(5), .enable("false")) multiplexer_4 (
    .in0(addr[20:16]), .in1(addr[15:11]), .out(multiplexer_4_out), .sel(\硬布线控制器_1_regdst ));
  Multiplexer #(.width(32), .enable("false")) multiplexer_5 (
    .in0(bit_extender_1_out), .in1(bit_extender_2_out), .out(multiplexer_5_out), .sel(SignedExt));
  Shifter #(.width(32)) shifter_1 (.in(bit_extender_2_out), .\dist (5'b00010), .out(shifter_1_out));
  Counter #(.width(16), .max('hffff)) counter_1 (
    .count(PCEnable), .Q(\总周期数 ), .clk(CLK), .clr(RST));  // open: load, D, carry
  Multiplexer #(.width(5), .enable("false")) multiplexer_6 (
    .in0(addr[25:21]), .in1(5'b00010), .out(multiplexer_6_out), .sel(syscall));
  Multiplexer #(.width(5), .enable("false")) multiplexer_7 (
    .in0(multiplexer_4_out), .in1({5{1'b1}}), .out(multiplexer_7_out), .sel(JAL));
  Adder #(.width(32)) adder_2 (.a(shifter_1_out), .b(pc_4), .out(adder_2_out));  // open: cin, cout
  MIPS_Regifile mips_regifile_1 (
    .Din(multiplexer_10_out), .Clk(CLK), .R1(R1), .R2(R2), .WE(\硬布线控制器_1_regwrite ),
    .W_num(multiplexer_7_out), .R1_num(multiplexer_6_out), .R2_num(multiplexer_3_out));
  Counter #(.width(16), .max('hffff)) counter_2 (
    .count(and_6_out), .Q(\条件分支成功数 ), .clk(CLK), .clr(RST));  // open: load, D, carry
  and and_6 (and_6_out, Cmp, PCEnable);
  Multiplexer #(.select(2), .width(32), .enable("false")) multiplexer_8 (
    .in0(R2), .in1(32'h1), .in2(multiplexer_5_out), .in3(32'h1), .out(Y), .sel({\硬布线控制器_1_alu_src [1], BLEZ}));
  Multiplexer #(.width(32), .enable("false")) multiplexer_9 (
    .in0({pc_4[31:28], addr, 2'b00}), .in1(adder_2_out), .out(Addr2), .sel(Cmp));
  Counter #(.width(16), .max('hffff)) counter_3 (
    .count(and_7_out), .Q(\无条件分支数 ), .clk(CLK), .clr(RST));  // open: load, D, carry
  and and_7 (and_7_out, JMP, PCEnable);
  MIPS_ALU mips_alu_1 (
    .X(R1), .Y(Y), .AluOP(\硬布线控制器_1_alu_op ), .Equal(Equal), .Result(result), .shamt(addr[10:6]));  // open: Result_2
  Multiplexer #(.select(3), .width(32), .enable("false")) multiplexer_10 (
    .in0(multiplexer_12_out), .in1(multiplexer_12_out), .in2(shifter_2_out), .in3({32{1'b0}}), .in4(pc_4),
    .in5({32{1'b0}}), .in7({32{1'b0}}), .out(multiplexer_10_out), .sel({JAL, LUI, XOR}));  // open: in6
  RAM #(.addrWidth(10), .dataWidth(32), .bus("separate")) ram_1 (
    .addr(result[11:2]), .din(R22), .data(ram_1_data), .str(MemWrite), .clk(CLK), .clr(RST));  // open: sel, ld
  Shifter #(.width(32)) shifter_2 (.in(Y), .\dist (5'b10000), .out(shifter_2_out));
  Multiplexer #(.width(32), .enable("false")) multiplexer_11 (
    .in0(R2), .in1({{16{1'b0}}, R2[15:0]}), .out(R22), .sel(SH));
  Multiplexer #(.width(32), .enable("false")) multiplexer_12 (
    .in0(result), .in1(ram_1_data), .out(multiplexer_12_out), .sel(\硬布线控制器_1_memtoreg ));

  // Other names for the same wires on the sheet: PC_choose = En[0]; JR = En[1]

  // Notes on the sheet:
  //   数码管输出
  //   指令存储器
  //   指令字
  //   contents of rom_1 (hex, n*v repeats v):
  //   20110001 8100005 20110001 20120002 20130003 8100009 20110001 20120002 20130003 810000d 20110001
  //   20120002 20130003 8100011 20110001 20120002 20130003 c1000fa 20100001 20110001 118fc0 112020
  //   20020022 c 118882 12200001 8100015 112020 20020022 c 20110001 118880 112020 20020022 c 12200001
  //   810001f 20110001 118fc0 112020 20020022 c 1188c3 112020 20020022 c 118903 112020 20020022 c 118903
  //   112020 20020022 c 118903 112020 20020022 c 118903 112020 20020022 c 118903 112020 20020022 c 118903
  //   112020 20020022 c 118903 112020 20020022 c 20100001 109fc0 139fc3 8021 2012000c 24160003 26100001
  //   3210000f 20080008 20090001 139900 2709825 132020 20020022 c 1094022 1500fff9 22100001 2018000f
  //   2188024 108700 20080008 20090001 139902 2709825 132021 20020022 c 1094022 1500fff9 108702 2c9b022
  //   12c00001 8100050 4020 1084027 84400 3508ffff 82021 20020022 c 2010ffff 20110000 ae300000 22100001
  //   22310004 ae300000 22100001 22310004 ae300000 22100001 22310004 ae300000 22100001 22310004 ae300000
  //   22100001 22310004 ae300000 22100001 22310004 ae300000 22100001 22310004 ae300000 22100001 22310004
  //   ae300000 22100001 22310004 ae300000 22100001 22310004 ae300000 22100001 22310004 ae300000 22100001
  //   22310004 ae300000 22100001 22310004 ae300000 22100001 22310004 ae300000 22100001 22310004 ae300000
  //   22100001 22310004 22100001 8020 2011003c 8e130000 8e340000 274402a 11000002 ae330000 ae140000
  //   2231fffc 1611fff8 102020 20020022 c 22100004 2011003c 1611fff2 20020032 c 2008ffff 20117777 112020
  //   20020022 c 200b0010 2288826 112020 20020022 c 216bffff 1560fffa 2002000a c 200b0008 3c11fedc
  //   3631ffff 112020 20020022 c 3c11ba98 112020 c 3c117654 112020 c 3c113210 112020 c 216bffff 1560fff0
  //   2002000a c 20090000 200b0020 20110001 20120001 a5310000 112020 20020022 c 2328820 21290002 216bffff
  //   1560fff8 200b0010 20090000 8d310000 112020 20020022 c 21290004 216bffff 1560fff9 2002000a c 2011fff1
  //   112020 20020022 c 22310001 1a20fffb 2002000a c 2002000a c 20100000 22100001 102020 20020022 c
  //   22100002 102020 20020022 c 22100003 102020 20020022 c 22100004 102020 20020022 c 22100005 102020
  //   20020022 c 22100006 102020 20020022 c 22100007 102020 20020022 c 22100008 102020 20020022 20020022 c
  //   3e00008
  //   OP
  //   Func
  //   rs
  //   rt
  //   rd
  //   sa
  //   JR
  //   Beq
  //   JMP
  //   Bne
  //   OP
  //   JAL
  //   Func
  //   Syscall
  //   MemToReg
  //   MemWrite
  //   AluOP
  //   AluSrcB
  //   RegWrite
  //   RegDst
endmodule
